// Logisim project KURSminutetestVhin_60_GOST_RESET.circ as structural Verilog
module main (
  input  in_1,
  input  [7:0] in_2,
  input  in_3,
  output [7:0] out_4,
  output [7:0] out_5,
  output [7:0] out_6,
  output out_7,
  output [7:0] out_8,
  output [7:0] out_9,
  output [7:0] out_10,
  output [7:0] out_11,
  output out_12
);

  wire clock_1_out, comp_3_out_3, comp_4_out_3, comp_5_out_5;
  wire [0:0] sum8_4_p;
  wire [1:0] comp_1_out_3, comp_2_out_3, comp_6_out_4;
  wire [7:0] counter8_1_out_4, counter8_2_out_4, mux2in1_8bit_1_q, mux2in1_8bit_2_q, mux2in1_8bit_3_q,
       mux8_2_2_q, mux8_2_3_q, reg_8_1_q, reg_8_2_q, reg_8_3_q, reg_8_4_q, reg_8_5_q, reg_8_8_q, sub8_2_q,
       sub8_3_q, sub8_4_q, sum8_1_q, sum8_2_q, sum8_3_q, sum8_6_q;
  wire [15:0] mux2in1_16bit_1_q, mux2in1_16bit_2_q, reg16_1_q, reg16_2_q, sub16_1_q, sum16_1_q, sum16_2_q;
  wire [23:0] mpl24_1_q;

  COUNTER8 counter8_1 (
    .in_1(in_1), .in_2(clock_1_out), .out_4({counter8_1_out_4[7:5], out_7, counter8_1_out_4[3:0]}));  // open: out_3
  Clock clock_1 (.out(clock_1_out));
  reg_8 reg_8_1 (.WE(1'b1), .C(clock_1_out), .R(in_1), .D(sum8_1_q), .Q(reg_8_1_q));
  COUNTER8 counter8_2 (.in_1(in_1), .in_2(reg_8_1_q[7]), .out_4(counter8_2_out_4));  // open: out_3
  sum8 sum8_1 (.D0(reg_8_1_q), .D1(mux8_2_3_q), .Q(sum8_1_q));  // open: P0, P
  reg_8 reg_8_2 (.WE(1'b1), .C(out_7), .R(in_1), .D(counter8_2_out_4), .Q(reg_8_2_q));
  reg_8 reg_8_3 (.WE(1'b1), .C(out_7), .R(in_1), .D(reg_8_2_q), .Q(reg_8_3_q));
  sub8 sub8_1 (.D0(reg_8_2_q), .D1(reg_8_3_q), .Q(out_6));  // open: P0, P
  comp comp_1 (.in_1(out_6), .in_2(out_8), .out_3(comp_1_out_3[0]), .out_5(comp_1_out_3[1]));  // open: out_4
  reg_8 reg_8_4 (.WE(1'b1), .C(out_7), .R(out_12), .D(sum8_2_q), .Q(reg_8_4_q));
  reg_8 reg_8_5 (.WE(1'b1), .C(out_7), .R(out_12), .D(sum8_3_q), .Q(reg_8_5_q));
  sum8 sum8_2 (.D0(out_8), .D1(reg_8_4_q), .Q(sum8_2_q));  // open: P0, P
  MPL24 mpl24_1 (.D0({{16{1'b0}}, in_2}), .D1(24'h444), .Q(mpl24_1_q));
  sum8 sum8_3 (.D0(out_6), .D1(reg_8_5_q), .Q(sum8_3_q));  // open: P0, P
  reg_8 reg_8_6 (.WE(1'b1), .C(out_12), .R(in_1), .D(sum8_2_q), .Q(out_9));
  reg16 reg16_1 (.WE(1'b1), .C(out_7), .D(mux2in1_16bit_2_q), .Q(reg16_1_q));  // open: R
  reg16 reg16_2 (.WE(1'b1), .C(out_7), .D(mux2in1_16bit_1_q), .Q(reg16_2_q));  // open: R
  reg_8 reg_8_7 (.WE(1'b1), .C(out_12), .R(in_1), .D(sum8_3_q), .Q(out_4));
  sum16 sum16_1 (.D0(mpl24_1_q[23:8]), .D1(16'h80), .Q(sum16_1_q));  // open: P0, P
  count60 count60_1 (.in_1(in_3), .in_2(out_7), .out_3(out_12));  // open: out_4
  comp comp_2 (.in_1(sum8_3_q), .in_2(sum8_2_q), .out_3(comp_2_out_3[0]), .out_5(comp_2_out_3[1]));  // open: out_4
  sum16 sum16_2 (.D0(reg16_2_q), .D1(mpl24_1_q[23:8]), .Q(sum16_2_q));  // open: P0, P
  MUX2in1_16bit mux2in1_16bit_1 (.A(out_12), .D0(sum16_2_q), .D1(sum16_1_q), .Q(mux2in1_16bit_1_q));
  sub8 sub8_2 (.D0(sum8_3_q), .D1(sum8_2_q), .Q(sub8_2_q));  // open: P0, P
  sub8 sub8_3 (.D0(sum8_2_q), .D1(sum8_3_q), .Q(sub8_3_q));  // open: P0, P
  sub16 sub16_1 (.D0(reg16_2_q), .D1(reg16_1_q), .Q(sub16_1_q));  // open: P0, P
  sub8 sub8_4 (.D0(out_10), .D1(mux2in1_8bit_3_q), .Q(sub8_4_q));  // open: P0, P
  sum8 sum8_4 (.D0(sub16_1_q[7:0]), .D1(reg_8_8_q), .Q(out_11), .P(sum8_4_p[0]));  // open: P0
  MUX2in1_16bit mux2in1_16bit_2 (.A(out_12), .D0(reg16_2_q), .D1(16'h80), .Q(mux2in1_16bit_2_q));
  sum8 sum8_5 (.D0({{7{1'b0}}, sum8_4_p[0]}), .D1(sub16_1_q[15:8]), .Q(out_8));  // open: P0, P
  reg_8 reg_8_8 (.WE(1'b1), .C(out_7), .D(out_11), .Q(reg_8_8_q));  // open: R
  sum8 sum8_6 (.D0(mux2in1_8bit_3_q), .D1(out_10), .Q(sum8_6_q));  // open: P0, P
  mux8_2 mux8_2_1 (.D0(8'h1), .D1(sub8_2_q), .D2(sub8_3_q), .D3(8'h1), .SEL(comp_2_out_3), .Q(out_5));
  mux8_2 mux8_2_2 (.D0(out_10), .D1(sub8_4_q), .D2(sum8_6_q), .D3(out_10), .SEL(comp_1_out_3), .Q(mux8_2_2_q));
  comp comp_3 (.in_1(out_5), .in_2(8'h1), .out_3(comp_3_out_3));  // open: out_4, out_5
  mux2in1_8bit mux2in1_8bit_1 (.A(comp_3_out_3), .D0(8'h1), .D1(8'h2), .Q(mux2in1_8bit_1_q));
  comp comp_4 (.in_1(out_5), .in_2(8'h2), .out_3(comp_4_out_3));  // open: out_4, out_5
  reg_8 reg_8_9 (.WE(1'b1), .C(out_7), .R(in_1), .D(mux8_2_2_q), .Q(out_10));
  mux2in1_8bit mux2in1_8bit_2 (.A(comp_4_out_3), .D0(mux2in1_8bit_1_q), .D1(8'h4), .Q(mux2in1_8bit_2_q));
  comp comp_5 (.in_1(8'h4), .in_2(out_5), .out_5(comp_5_out_5));  // open: out_3, out_4
  comp comp_6 (.in_1(out_8), .in_2({8{1'b0}}), .out_4(comp_6_out_4[0]));  // open: out_3, out_5
  mux2in1_8bit mux2in1_8bit_3 (.A(comp_5_out_5), .D0(mux2in1_8bit_2_q), .D1(8'h6), .Q(mux2in1_8bit_3_q));
  comp comp_7 (.in_1({8{1'b0}}), .in_2(out_10), .out_4(comp_6_out_4[1]));  // open: out_3, out_5
  mux8_2 mux8_2_3 (.D0(out_10), .D1({8{1'b0}}), .D2(8'h1), .D3(out_10), .SEL(comp_6_out_4), .Q(mux8_2_3_q));
endmodule

module main2_basis (
  input  RESET
);

  wire button_1_out, button_2_out, cl, CLEAR, CLK, CLK_out, comp_xor_1_p5, comp_xor_1_p6, or_1_out, R, RC,
       RC_out, RCC, RCC_out, RES, rgb_video_2_p3, rx_worksaaaaaaaaa_1_sign_out, sotiiireeed_1_v,
       use_transmitter_reg_v1_1_tx_out, use_transmitter_reg_v1_1_tx_signal;
  wire [1:0] control_1_control_out;
  wire [2:0] rgb_video_1_p10, rgb_video_2_p5;
  wire [4:0] decomp_naaaahb_1_x0, rgb_video_2_p4;
  wire [6:0] comp_xor_1_p4, rx_worksaaaaaaaaa_1_data_out, sotiiireeed_1_data_out;
  wire [9:0] counter_1_q;
  wire [31:0] memory_1_line_out;

  Button u_RC (.out(RC_out));
  Button u_RCC (.out(RCC_out));
  Button button_1 (.out(button_1_out));
  Clock u_CLK (.out(CLK_out));
  Button button_2 (.out(button_2_out));
  Counter #(.max('h3ff), .width(10)) counter_1 (
    .clr(or_1_out), .clk(CLK), .Q(counter_1_q));  // open: load, up, count, D, carry
  or or_1 (or_1_out, RES, R, cl);
  or or_2 (R, RESET, button_1_out);
  or or_3 (CLK, CLK_out, button_2_out);
  or or_4 (CLEAR, R, RES);
  or or_5 (cl, RCC, RC);
  stability_unput_v4_v2 stability_unput_v4_v2_1 (
    .KEY_OUTPUT_1(RC), .KEY_OUTPUT_2(RCC));  // open: KEY_INPUT_1, CLK, KEY_INPUT_2
  control control_1 (.CONTROL_OUT(control_1_control_out));  // open: RC, RESET, CLK, RCC
  memory memory_1 (.CONTROL(control_1_control_out), .COUNTER(counter_1_q[9:5]), .LINE_OUT(memory_1_line_out));
  // RGB_Video #(.height(32), .scale(8), .width(32)) rgb_video_1: pin names not known; wires that end beside it: {24{1'b0}}, {24{1'b1}}, memory_1_line_out, counter_1_q[4:0], R, CLK, 1'b1, counter_1_q[4:0], counter_1_q[9:5], rgb_video_1_p10
  pixel_selector pixel_selector_1 (.DATA_output(rgb_video_1_p10));  // open: ROM_input, COUNTER_input, COLOR_0, COLOR_1
  // comp_xor comp_xor_1: pin names not known; wires that end beside it: memory_1_line_out, CLEAR, CLK, comp_xor_1_p4, comp_xor_1_p5, comp_xor_1_p6, comp_xor_1_p5
  SOTIIIREEED sotiiireeed_1 (
    .wr(comp_xor_1_p6), .rd(use_transmitter_reg_v1_1_tx_signal), .clk(CLK), .d_in(comp_xor_1_p4),
    .CLR(CLEAR), .V(sotiiireeed_1_v), .data_out(sotiiireeed_1_data_out));
  use_transmitter_reg_v1 use_transmitter_reg_v1_1 (
    .CLK(CLK), .RESET(CLEAR), .VALID_SIG(sotiiireeed_1_v), .DATA_IN(sotiiireeed_1_data_out),
    .TX_SIGNAL(use_transmitter_reg_v1_1_tx_signal), .TX_OUT(use_transmitter_reg_v1_1_tx_out));
  rx_WORKSAAAAAAAAA rx_worksaaaaaaaaa_1 (
    .RESET(CLEAR), .CLK(CLK), .RX_IN(use_transmitter_reg_v1_1_tx_out),
    .SIGN_OUT(rx_worksaaaaaaaaa_1_sign_out), .DATA_OUT(rx_worksaaaaaaaaa_1_data_out));
  // NOT_Gate not_1 has open pins: in=decomp_naaaahb_1_x0, out=open
  // RGB_Video #(.height(32), .scale(8), .width(32)) rgb_video_2: pin names not known; wires that end beside it: R, CLK, rgb_video_2_p3, rgb_video_2_p4, rgb_video_2_p5
  decomp_naaaahb decomp_naaaahb_1 (
    .RESET(R), .SIGN(rx_worksaaaaaaaaa_1_sign_out), .DATA_IN(rx_worksaaaaaaaaa_1_data_out), .CLK(CLK),
    .stahp(RES), .DATA_RGB_OUT(rgb_video_2_p5), .WE_RGB(rgb_video_2_p3), .X0(decomp_naaaahb_1_x0),
    .Y0(rgb_video_2_p4));
  RES_SYS res_sys_1 (.X(decomp_naaaahb_1_x0), .Y(rgb_video_2_p4), .CL(cl), .CLK(CLK), .RES(RES));

  // Notes on the sheet:
  //   База цепи. 
  //   Компрессор идеален
  //   FIFO теперь конфетка
endmodule

module control (
  input  RC,
  input  RCC,
  input  RESET,
  input  CLK,
  output [1:0] CONTROL_OUT
);

  wire and_1_out, and_2_out, dtrig_1_not_q, dtrig_2_not_q, nand_1_out, nand_2_out, nand_3_out, nand_4_out,
       nand_5_out, not_1_out, not_2_out, not_3_out, not_4_out;
  wire [1:0] nand_6_out;

  dtrig dtrig_1 (.D(RC), .C(CLK), .R(RESET), .NOT_Q(dtrig_1_not_q));  // open: S, Q
  and and_1 (and_1_out, RC, dtrig_1_not_q);
  not not_1 (not_1_out, CONTROL_OUT[1]);
  not not_2 (not_2_out, CONTROL_OUT[0]);
  not not_3 (not_3_out, and_1_out);
  not not_4 (not_4_out, and_2_out);
  nand nand_1 (nand_1_out, not_1_out, not_2_out, not_3_out, and_2_out);
  nand nand_2 (nand_2_out, not_1_out, CONTROL_OUT[0], and_1_out, not_4_out);
  nand nand_3 (nand_3_out, CONTROL_OUT[1], not_2_out, and_1_out);
  nand nand_4 (nand_4_out, CONTROL_OUT[1], not_3_out, not_4_out);
  nand nand_5 (nand_5_out, CONTROL_OUT[1], CONTROL_OUT[0], and_2_out);
  xor xor_1 (nand_6_out[1], CONTROL_OUT[0], and_1_out, and_2_out);
  dtrig dtrig_2 (.D(RCC), .C(CLK), .R(RESET), .NOT_Q(dtrig_2_not_q));  // open: S, Q
  nand nand_6 (nand_6_out[0], nand_1_out, nand_2_out, nand_3_out, nand_4_out, nand_5_out);
  and and_2 (and_2_out, RCC, dtrig_2_not_q);
  reg_2 reg_2_1 (.WE(1'b1), .C(CLK), .R(RESET), .D(nand_6_out), .Q({CONTROL_OUT[0], CONTROL_OUT[1]}));

  // Other names for the same wires on the sheet: R = RESET

  // Notes on the sheet:
  //   Конечный автомат для выбора блока памяти, содержащего спрайт
  //   Для решения проблемы "вентилятор". Автомат получит команду повернуть только один раз.
endmodule

module pixel_selector (
  input  [4:0] COUNTER_input,
  input  [2:0] COLOR_0,
  input  [2:0] COLOR_1,
  input  [31:0] ROM_input,
  output [2:0] DATA_output
);

  wire mux32bit_1_q;

  mux32bit mux32bit_1 (
    .D0(ROM_input[0]), .D1(ROM_input[1]), .D2(ROM_input[2]), .D3(ROM_input[3]), .D4(ROM_input[4]),
    .D5(ROM_input[5]), .D6(ROM_input[6]), .D7(ROM_input[7]), .D8(ROM_input[8]), .D9(ROM_input[9]),
    .D10(ROM_input[10]), .D11(ROM_input[11]), .D12(ROM_input[12]), .D13(ROM_input[13]), .D14(ROM_input[14]),
    .D15(ROM_input[15]), .D16(ROM_input[16]), .D17(ROM_input[17]), .D18(ROM_input[18]), .D19(ROM_input[19]),
    .D20(ROM_input[20]), .D21(ROM_input[21]), .D22(ROM_input[22]), .D23(ROM_input[23]), .D24(ROM_input[24]),
    .D25(ROM_input[25]), .D26(ROM_input[26]), .D27(ROM_input[27]), .D28(ROM_input[28]), .D29(ROM_input[29]),
    .D30(ROM_input[30]), .D31(ROM_input[31]), .A(COUNTER_input), .Q(mux32bit_1_q));
  // mux2in1_8bit mux2in1_8bit_1: pin names not known; wires that end beside it: mux32bit_1_q, COLOR_0, COLOR_1, DATA_output

  // Notes on the sheet:
  //   Для задания биту цвета и передачи его на RGB экран
endmodule

module stability_unput_v4_v2 (
  input  KEY_INPUT_1,
  input  CLK,
  input  KEY_INPUT_2,
  output KEY_OUTPUT_1,
  output KEY_OUTPUT_2
);

  wire counter_stabil_7bit_1_s0, counter_stabil_7bit_1_s2, counter_stabil_7bit_1_s3,
       counter_stabil_7bit_1_s4, counter_stabil_7bit_1_s5, counter_stabil_7bit_1_s6,
       counter_stabil_7bit_2_s0, counter_stabil_7bit_2_s2, counter_stabil_7bit_2_s3,
       counter_stabil_7bit_2_s4, counter_stabil_7bit_2_s5, counter_stabil_7bit_2_s6;

  counter_stabil_7bit counter_stabil_7bit_1 (
    .EN(KEY_INPUT_1), .CLK(CLK), .S5(counter_stabil_7bit_1_s5), .S6(counter_stabil_7bit_1_s6),
    .S0(counter_stabil_7bit_1_s0), .S1(counter_stabil_7bit_1_s0), .S2(counter_stabil_7bit_1_s2),
    .S3(counter_stabil_7bit_1_s3), .S4(counter_stabil_7bit_1_s4));
  counter_stabil_7bit counter_stabil_7bit_2 (
    .EN(KEY_INPUT_2), .CLK(CLK), .S5(counter_stabil_7bit_2_s5), .S6(counter_stabil_7bit_2_s6),
    .S0(counter_stabil_7bit_2_s0), .S1(counter_stabil_7bit_2_s0), .S2(counter_stabil_7bit_2_s2),
    .S3(counter_stabil_7bit_2_s3), .S4(counter_stabil_7bit_2_s4));
  and and_1 (KEY_OUTPUT_1, KEY_INPUT_1, counter_stabil_7bit_1_s6, counter_stabil_7bit_1_s5, counter_stabil_7bit_1_s4, counter_stabil_7bit_1_s3, counter_stabil_7bit_1_s2, counter_stabil_7bit_1_s0, counter_stabil_7bit_1_s0);
  and and_2 (KEY_OUTPUT_2, KEY_INPUT_2, counter_stabil_7bit_2_s6, counter_stabil_7bit_2_s5, counter_stabil_7bit_2_s4, counter_stabil_7bit_2_s3, counter_stabil_7bit_2_s2, counter_stabil_7bit_2_s0, counter_stabil_7bit_2_s0);

  // Notes on the sheet:
  //   Система антидребезга. При чатсоте 128 кГц выдаёт стабилизацию в 1мс.
  //   Выходы CI_1 и CI_2 - Check Interface - служат для проверки работы системы.
endmodule

module memory (
  input  [1:0] CONTROL,
  input  [4:0] COUNTER,
  output [31:0] LINE_OUT
);

  wire [31:0] rom_1_data, rom_2_data, rom_3_data, rom_4_data;

  ROM #(.addrWidth(5), .dataWidth(32)) rom_1 (.addr(COUNTER), .data(rom_1_data));
  ROM #(.addrWidth(5), .dataWidth(32)) rom_2 (.addr(COUNTER), .data(rom_2_data));
  ROM #(.addrWidth(5), .dataWidth(32)) rom_3 (.addr(COUNTER), .data(rom_3_data));
  ROM #(.addrWidth(5), .dataWidth(32)) rom_4 (.addr(COUNTER), .data(rom_4_data));
  Multiplexer #(.select(2), .width(32)) multiplexer_1 (
    .in0(rom_1_data), .in1(rom_2_data), .in2(rom_3_data), .in3(rom_4_data), .out(LINE_OUT), .sel(CONTROL));

  // Notes on the sheet:
  //   Блок памяти. Содержит всевозможные спрайты в ПЗУ. Выходной спрайт регулируется CONTROL
  //   contents of rom_1 (hex, n*v repeats v):
  //   18000 18000 3c000 3c000 7e000 7e000 ff000 ff000 1ff800 1ff800 3ffc00 3ffc00 7ffe00 7ffe00 ffff00
  //   ffff00 1ffff80 1ffff80 3ffffc0 3ffffc0 7ffffe0 7ffffe0 ffffff0 ffffff0 1ffffff8 1ffffff8 3ffffffc
  //   3ffffffc 7ffffffe 7ffffffe ffffffff ffffffff
  //   contents of rom_2 (hex, n*v repeats v):
  //   3 f 3f ff 3ff fff 3fff ffff 3ffff fffff 3fffff ffffff 3ffffff fffffff 3fffffff ffffffff ffffffff
  //   3fffffff fffffff 3ffffff ffffff 3fffff fffff 3ffff ffff 3fff fff 3ff ff 3f f 3
  //   contents of rom_3 (hex, n*v repeats v):
  //   ffffffff ffffffff 7ffffffe 7ffffffe 3ffffffc 3ffffffc 1ffffff8 1ffffff8 ffffff0 ffffff0 7ffffe0
  //   7ffffe0 3ffffc0 3ffffc0 1ffff80 1ffff80 ffff00 ffff00 7ffe00 7ffe00 3ffc00 3ffc00 1ff800 1ff800
  //   ff000 ff000 7e000 7e000 3c000 3c000 18000 18000
  //   contents of rom_4 (hex, n*v repeats v):
  //   c0000000 f0000000 fc000000 ff000000 ffc00000 fff00000 fffc0000 ffff0000 ffffc000 fffff000 fffffc00
  //   ffffff00 ffffffc0 fffffff0 fffffffc ffffffff ffffffff fffffffc fffffff0 ffffffc0 ffffff00 fffffc00
  //   fffff000 ffffc000 ffff0000 fffc0000 fff00000 ffc00000 ff000000 fc000000 f0000000 c0000000
endmodule

module compression_v1 (
  input  [31:0] DATA_IN,
  input  RESET,
  input  CLK,
  output [6:0] COMP_STR,
  output CI_CLR,
  output [5:0] CI_NUM,
  output PUSH
);

  wire and_1_out, and_2_out, comparator_1_eq, d_ff_1_q, d_ff_2_q, multiplexer_1_out, not_1_out, xor_1_out;
  wire [4:0] counter_1_q;

  Counter #(.max('h1f), .width(5)) counter_1 (
    .clr(RESET), .clk(CLK), .Q(counter_1_q));  // open: load, up, count, D, carry
  Multiplexer #(.select(5)) multiplexer_1 (
    .in0(DATA_IN[31]), .in1(DATA_IN[30]), .in2(DATA_IN[29]), .in3(DATA_IN[28]), .in4(DATA_IN[27]),
    .in5(DATA_IN[26]), .in6(DATA_IN[25]), .in7(DATA_IN[24]), .in8(DATA_IN[23]), .in9(DATA_IN[22]),
    .in10(DATA_IN[21]), .in11(DATA_IN[20]), .in12(DATA_IN[19]), .in13(DATA_IN[18]), .in14(DATA_IN[17]),
    .in15(DATA_IN[16]), .in16(DATA_IN[15]), .in17(DATA_IN[14]), .in18(DATA_IN[13]), .in19(DATA_IN[12]),
    .in20(DATA_IN[11]), .in21(DATA_IN[10]), .in22(DATA_IN[9]), .in23(DATA_IN[8]), .in24(DATA_IN[7]),
    .in25(DATA_IN[6]), .in26(DATA_IN[5]), .in27(DATA_IN[4]), .in28(DATA_IN[3]), .in29(DATA_IN[2]),
    .in30(DATA_IN[1]), .in31(DATA_IN[0]), .out(multiplexer_1_out), .sel(counter_1_q));
  Comparator #(.width(5)) comparator_1 (.a(counter_1_q), .b({5{1'b0}}), .eq(comparator_1_eq));  // open: gt, lt
  and and_1 (and_1_out, counter_1_q[0], counter_1_q[1], counter_1_q[2], counter_1_q[3], counter_1_q[4]);
  not not_1 (not_1_out, comparator_1_eq);
  D_Flip_Flop d_ff_1 (.D(and_1_out), .clk(CLK), .Q(d_ff_1_q));  // open: Qn, preset, reset
  D_Flip_Flop d_ff_2 (.D(multiplexer_1_out), .clk(CLK), .Q(d_ff_2_q), .reset(RESET));  // open: Qn, preset
  xor xor_1 (xor_1_out, multiplexer_1_out, d_ff_2_q);
  and and_2 (and_2_out, xor_1_out, not_1_out);
  or or_1 (PUSH, and_2_out, d_ff_1_q);
  // OR_Gate or_2 has open pins: in0=xor_1_out, in1=d_ff_1_q, out=open
  // counter_pix counter_pix_1: pin names not known; wires that end beside it: COMP_STR, CI_CLR, CI_NUM

  // Notes on the sheet:
  //   Сложная система сжатия. На вход подаются данные строки. 
  //   Полученные сжатые данные будут храниться в ОЗУ.
  //   Тут хранится строка
  //   Счётчик строки
  //   Выборка бита
  //   Сравнение цвета и бита
  //   триггер решает проблему срабатываения PUSH на 0000110
  //   XOR_OUT - важный выход. Он - индикатор окончания серии.
  //   Слово 7 бит
endmodule

module decompression (
  input  RESET,
  input  SIGN,
  input  CLK,
  input  [6:0] DATA_IN,
  output [23:0] DATA_OUT,
  output [4:0] X_OUT,
  output [4:0] Y_OUT
);

  wire and_1_out, counter_3bit_reset_1_s0, counter_3bit_reset_1_s1, counter_3bit_reset_1_s2, d_ff_1_q,
       d_ff_1_qn, shift_register_1_p6;

  D_Flip_Flop d_ff_1 (.clk(CLK), .Q(d_ff_1_q), .Qn(d_ff_1_qn), .preset(CLK), .reset(and_1_out));  // open: D
  counter_3bit_reset counter_3bit_reset_1 (
    .EN(d_ff_1_q), .CLK(CLK), .RESET(d_ff_1_qn), .S0(counter_3bit_reset_1_s0), .S1(counter_3bit_reset_1_s1),
    .S2(counter_3bit_reset_1_s2));
  and and_1 (and_1_out, counter_3bit_reset_1_s0, counter_3bit_reset_1_s1, counter_3bit_reset_1_s2);
  // Shift_Register #(.length(7)) shift_register_1: pin names not known; wires that end beside it: RESET, SIGN, d_ff_1_q, CLK, 1'b1, shift_register_1_p6
  // counter_10bit counter_10bit_1: pin names not known; wires that end beside it: X_OUT[0]
  Multiplexer #(.width(24)) multiplexer_1 (
    .in0({24{1'b0}}), .in1({24{1'b1}}), .out(DATA_OUT), .sel(shift_register_1_p6));
endmodule

module decompression_v1 (
  input  RESET,
  input  SIGN,
  input  CLK,
  input  [6:0] DATA_IN,
  output [23:0] DATA_OUT,
  output WRITE_EN,
  output [4:0] X_OUT,
  output [4:0] Y_OUT
);

  wire and_1_out, and_2_out, and_3_out, d_ff_1_q, d_ff_2_q, nor_1_out, or_1_out, or_2_out,
       shift_register_1_p5;
  wire [5:0] counter_1_q, undriven;

  // AND_Gate and_1 has open pins: out=and_1_out
  // AND_Gate and_2 has open pins: out=and_2_out
  or or_1 (or_1_out, and_1_out, and_2_out);
  D_Flip_Flop d_ff_1 (.D(SIGN), .clk(CLK), .Q(d_ff_1_q));  // open: Qn, preset, reset
  and and_3 (and_3_out, d_ff_2_q, ~nor_1_out);  // AND_Gate
  or or_2 (or_2_out, d_ff_1_q, and_3_out);
  D_Flip_Flop d_ff_2 (.D(or_2_out), .clk(CLK), .Q(d_ff_2_q));  // open: Qn, preset, reset
  // Shift_Register #(.length(7)) shift_register_1: pin names not known; wires that end beside it: RESET, SIGN, CLK, 1'b1, shift_register_1_p5
  and and_4 (WRITE_EN, ~CLK, d_ff_2_q);  // AND_Gate
  // counter_10bit counter_10bit_1: pin names not known; wires that end beside it: X_OUT[0]
  Multiplexer #(.width(24)) multiplexer_1 (
    .in0({24{1'b0}}), .in1({24{1'b1}}), .out(DATA_OUT), .sel(shift_register_1_p5));
  Counter #(.max('h3f), .ongoal("stay"), .width(6)) counter_1 (
    .load(d_ff_1_q), .up(1'b0), .count(d_ff_2_q), .clk(CLK), .D(undriven), .Q(counter_1_q));  // open: clr, carry
  nor nor_1 (nor_1_out, counter_1_q[0], counter_1_q[1], counter_1_q[2], counter_1_q[3], counter_1_q[4], counter_1_q[5]);
endmodule

module uart_transmitter_mult (
  input  [6:0] DATA_IN,
  input  CLK,
  input  VALID_SIG,
  output TX_OUT,
  output TX_SIGNAL
);

  wire and_1_out, d_ff_1_q, d_ff_1_qn, multiplexer_1_out, nand_1_out, or_1_out;
  wire [2:0] counter_3bit_1_s0;

  Multiplexer #(.select(3)) multiplexer_1 (
    .in0(1'b0), .in1(DATA_IN[0]), .in2(DATA_IN[1]), .in3(DATA_IN[2]), .in4(DATA_IN[3]), .in5(DATA_IN[4]),
    .in6(DATA_IN[5]), .in7(1'b1), .out(multiplexer_1_out), .sel(counter_3bit_1_s0));
  counter_3bit counter_3bit_1 (
    .EN(d_ff_1_q), .CLK(CLK), .S0(counter_3bit_1_s0[0]), .S1(counter_3bit_1_s0[1]), .S2(counter_3bit_1_s0[2]));
  nand nand_1 (nand_1_out, counter_3bit_1_s0[0], counter_3bit_1_s0[1], counter_3bit_1_s0[2]);
  or or_1 (or_1_out, nand_1_out, VALID_SIG);
  D_Flip_Flop d_ff_1 (.D(or_1_out), .clk(CLK), .Q(d_ff_1_q), .Qn(d_ff_1_qn));  // open: preset, reset
  and and_1 (and_1_out, counter_3bit_1_s0[2], counter_3bit_1_s0[1], counter_3bit_1_s0[0]);
  and and_2 (TX_SIGNAL, ~CLK, and_1_out);  // AND_Gate
  or or_2 (TX_OUT, multiplexer_1_out, d_ff_1_qn);
  // Pins of 6 and 7 bits meet at DATA_IN

  // Notes on the sheet:
  //   Счётчик пересчитывает эту линию
  //   Это считай вместо сдвиговых регистров, но я не знаю оно сработает или нет
  //   Логика мультиплексора - преобразование поступающей 6-битной линии сигнала в 8-битную линию.
  //   Сначала добавляется бит начала - я сказал что это 0. В конце - бит конца, я сказал что это 1.
endmodule

module use_transmitter_reg (
  input  CLK,
  input  RESET,
  input  VALID_SIG,
  input  [6:0] DATA_IN,
  output TX_SIGNAL,
  output TX_OUT
);

  wire and_1_out, and_2_out, counter_3bit_1_s0, counter_3bit_1_s1, counter_3bit_1_s2, d_ff_1_q, d_ff_1_qn,
       or_1_out, shift_register_1_p8;

  counter_3bit counter_3bit_1 (
    .EN(d_ff_1_q), .CLK(CLK), .S0(counter_3bit_1_s0), .S1(counter_3bit_1_s1), .S2(counter_3bit_1_s2));
  or or_1 (or_1_out, d_ff_1_q, VALID_SIG);
  and and_1 (and_1_out, counter_3bit_1_s0, counter_3bit_1_s1, counter_3bit_1_s2);
  D_Flip_Flop d_ff_1 (.D(or_1_out), .clk(CLK), .Q(d_ff_1_q), .Qn(d_ff_1_qn), .reset(and_1_out));  // open: preset
  and and_2 (and_2_out, d_ff_1_qn, VALID_SIG);
  // Shift_Register #(.length(9)) shift_register_1: pin names not known; wires that end beside it: RESET, and_2_out, d_ff_1_q, CLK, 1'b1, 1'b1, 1'b0, shift_register_1_p8
  and and_3 (TX_SIGNAL, and_2_out, ~CLK);  // AND_Gate
  or or_2 (TX_OUT, shift_register_1_p8, d_ff_1_qn);

  // Notes on the sheet:
  //   По первому фронту CLK сдвиговый регистр обработает команду load и защёлкнет данные
  //   D-триггер и счётчик формируют мозг операции. Как только данные пришли, триггер застревает на 1, пока счётчик не выведет 111. 
  //   Пометка: Счётчик, хоть и не имеет сам по себе "сброс", при EN = 0 делает его автоматически. Не уверен, вызовет ли это проблему.
  //   Пояснение за логику M2: Когда схема в покое, то есть Q = 0, а данные пришли (VALID_SIG = 1) - M2 загорается до импульса CLK.
  //   Пояснение за логику M1: Как только триггер покажет состояние работы (Q = 1), то надо сделать сдвиг, так как в следующем такте M2 = 0.
  //   Сдвиговый регистр хранит в себе серию битов. Сигнал DATA_IN запускает промежуточные 6 битов. По краям выстроены граничные биты.
  //   Пояснение за логику TX_OUT: В идеальном варианте UART нам надо, чтоб приёмник не крякнулся от количества начальных флагов (я поставил как 0), чтоб в состоянии покоя в линии была гарантированная 1.
endmodule

module use_transmitter_reg_v1 (
  input  CLK,
  input  RESET,
  input  VALID_SIG,
  input  [6:0] DATA_IN,
  output TX_SIGNAL,
  output TX_OUT
);

  wire and_1_out, and_2_out, and_3_out, and_4_out, counter_3bit_reset_1_s0, counter_3bit_reset_1_s1,
       counter_3bit_reset_1_s2, d_ff_1_q, d_ff_1_qn, or_1_out, shift_register_1_p8;

  and and_1 (and_1_out, d_ff_1_qn, VALID_SIG);
  or or_1 (or_1_out, and_1_out, and_2_out);
  and and_2 (and_2_out, d_ff_1_q, ~and_3_out);  // AND_Gate
  counter_3bit_reset counter_3bit_reset_1 (
    .EN(d_ff_1_q), .CLK(CLK), .RESET(d_ff_1_qn), .S0(counter_3bit_reset_1_s0), .S1(counter_3bit_reset_1_s1),
    .S2(counter_3bit_reset_1_s2));
  D_Flip_Flop d_ff_1 (.D(or_1_out), .clk(CLK), .Q(d_ff_1_q), .Qn(d_ff_1_qn), .reset(RESET));  // open: preset
  and and_3 (and_3_out, counter_3bit_reset_1_s0, counter_3bit_reset_1_s1, counter_3bit_reset_1_s2);
  and and_4 (and_4_out, d_ff_1_qn, VALID_SIG);
  // Shift_Register #(.length(9)) shift_register_1: pin names not known; wires that end beside it: RESET, and_4_out, d_ff_1_q, CLK, 1'b1, 1'b1, 1'b0, shift_register_1_p8
  and and_5 (TX_SIGNAL, VALID_SIG, d_ff_1_qn);
  or or_2 (TX_OUT, shift_register_1_p8, d_ff_1_qn);

  // Other names for the same wires on the sheet: R = RESET

  // Notes on the sheet:
  //   По первому фронту CLK сдвиговый регистр обработает команду load и защёлкнет данные
  //   D-триггер и счётчик формируют мозг операции. Как только данные пришли, триггер застревает на 1, пока счётчик не выведет 111. 
  //   Пометка: Счётчик, хоть и не имеет сам по себе "сброс", при EN = 0 делает его автоматически. Не уверен, вызовет ли это проблему.
  //   Пояснение за логику M2: Когда схема в покое, то есть Q = 0, а данные пришли (VALID_SIG = 1) - M2 загорается до импульса CLK.
  //   Сдвиговый регистр хранит в себе серию битов. Сигнал DATA_IN запускает промежуточные 7 битов. По краям выстроены граничные биты.
  //   Пояснение за логику M1: Как только триггер покажет состояние работы (Q = 1), то надо сделать сдвиг, так как в следующем такте M2 = 0.
  //   Пояснение за логику TX_SIGNAL: По сути это разрешение на выдачу следующей порции данных. По сути он делает переход к новому пакету в счётчике READ FIFO-буфера. 
  //   Пояснение за логику TX_OUT: В идеальном варианте UART нам надо, чтоб приёмник не крякнулся от количества начальных флагов (я поставил как 0), чтоб в состоянии покоя в линии была гарантированная 1.
endmodule

module uart_receiver (
  input  RESET,
  input  CLK,
  input  RX_IN,
  output [6:0] DATA_OUT,
  output SIGN_OUT
);

  wire and_1_out, d_ff_1_q, nor_1_out, or_1_out;
  wire [3:0] counter_1_q;
  wire [6:0] undriven;

  Counter #(.max('hf), .width(4)) counter_1 (
    .clr(RESET), .count(d_ff_1_q), .clk(CLK), .Q(counter_1_q));  // open: load, up, D, carry
  Comparator #(.width(4)) comparator_1 (.a(counter_1_q), .b(4'b0110), .eq(SIGN_OUT));  // open: gt, lt
  nor nor_1 (nor_1_out, d_ff_1_q, RX_IN);
  and and_1 (and_1_out, d_ff_1_q, ~SIGN_OUT);  // AND_Gate
  D_Flip_Flop d_ff_1 (.D(or_1_out), .clk(CLK), .Q(d_ff_1_q), .reset(RESET));  // open: Qn, preset
  or or_1 (or_1_out, nor_1_out, and_1_out);
  // Shift_Register #(.length(9)) shift_register_1: pin names not known; wires that end beside it: RESET, 1'b0, d_ff_1_q, CLK, RX_IN
  Register #(.width(7)) register_1 (.D(undriven), .en(SIGN_OUT), .clk(CLK), .Q(DATA_OUT), .clr(RESET));

  // Notes on the sheet:
  //   Так же можно не инвертировать CLK у конечного регистра. 
  //   3И идёт на вход D ещё одного триггера. Его Q будет загораться на 1 такт позже, чем счётчик дошёл до 7. Поставить его к WE регистра.
  //   Это концепт
endmodule

module counter_10bit (
  input  EN,
  input  CLK,
  input  RESET,
  output [9:0] Q
);

  wire and_1_out, and_2_out, and_3_out, and_4_out, and_5_out, and_6_out, and_7_out, and_8_out, and_9_out;

  T_Flip_Flop t_ff_1 (.T(EN), .clk(CLK), .Q(Q[0]), .reset(RESET));  // open: Qn, preset
  and and_1 (and_1_out, EN, Q[0]);
  T_Flip_Flop t_ff_2 (.T(and_1_out), .clk(CLK), .Q(Q[1]), .reset(RESET));  // open: Qn, preset
  and and_2 (and_2_out, and_1_out, Q[1]);
  T_Flip_Flop t_ff_3 (.T(and_2_out), .clk(CLK), .Q(Q[2]), .reset(RESET));  // open: Qn, preset
  and and_3 (and_3_out, and_2_out, Q[2]);
  T_Flip_Flop t_ff_4 (.T(and_3_out), .clk(CLK), .Q(Q[3]), .reset(RESET));  // open: Qn, preset
  and and_4 (and_4_out, and_3_out, Q[3]);
  T_Flip_Flop t_ff_5 (.T(and_4_out), .clk(CLK), .Q(Q[4]), .reset(RESET));  // open: Qn, preset
  and and_5 (and_5_out, and_4_out, Q[4]);
  T_Flip_Flop t_ff_6 (.T(and_5_out), .clk(CLK), .Q(Q[5]), .reset(RESET));  // open: Qn, preset
  and and_6 (and_6_out, and_5_out, Q[5]);
  T_Flip_Flop t_ff_7 (.T(and_6_out), .clk(CLK), .Q(Q[6]), .reset(RESET));  // open: Qn, preset
  and and_7 (and_7_out, and_6_out, Q[6]);
  T_Flip_Flop t_ff_8 (.T(and_7_out), .clk(CLK), .Q(Q[7]), .reset(RESET));  // open: Qn, preset
  and and_8 (and_8_out, and_7_out, Q[7]);
  T_Flip_Flop t_ff_9 (.T(and_8_out), .clk(CLK), .Q(Q[8]), .reset(RESET));  // open: Qn, preset
  and and_9 (and_9_out, and_8_out, Q[8]);
  T_Flip_Flop t_ff_10 (.T(and_9_out), .clk(CLK), .Q(Q[9]), .reset(RESET));  // open: Qn, preset

  // Notes on the sheet:
  //   Простой счётчик на 10 бит.
endmodule

module counter_8bit (
  input  EN,
  input  CLK,
  output S0,
  output S1,
  output S2,
  output S3,
  output S4,
  output S5,
  output S6,
  output S7
);

  wire and_1_out, and_2_out, and_3_out, and_4_out, and_5_out, and_6_out, and_7_out, not_1_out;

  not not_1 (not_1_out, EN);
  T_Flip_Flop t_ff_1 (.T(EN), .clk(CLK), .Q(S0), .reset(not_1_out));  // open: Qn, preset
  and and_1 (and_1_out, EN, S0);
  T_Flip_Flop t_ff_2 (.T(and_1_out), .clk(CLK), .Q(S1), .reset(not_1_out));  // open: Qn, preset
  and and_2 (and_2_out, and_1_out, S1);
  T_Flip_Flop t_ff_3 (.T(and_2_out), .clk(CLK), .Q(S2), .reset(not_1_out));  // open: Qn, preset
  and and_3 (and_3_out, and_2_out, S2);
  T_Flip_Flop t_ff_4 (.T(and_3_out), .clk(CLK), .Q(S3), .reset(not_1_out));  // open: Qn, preset
  and and_4 (and_4_out, and_3_out, S3);
  T_Flip_Flop t_ff_5 (.T(and_4_out), .clk(CLK), .Q(S4), .reset(not_1_out));  // open: Qn, preset
  and and_5 (and_5_out, and_4_out, S4);
  T_Flip_Flop t_ff_6 (.T(and_5_out), .clk(CLK), .Q(S5), .reset(not_1_out));  // open: Qn, preset
  and and_6 (and_6_out, and_5_out, S5);
  T_Flip_Flop t_ff_7 (.T(and_6_out), .clk(CLK), .Q(S6), .reset(not_1_out));  // open: Qn, preset
  and and_7 (and_7_out, and_6_out, S6);
  T_Flip_Flop t_ff_8 (.T(and_7_out), .clk(CLK), .Q(S7), .reset(not_1_out));  // open: Qn, preset

  // Notes on the sheet:
  //   Простой счётчик на 8 бит.
endmodule

module counter_stabil_7bit (
  input  EN,
  input  CLK,
  output S0,
  output S1,
  output S2,
  output S3,
  output S4,
  output S5,
  output S6
);

  wire and_1_out, and_2_out, and_3_out, and_4_out, and_5_out, and_6_out, and_7_out, nand_1_out, not_1_out;

  not not_1 (not_1_out, EN);
  nand nand_1 (nand_1_out, S0, S1, S2, S3, S4, S5, S6);
  and and_1 (and_1_out, nand_1_out, EN);
  T_Flip_Flop t_ff_1 (.T(and_1_out), .clk(CLK), .Q(S0), .reset(not_1_out));  // open: Qn, preset
  and and_2 (and_2_out, and_1_out, S0);
  T_Flip_Flop t_ff_2 (.T(and_2_out), .clk(CLK), .Q(S1), .reset(not_1_out));  // open: Qn, preset
  and and_3 (and_3_out, and_2_out, S1);
  T_Flip_Flop t_ff_3 (.T(and_3_out), .clk(CLK), .Q(S2), .reset(not_1_out));  // open: Qn, preset
  and and_4 (and_4_out, and_3_out, S2);
  T_Flip_Flop t_ff_4 (.T(and_4_out), .clk(CLK), .Q(S3), .reset(not_1_out));  // open: Qn, preset
  and and_5 (and_5_out, and_4_out, S3);
  T_Flip_Flop t_ff_5 (.T(and_5_out), .clk(CLK), .Q(S4), .reset(not_1_out));  // open: Qn, preset
  and and_6 (and_6_out, and_5_out, S4);
  T_Flip_Flop t_ff_6 (.T(and_6_out), .clk(CLK), .Q(S5), .reset(not_1_out));  // open: Qn, preset
  and and_7 (and_7_out, and_6_out, S5);
  T_Flip_Flop t_ff_7 (.T(and_7_out), .clk(CLK), .Q(S6), .reset(not_1_out));  // open: Qn, preset

  // Notes on the sheet:
  //   Кодовое названиие схемы - Рельсотрон
  //   7-битный счётчик. Замирает на значении 1111111, пока EN = 1. Именно он создаёт нужную задержку в антидребезге.
endmodule

module counter_6bit (
  input  EN,
  input  CLK,
  input  RESET,
  output S0,
  output S1,
  output S2,
  output S3,
  output S4,
  output S5
);

  wire and_1_out, and_2_out, and_3_out, and_4_out, and_5_out;

  T_Flip_Flop t_ff_1 (.T(EN), .clk(CLK), .Q(S0), .reset(RESET));  // open: Qn, preset
  and and_1 (and_1_out, EN, S0);
  T_Flip_Flop t_ff_2 (.T(and_1_out), .clk(CLK), .Q(S1), .reset(RESET));  // open: Qn, preset
  and and_2 (and_2_out, and_1_out, S1);
  T_Flip_Flop t_ff_3 (.T(and_2_out), .clk(CLK), .Q(S2), .reset(RESET));  // open: Qn, preset
  and and_3 (and_3_out, and_2_out, S2);
  T_Flip_Flop t_ff_4 (.T(and_3_out), .clk(CLK), .Q(S3), .reset(RESET));  // open: Qn, preset
  and and_4 (and_4_out, and_3_out, S3);
  T_Flip_Flop t_ff_5 (.T(and_4_out), .clk(CLK), .Q(S4), .reset(RESET));  // open: Qn, preset
  and and_5 (and_5_out, and_4_out, S4);
  T_Flip_Flop t_ff_6 (.T(and_5_out), .clk(CLK), .Q(S5), .reset(RESET));  // open: Qn, preset

  // Notes on the sheet:
  //   Простой счётчик на 5 бит.
endmodule

module counter_5bit (
  input  EN,
  input  CLK,
  output S0,
  output S1,
  output S2,
  output S3,
  output S4
);

  wire and_1_out, and_2_out, and_3_out, and_4_out, not_1_out;

  not not_1 (not_1_out, EN);
  T_Flip_Flop t_ff_1 (.T(EN), .clk(CLK), .Q(S0), .reset(not_1_out));  // open: Qn, preset
  and and_1 (and_1_out, EN, S0);
  T_Flip_Flop t_ff_2 (.T(and_1_out), .clk(CLK), .Q(S1), .reset(not_1_out));  // open: Qn, preset
  and and_2 (and_2_out, and_1_out, S1);
  T_Flip_Flop t_ff_3 (.T(and_2_out), .clk(CLK), .Q(S2), .reset(not_1_out));  // open: Qn, preset
  and and_3 (and_3_out, and_2_out, S2);
  T_Flip_Flop t_ff_4 (.T(and_3_out), .clk(CLK), .Q(S3), .reset(not_1_out));  // open: Qn, preset
  and and_4 (and_4_out, and_3_out, S3);
  T_Flip_Flop t_ff_5 (.T(and_4_out), .clk(CLK), .Q(S4), .reset(not_1_out));  // open: Qn, preset

  // Notes on the sheet:
  //   Простой счётчик на 5 бит.
endmodule

module counter_3bit (
  input  EN,
  input  CLK,
  output S0,
  output S1,
  output S2
);

  wire and_1_out, and_2_out, not_1_out;

  not not_1 (not_1_out, EN);
  T_Flip_Flop t_ff_1 (.T(EN), .clk(CLK), .Q(S0), .reset(not_1_out));  // open: Qn, preset
  and and_1 (and_1_out, EN, S0);
  T_Flip_Flop t_ff_2 (.T(and_1_out), .clk(CLK), .Q(S1), .reset(not_1_out));  // open: Qn, preset
  and and_2 (and_2_out, and_1_out, S1);
  T_Flip_Flop t_ff_3 (.T(and_2_out), .clk(CLK), .Q(S2), .reset(not_1_out));  // open: Qn, preset

  // Notes on the sheet:
  //   Простой счётчик на 3 бита.
endmodule

module counter_3bit_reset (
  input  EN,
  input  CLK,
  input  RESET,
  output S0,
  output S1,
  output S2
);

  wire and_1_out, and_2_out;

  T_Flip_Flop t_ff_1 (.T(EN), .clk(CLK), .Q(S0), .reset(RESET));  // open: Qn, preset
  and and_1 (and_1_out, EN, S0);
  T_Flip_Flop t_ff_2 (.T(and_1_out), .clk(CLK), .Q(S1), .reset(RESET));  // open: Qn, preset
  and and_2 (and_2_out, and_1_out, S1);
  T_Flip_Flop t_ff_3 (.T(and_2_out), .clk(CLK), .Q(S2), .reset(RESET));  // open: Qn, preset

  // Notes on the sheet:
  //   Простой счётчик на 3 бита.
endmodule

module counter_pix (
  input  COLOR_IN,
  input  PUSH,
  input  CLK,
  input  RESET,
  output [6:0] MEMORY_OUT
);

  wire mux2in1_6bit_1_p2, mux2in1_6bit_1_p4;

  // mux2in1_6bit mux2in1_6bit_1: pin names not known; wires that end beside it: PUSH, mux2in1_6bit_1_p2, 6'b000001, mux2in1_6bit_1_p4
  // reg_8 reg_8_1: pin names not known; wires that end beside it: mux2in1_6bit_1_p4, 1'b1, CLK, RESET, MEMORY_OUT[6:1]
  // sum8 sum8_1: pin names not known; wires that end beside it: MEMORY_OUT[6:1], 6'b000001, mux2in1_6bit_1_p2

  assign MEMORY_OUT[0] = COLOR_IN;

  // Other names for the same wires on the sheet: R = RESET

  // Notes on the sheet:
  //   Система подсчёта последовательности пикселей с одинаковым цветом.
endmodule

module comp_xor (
  input  [31:0] DATA_IN,
  input  RESET,
  input  CLK,
  output [6:0] COMP_STR,
  output PUSH
);

  wire dtrig_1_q, mux32bit_1_q, nor_1_out, or_2_out, xor_1_out;
  wire [4:0] A;
  wire [5:5] cnt6_comp_1_out_5;

  cnt6_comp cnt6_comp_1 (.L(nor_1_out), .C(CLK), .EN(1'b1), .R(RESET), .out_5({cnt6_comp_1_out_5[5], A}));
  mux32bit mux32bit_1 (
    .D0(DATA_IN[31]), .D1(DATA_IN[30]), .D2(DATA_IN[29]), .D3(DATA_IN[28]), .D4(DATA_IN[27]),
    .D5(DATA_IN[26]), .D6(DATA_IN[25]), .D7(DATA_IN[24]), .D8(DATA_IN[23]), .D9(DATA_IN[22]),
    .D10(DATA_IN[21]), .D11(DATA_IN[20]), .D12(DATA_IN[19]), .D13(DATA_IN[18]), .D14(DATA_IN[17]),
    .D15(DATA_IN[16]), .D16(DATA_IN[15]), .D17(DATA_IN[14]), .D18(DATA_IN[13]), .D19(DATA_IN[12]),
    .D20(DATA_IN[11]), .D21(DATA_IN[10]), .D22(DATA_IN[9]), .D23(DATA_IN[8]), .D24(DATA_IN[7]),
    .D25(DATA_IN[6]), .D26(DATA_IN[5]), .D27(DATA_IN[4]), .D28(DATA_IN[3]), .D29(DATA_IN[2]),
    .D30(DATA_IN[1]), .D31(DATA_IN[0]), .A(A), .Q(mux32bit_1_q));
  nor nor_1 (nor_1_out, A[0], A[1], A[2], A[3], A[4], ~cnt6_comp_1_out_5[5]);  // NOR_Gate
  xor xor_1 (xor_1_out, mux32bit_1_q, dtrig_1_q);
  dtrig dtrig_1 (.D(mux32bit_1_q), .C(CLK), .R(RESET), .Q(dtrig_1_q));  // open: S, NOT_Q
  or or_1 (PUSH, xor_1_out, nor_1_out);
  or or_2 (or_2_out, xor_1_out, nor_1_out);
  counter_pix counter_pix_1 (.COLOR_IN(dtrig_1_q), .PUSH(or_2_out), .CLK(CLK), .RESET(RESET), .MEMORY_OUT(COMP_STR));

  // Other names for the same wires on the sheet: R = RESET
endmodule

module decompression_prikoli (
  input  RESET,
  input  CLK,
  input  [6:0] DATA_IN,
  input  XOR_IN,
  output COLOR_OUT,
  output [4:0] X,
  output [4:0] Y
);

  wire counter_2_carry, nor_1_out, or_1_out;
  wire [5:0] counter_1_q;
  wire [6:0] str_line_q;

  Register #(.width(7)) str_line (.D(DATA_IN), .en(XOR_IN), .clk(CLK), .Q(str_line_q), .clr(RESET));
  Counter #(.max('h3f), .ongoal("stay"), .width(6)) counter_1 (
    .clr(RESET), .load(or_1_out), .up(1'b0), .clk(CLK), .D(str_line_q[5:0]), .Q(counter_1_q));  // open: count, carry
  or or_1 (or_1_out, nor_1_out, XOR_IN);
  D_Flip_Flop color (.D(str_line_q[6]), .clk(CLK), .Q(COLOR_OUT), .reset(RESET));  // open: Qn, preset
  Counter #(.max('h1f), .width(5)) counter_2 (
    .clr(RESET), .clk(CLK), .carry(counter_2_carry), .Q(X));  // open: load, up, count, D
  nor nor_1 (nor_1_out, counter_1_q[0], counter_1_q[1], counter_1_q[2], counter_1_q[4], counter_1_q[5], counter_1_q[3]);
  Counter #(.max('h1f), .width(5)) counter_3 (
    .clr(RESET), .clk(counter_2_carry), .Q(Y));  // open: load, up, count, D, carry
endmodule

module FIFO_buffer_v1 (
  input  WRITE_SIG,
  input  READ_SIG,
  input  [6:0] DATA_IN,
  input  CLK,
  input  RESET,
  output VALID_SIG,
  output [6:0] write_s,
  output [6:0] DATA_OUT,
  output [6:0] read_s
);

  wire comparator_1_eq;
  wire [6:0] multiplexer_1_out;

  Counter #(.max('h7f), .width(7)) write (
    .clr(RESET), .count(WRITE_SIG), .clk(CLK), .Q(write_s));  // open: load, up, D, carry
  Counter #(.max('h7f), .width(7)) read (
    .clr(RESET), .count(READ_SIG), .clk(CLK), .Q(read_s));  // open: load, up, D, carry
  Multiplexer #(.width(7)) multiplexer_1 (.in0(read_s), .in1(write_s), .out(multiplexer_1_out), .sel(WRITE_SIG));
  RAM #(.addrWidth(7), .clearpin("true"), .dataWidth(7), .enables("line")) ram_1 (
    .addr(multiplexer_1_out), .we(WRITE_SIG), .clk(CLK), .din(DATA_IN), .dout(DATA_OUT));  // open: clr
  not not_1 (VALID_SIG, comparator_1_eq);
  Comparator #(.mode("unsigned"), .width(7)) comparator_1 (
    .a(write_s), .b(read_s), .eq(comparator_1_eq));  // open: gt, lt
  dual_port_RAM_forum dual_port_ram_forum_1 ();  // open: WR_SIG, RD_SIG, CLK, DATA_IN, R, VALID_SIG, DATA_OUT

  // Other names for the same wires on the sheet: R = RESET

  // Notes on the sheet:
  //   Выдаёт 1, если ячейка не пуста
  //   Cчётчик WRITE увеличивается на 1 каждый раз, как происходит импульс XOR в блоке сжатия
  //   Счётчик READ увеличивается на 1 каждый раз, когда передатчик успешно отправил слово в канал.
endmodule

module compression_v2 (
  input  CLK,
  input  RESET,
  input  in_3,
  input  [31:0] DATA_IN,
  input  in_5,
  input  [4:0] in_6,
  input  in_7
);

  wire and_1_out, clock_1_out, counter_5bit_1_s0, counter_5bit_1_s1, counter_5bit_1_s2, counter_5bit_1_s3,
       counter_5bit_1_s4, not_1_out, undriven, xor_1_out;
  wire [0:0] d_ff_1_q;
  wire [4:0] adder_1_out, multiplexer_1_out, register_1_q;

  Clock clock_1 (.out(clock_1_out));
  counter_5bit counter_5bit_1 (
    .EN(in_5), .CLK(clock_1_out), .S0(counter_5bit_1_s0), .S1(counter_5bit_1_s1), .S2(counter_5bit_1_s2),
    .S3(counter_5bit_1_s3), .S4(counter_5bit_1_s4));
  not not_1 (not_1_out, RESET);
  and and_1 (and_1_out, counter_5bit_1_s0, counter_5bit_1_s1, counter_5bit_1_s2, counter_5bit_1_s3, counter_5bit_1_s4);
  // Shift_Register #(.length(32)) shift_register_1: pin names not known; wires that end beside it: RESET, and_1_out, not_1_out, clock_1_out, in_3
  D_Flip_Flop d_ff_1 (.D(undriven), .clk(clock_1_out), .Q(d_ff_1_q[0]), .reset(RESET));  // open: Qn, preset
  xor xor_1 (xor_1_out, undriven, d_ff_1_q[0]);
  Register #(.width(5)) register_1 (.D(multiplexer_1_out), .en(in_7), .clk(clock_1_out), .Q(register_1_q), .clr(RESET));
  Multiplexer #(.width(5)) multiplexer_1 (.in0(adder_1_out), .in1(in_6), .out(multiplexer_1_out), .sel(xor_1_out));
  Adder #(.width(5)) adder_1 (.a(register_1_q), .b(in_6), .out(adder_1_out));  // open: cin, cout
  // Probe on {register_1_q, d_ff_1_q[0]}
endmodule

module stability_input_v4_v1 (
  input  KEY_INPUT_1,
  input  CLK,
  input  KEY_INPUT_2,
  output KEY_OUTPUT_1,
  output [7:0] CI_1,
  output KEY_OUTPUT_2,
  output [7:0] CI_2
);

  counter_stabil_v1 counter_stabil_v1_1 (
    .EN(KEY_INPUT_1), .CLK(CLK), .S5(CI_1[5]), .S6(CI_1[6]), .S7(CI_1[7]), .S0(CI_1[0]), .S1(CI_1[1]),
    .S2(CI_1[2]), .S3(CI_1[3]), .S4(CI_1[4]));
  counter_stabil_v1 counter_stabil_v1_2 (
    .EN(KEY_INPUT_2), .CLK(CLK), .S5(CI_2[5]), .S6(CI_2[6]), .S7(CI_2[7]), .S0(CI_2[0]), .S1(CI_2[1]),
    .S2(CI_2[2]), .S3(CI_2[3]), .S4(CI_2[4]));
  and and_1 (KEY_OUTPUT_1, KEY_INPUT_1, CI_1[7]);
  and and_2 (KEY_OUTPUT_2, KEY_INPUT_2, CI_2[7]);

  // Notes on the sheet:
  //   CI_1 и CI_2 - чисто тестовые выходы. Чтоб я видел процессы.
endmodule

module counter_stabil_v1 (
  input  EN,
  input  CLK,
  output S0,
  output S1,
  output S2,
  output S3,
  output S4,
  output S5,
  output S6,
  output S7
);

  wire and_1_out, and_2_out, and_3_out, and_4_out, and_5_out, and_6_out, and_7_out, and_8_out, not_1_out,
       not_2_out;

  not not_1 (not_1_out, EN);
  not not_2 (not_2_out, S7);
  and and_1 (and_1_out, not_2_out, EN);
  T_Flip_Flop t_ff_1 (.T(and_1_out), .clk(CLK), .Q(S0), .reset(not_1_out));  // open: Qn, preset
  and and_2 (and_2_out, and_1_out, S0);
  T_Flip_Flop t_ff_2 (.T(and_2_out), .clk(CLK), .Q(S1), .reset(not_1_out));  // open: Qn, preset
  and and_3 (and_3_out, and_2_out, S1);
  T_Flip_Flop t_ff_3 (.T(and_3_out), .clk(CLK), .Q(S2), .reset(not_1_out));  // open: Qn, preset
  and and_4 (and_4_out, and_3_out, S2);
  T_Flip_Flop t_ff_4 (.T(and_4_out), .clk(CLK), .Q(S3), .reset(not_1_out));  // open: Qn, preset
  and and_5 (and_5_out, and_4_out, S3);
  T_Flip_Flop t_ff_5 (.T(and_5_out), .clk(CLK), .Q(S4), .reset(not_1_out));  // open: Qn, preset
  and and_6 (and_6_out, and_5_out, S4);
  T_Flip_Flop t_ff_6 (.T(and_6_out), .clk(CLK), .Q(S5), .reset(not_1_out));  // open: Qn, preset
  and and_7 (and_7_out, and_6_out, S5);
  T_Flip_Flop t_ff_7 (.T(and_7_out), .clk(CLK), .Q(S6), .reset(not_1_out));  // open: Qn, preset
  and and_8 (and_8_out, and_7_out, S6);
  T_Flip_Flop t_ff_8 (.T(and_8_out), .clk(CLK), .Q(S7), .reset(not_1_out));  // open: Qn, preset

  // Notes on the sheet:
  //   Кодовое названиие схемы - Рельсотрон
  //   8 бит для того чтоб мы увидели число 128, при частоте в 128 кГц стабилизация кнопки будет 1мс
endmodule

module stability_input_v1 (
  input  KEY_INPUT,
  output KEY_OUTPUT
);

  wire controlled_buffer_1_out, controlled_buffer_2_out, controlled_buffer_3_out, controlled_buffer_4_out,
       not_1_out, s_r_ff_1_q;

  assign controlled_buffer_1_out = KEY_INPUT ? KEY_INPUT : 1'bz;  // Controlled_Buffer controlled_buffer_1
  assign controlled_buffer_2_out = KEY_INPUT ? controlled_buffer_1_out : 1'bz;  // Controlled_Buffer controlled_buffer_2
  assign controlled_buffer_3_out = KEY_INPUT ? controlled_buffer_2_out : 1'bz;  // Controlled_Buffer controlled_buffer_3
  assign controlled_buffer_4_out = KEY_INPUT ? controlled_buffer_3_out : 1'bz;  // Controlled_Buffer controlled_buffer_4
  S_R_Flip_Flop s_r_ff_1 (.Q(s_r_ff_1_q), .reset(KEY_OUTPUT), .preset(controlled_buffer_4_out));  // open: S, R, clk, Qn
  not not_1 (not_1_out, KEY_INPUT);
  and and_1 (KEY_OUTPUT, not_1_out, s_r_ff_1_q);
endmodule

module stability_input_v2 (
  input  KEY_INPUT_1,
  input  CLK,
  input  KEY_INPUT_2,
  output KEY_OUTPUT_1,
  output KEY_OUTPUT_2
);

  wire d_ff_1_q, d_ff_2_q, d_ff_3_q, d_ff_4_q, d_ff_5_q, d_ff_6_q;

  D_Flip_Flop d_ff_1 (.D(KEY_INPUT_1), .clk(CLK), .Q(d_ff_1_q));  // open: Qn, preset, reset
  D_Flip_Flop d_ff_2 (.D(KEY_INPUT_2), .clk(CLK), .Q(d_ff_2_q));  // open: Qn, preset, reset
  D_Flip_Flop d_ff_3 (.D(d_ff_1_q), .clk(CLK), .Q(d_ff_3_q));  // open: Qn, preset, reset
  D_Flip_Flop d_ff_4 (.D(d_ff_2_q), .clk(CLK), .Q(d_ff_4_q));  // open: Qn, preset, reset
  D_Flip_Flop d_ff_5 (.D(d_ff_3_q), .clk(CLK), .Q(d_ff_5_q));  // open: Qn, preset, reset
  D_Flip_Flop d_ff_6 (.D(d_ff_4_q), .clk(CLK), .Q(d_ff_6_q));  // open: Qn, preset, reset
  and and_1 (KEY_OUTPUT_1, d_ff_1_q, d_ff_3_q, d_ff_5_q);
  and and_2 (KEY_OUTPUT_2, d_ff_2_q, d_ff_4_q, d_ff_6_q);
endmodule

module stability_input_v3 (
  input  KEY_INPUT_1,
  input  KEY_INPUT_2,
  input  RESET,
  input  CLK,
  output KEY_OUTPUT_1,
  output KEY_OUTPUT_2
);

  wire counter_1_carry, d_ff_1_q, d_ff_2_q, d_ff_3_q, d_ff_4_q, d_ff_5_q, d_ff_6_q;

  Counter #(.max('h7f), .width(7)) counter_1 (
    .clr(RESET), .clk(CLK), .carry(counter_1_carry));  // open: load, up, count, D, Q
  D_Flip_Flop d_ff_1 (.D(KEY_INPUT_1), .clk(counter_1_carry), .Q(d_ff_1_q));  // open: Qn, preset, reset
  D_Flip_Flop d_ff_2 (.D(KEY_INPUT_2), .clk(counter_1_carry), .Q(d_ff_2_q));  // open: Qn, preset, reset
  D_Flip_Flop d_ff_3 (.D(d_ff_1_q), .clk(counter_1_carry), .Q(d_ff_3_q));  // open: Qn, preset, reset
  D_Flip_Flop d_ff_4 (.D(d_ff_2_q), .clk(counter_1_carry), .Q(d_ff_4_q));  // open: Qn, preset, reset
  D_Flip_Flop d_ff_5 (.D(d_ff_3_q), .clk(counter_1_carry), .Q(d_ff_5_q));  // open: Qn, preset, reset
  D_Flip_Flop d_ff_6 (.D(d_ff_4_q), .clk(counter_1_carry), .Q(d_ff_6_q));  // open: Qn, preset, reset
  and and_1 (KEY_OUTPUT_1, d_ff_1_q, d_ff_3_q, d_ff_5_q);
  and and_2 (KEY_OUTPUT_2, d_ff_2_q, d_ff_4_q, d_ff_6_q);
endmodule

module FIFO_buffer_v2 (
  input  RESET,
  input  PUSH_IN,
  input  TX_SIGNAL,
  input  [5:0] DATA_IN,
  input  CLK,
  output VALID_SIG,
  output [5:0] DATA_OUT
);

  wire comparator_1_eq;
  wire [7:0] multiplexer_1_out, read_q, write_q;

  Counter write (.clr(RESET), .clk(PUSH_IN), .Q(write_q));  // open: load, up, count, D, carry
  Counter read (.clr(RESET), .clk(TX_SIGNAL), .Q(read_q));  // open: load, up, count, D, carry
  RAM #(.dataWidth(6)) ram_1 (
    .addr(multiplexer_1_out), .we(PUSH_IN), .oe(1'b1), .clk(CLK), .din(DATA_IN), .dout(DATA_OUT));
  Multiplexer #(.width(8)) multiplexer_1 (.in0(write_q), .in1(read_q), .out(multiplexer_1_out), .sel(PUSH_IN));
  not not_1 (VALID_SIG, comparator_1_eq);
  Comparator comparator_1 (.a(write_q), .b(read_q), .eq(comparator_1_eq));  // open: gt, lt

  // Notes on the sheet:
  //   Cчётчик WRITE увеличивается на 1 каждый раз, как происходит импульс XOR в блоке сжатия
  //   Счётчик READ увеличивается на 1 каждый раз, когда передатчик успешно отправил слово в канал.
endmodule

module test_fifo (
  input  RESET,
  input  [31:0] in_2,
  input  TX_SIG,
  output out_4,
  output [5:0] out_5,
  output [2:0] write_s,
  output [6:0] DATA_OUT,
  output VALID_SIG,
  output [2:0] read_s
);

  wire button_1_out, comparator_1_eq, compression_v1_1_p4;
  wire [2:0] multiplexer_1_out;
  wire [6:0] compression_v1_1_p5;

  Button button_1 (.out(button_1_out));
  // compression_v1 compression_v1_1: pin names not known; wires that end beside it: in_2, RESET, button_1_out, compression_v1_1_p4, compression_v1_1_p5, out_4, out_5
  DotMatrix #(.dotshape("circle"), .matrixcols(1), .matrixrows(32)) dotmatrix_1 (.col0(in_2));
  Counter #(.max('h7), .width(3)) write (
    .clr(RESET), .clk(compression_v1_1_p4), .Q(write_s));  // open: load, up, count, D, carry
  Counter #(.max('h7), .width(3)) read (.clr(RESET), .clk(TX_SIG), .Q(read_s));  // open: load, up, count, D, carry
  Multiplexer #(.width(3)) multiplexer_1 (
    .in0(write_s), .in1(read_s), .out(multiplexer_1_out), .sel(compression_v1_1_p4));
  RAM #(.addrWidth(3), .dataWidth(7)) ram_1 (
    .addr(multiplexer_1_out), .we(compression_v1_1_p4), .oe(1'b1), .clk(button_1_out),
    .din(compression_v1_1_p5), .dout(DATA_OUT));
  not not_1 (VALID_SIG, comparator_1_eq);
  Comparator #(.width(3)) comparator_1 (.a(write_s), .b(read_s), .eq(comparator_1_eq));  // open: gt, lt

  // Notes on the sheet:
  //   Выдаёт 1, если ячейка не пуста
  //   Cчётчик WRITE увеличивается на 1 каждый раз, как происходит импульс XOR в блоке сжатия
  //   Счётчик READ увеличивается на 1 каждый раз, когда передатчик успешно отправил слово в канал.
endmodule

module test_without_aah_uart (
  input  Drawing_EN,
  input  [23:0] COLOR_BACK,
  input  [23:0] COLOR_BASE,
  input  RESET,
  output [6:0] CI1,
  output [6:0] CI2,
  output out_7,
  output [5:0] out_8
);

  wire CLK_out, comp_xor_1_p5, comp_xor_1_p6, RC_out, RCC_out, rgb_video_2_p3, stability_unput_v4_v2_1_p3,
       stability_unput_v4_v2_1_p4;
  wire [0:0] counter_10bit_1_p1;
  wire [1:0] control_1_control_out;
  wire [2:0] rgb_video_1_p11, rgb_video_2_p6;
  wire [4:0] rgb_video_2_p4, rgb_video_2_p5;
  wire [6:0] comp_xor_1_p4;
  wire [9:0] counter_1_q;
  wire [31:0] memory_1_line_out;

  Clock CLK (.out(CLK_out));
  Button button_1 ();  // open: out
  Button RC (.out(RC_out));
  Button RCC (.out(RCC_out));
  Counter #(.max('h3ff), .width(10)) counter_1 (
    .clr(RESET), .clk(CLK_out), .Q(counter_1_q));  // open: load, up, count, D, carry
  // stability_unput_v4_v2 stability_unput_v4_v2_1: pin names not known; wires that end beside it: CI1, CI2, stability_unput_v4_v2_1_p3, stability_unput_v4_v2_1_p4
  // counter_10bit counter_10bit_1: pin names not known; wires that end beside it: counter_10bit_1_p1[0]
  compression_v1 compression_v1_1 ();  // open: DATA_IN, RESET, CLK, COMP_STR, CI_CLR, CI_NUM, PUSH
  control control_1 (.CONTROL_OUT(control_1_control_out));  // open: RC, RESET, CLK, RCC
  memory memory_1 (.CONTROL(control_1_control_out), .COUNTER(counter_1_q[9:5]), .LINE_OUT(memory_1_line_out));
  // RGB_Video #(.height(32), .scale(8), .width(32)) rgb_video_1: pin names not known; wires that end beside it: COLOR_BACK, COLOR_BASE, memory_1_line_out, counter_1_q[4:0], memory_1_line_out, RESET, CLK_out, 1'b1, counter_1_q[4:0], counter_1_q[9:5], rgb_video_1_p11
  pixel_selector pixel_selector_1 (.DATA_output(rgb_video_1_p11));  // open: ROM_input, COUNTER_input, COLOR_0, COLOR_1
  // comp_xor comp_xor_1: pin names not known; wires that end beside it: memory_1_line_out, RESET, CLK_out, comp_xor_1_p4, comp_xor_1_p5, comp_xor_1_p6, comp_xor_1_p5
  FIFO_buffer_v1 fifo_buffer_v1_1 ();  // open: WRITE_SIG, READ_SIG, DATA_IN, CLK, RESET, VALID_SIG, write_s, DATA_OUT, read_s
  // RGB_Video #(.height(32), .scale(8), .width(32)) rgb_video_2: pin names not known; wires that end beside it: RESET, CLK_out, rgb_video_2_p3, rgb_video_2_p4, rgb_video_2_p5, rgb_video_2_p6
  decomp_naaaahb decomp_naaaahb_1 (
    .RESET(RESET), .SIGN(comp_xor_1_p6), .DATA_IN(comp_xor_1_p4), .CLK(CLK_out),
    .DATA_RGB_OUT(rgb_video_2_p6), .WE_RGB(rgb_video_2_p3), .X0(rgb_video_2_p4), .Y0(rgb_video_2_p5));  // open: stahp
  decompression decompression_1 ();  // open: RESET, SIGN, CLK, DATA_IN, DATA_OUT, X_OUT, Y_OUT

  // Notes on the sheet:
  //   База цепи. 
  //   1. Сделать блок сжатия
  //   2. Сделать блок разжатия
  //   3. Проверить систему прямо
  //   4. Сделать систему  UART
  //   4.1 Сделать TX 
  //   4.2 Сделать RX
  //   4.3 Проверить в отдельности передачу картинки
endmodule

module decompression_v2 (
  input  RESET,
  input  SIGN,
  input  CLK,
  input  [6:0] DATA_IN,
  output [23:0] DATA_OUT,
  output WRITE_EN,
  output [4:0] X_OUT,
  output [4:0] Y_OUT
);

  wire and_1_out, and_2_out, and_3_out, and_4_out, counter_3bit_reset_1_s0, counter_3bit_reset_1_s1,
       counter_3bit_reset_1_s2, d_ff_1_q, d_ff_1_qn, or_1_out, shift_register_1_p6;

  and and_1 (and_1_out, d_ff_1_qn, SIGN);
  or or_1 (or_1_out, and_1_out, and_2_out);
  and and_2 (and_2_out, d_ff_1_q, ~and_4_out);  // AND_Gate
  D_Flip_Flop d_ff_1 (.D(or_1_out), .clk(CLK), .Q(d_ff_1_q), .Qn(d_ff_1_qn));  // open: preset, reset
  and and_3 (and_3_out, SIGN, d_ff_1_qn);
  counter_3bit_reset counter_3bit_reset_1 (
    .EN(d_ff_1_q), .CLK(CLK), .RESET(d_ff_1_qn), .S0(counter_3bit_reset_1_s0), .S1(counter_3bit_reset_1_s1),
    .S2(counter_3bit_reset_1_s2));
  and and_4 (and_4_out, ~counter_3bit_reset_1_s0, counter_3bit_reset_1_s1, counter_3bit_reset_1_s2);  // AND_Gate
  // Shift_Register #(.length(7)) shift_register_1: pin names not known; wires that end beside it: RESET, and_3_out, d_ff_1_q, CLK, 1'b1, shift_register_1_p6
  and and_5 (WRITE_EN, d_ff_1_q, CLK);
  // counter_10bit counter_10bit_1: pin names not known; wires that end beside it: X_OUT[0]
  Multiplexer #(.width(24)) multiplexer_1 (
    .in0({24{1'b0}}), .in1({24{1'b1}}), .out(DATA_OUT), .sel(shift_register_1_p6));
endmodule

module compression_v1_backup (
  input  [31:0] DATA_IN,
  input  RESET,
  input  CLK,
  output XOR_OUT,
  output [6:0] COMP_STR,
  output CI_CLR,
  output [5:0] CI_NUM
);

  wire counter_1_carry, d_ff_1_q, multiplexer_1_out;
  wire [4:0] counter_1_q;
  wire [31:0] register_1_q;

  Counter #(.max('h1f), .width(5)) counter_1 (
    .clr(RESET), .clk(CLK), .carry(counter_1_carry), .Q(counter_1_q));  // open: load, up, count, D
  Register #(.width(32)) register_1 (.D(DATA_IN), .clk(CLK), .Q(register_1_q), .clr(RESET));  // open: en
  Multiplexer #(.select(5)) multiplexer_1 (
    .in0(register_1_q[0]), .in1(register_1_q[1]), .in2(register_1_q[2]), .in3(register_1_q[3]),
    .in4(register_1_q[4]), .in5(register_1_q[5]), .in6(register_1_q[6]), .in7(register_1_q[7]),
    .in8(register_1_q[8]), .in9(register_1_q[9]), .in10(register_1_q[10]), .in11(register_1_q[11]),
    .in12(register_1_q[12]), .in13(register_1_q[13]), .in14(register_1_q[14]), .in15(register_1_q[15]),
    .in16(register_1_q[16]), .in17(register_1_q[17]), .in18(register_1_q[18]), .in19(register_1_q[19]),
    .in20(register_1_q[20]), .in21(register_1_q[21]), .in22(register_1_q[22]), .in23(register_1_q[23]),
    .in24(register_1_q[24]), .in25(register_1_q[25]), .in26(register_1_q[26]), .in27(register_1_q[27]),
    .in28(register_1_q[28]), .in29(register_1_q[29]), .in30(register_1_q[30]), .in31(register_1_q[31]),
    .out(multiplexer_1_out), .sel(counter_1_q));
  D_Flip_Flop d_ff_1 (.D(multiplexer_1_out), .clk(CLK), .Q(d_ff_1_q), .reset(RESET));  // open: Qn, preset
  xor xor_1 (XOR_OUT, multiplexer_1_out, d_ff_1_q);
  // counter_pix counter_pix_1: pin names not known; wires that end beside it: COMP_STR, CI_CLR, CI_NUM

  // Notes on the sheet:
  //   Сложная система сжатия. На вход подаются данные строки. 
  //   Полученные сжатые данные будут храниться в ОЗУ.
  //   Тут хранится строка
  //   Счётчик строки
  //   Выборка бита
  //   Сравнение цвета и бита
  //   Слово 7 бит
  //   XOR_OUT - важный выход. Он - индикатор окончания серии.
endmodule

module decompression_v3 (
  input  RESET,
  input  SIGN,
  input  CLK,
  input  [6:0] DATA_IN,
  output [23:0] DATA_OUT,
  output DRAW_EN,
  output [4:0] X0,
  output [4:0] Y0
);

  wire and_1_out, and_2_out, comparator_1_eq, counter_2_carry, D_out, L_out, register_2_q;
  wire [1:0] nor_1_out, register_1_q;
  wire [5:0] counter_1_q;

  and and_1 (and_1_out, ~register_1_q[1], register_1_q[0]);  // AND_Gate
  and and_2 (and_2_out, register_1_q[1], comparator_1_eq);
  nor nor_1 (nor_1_out[0], register_1_q[0], register_1_q[1], ~SIGN);  // NOR_Gate
  or or_1 (nor_1_out[1], and_1_out, and_2_out);
  Register #(.width(2)) register_1 (.D(nor_1_out), .clk(CLK), .Q(register_1_q), .clr(RESET));  // open: en
  Register #(.width(1)) register_2 (.D(DATA_IN[0]), .en(L_out), .clk(CLK), .Q(register_2_q), .clr(RESET));
  and D (D_out, ~register_1_q[0], register_1_q[1]);  // AND_Gate
  and L (L_out, register_1_q[0], ~register_1_q[1]);  // AND_Gate
  nor R (DRAW_EN, register_1_q[1], register_1_q[0]);
  Counter #(.max('h3f), .ongoal("stay"), .width(6)) counter_1 (
    .clr(RESET), .load(L_out), .up(1'b0), .count(D_out), .clk(CLK), .D(DATA_IN[6:1]), .Q(counter_1_q));  // open: carry
  Counter #(.max('h1f), .width(5)) counter_2 (
    .clr(RESET), .count(D_out), .clk(CLK), .carry(counter_2_carry), .Q(X0));  // open: load, up, D
  Multiplexer #(.width(24)) multiplexer_1 (.in0({24{1'b0}}), .in1({24{1'b1}}), .out(DATA_OUT), .sel(register_2_q));
  Comparator #(.width(6)) comparator_1 (.a(counter_1_q), .b({6{1'b0}}), .eq(comparator_1_eq));  // open: gt, lt
  Counter #(.max('h1f), .width(5)) counter_3 (
    .clr(RESET), .count(counter_2_carry), .clk(CLK), .Q(Y0));  // open: load, up, D, carry

  // Notes on the sheet:
  //   из покоя (Q=0) переходим в работу по SIGN. В работе остаёмся, пока CNT_LEN не досчитает до 0. Когда ZERO=1 — возврат в покой. 
endmodule

module test_uart (
  input  in_1,
  input  [6:0] in_2,
  output [6:0] out_3
);

  wire button_1_out, button_2_out, use_transmitter_reg_v1_1_tx_out;

  Button button_1 (.out(button_1_out));
  Button button_2 (.out(button_2_out));
  use_transmitter_reg_v1 use_transmitter_reg_v1_1 (
    .CLK(button_1_out), .RESET(button_2_out), .VALID_SIG(in_1), .DATA_IN(in_2),
    .TX_OUT(use_transmitter_reg_v1_1_tx_out));  // open: TX_SIGNAL
  uart_receiver uart_receiver_1 (
    .RESET(button_2_out), .CLK(button_1_out), .RX_IN(use_transmitter_reg_v1_1_tx_out), .DATA_OUT(out_3));  // open: SIGN_OUT

  // Notes on the sheet:
  //   Идёт сдвиг бита. Ёпта...
endmodule

module mem_test (
  input  [1:0] CONTROL,
  input  [4:0] COUNTER,
  output [31:0] LINE_OUT
);

  wire [31:0] rom_1_data, rom_2_data, rom_3_data, rom_4_data;

  ROM #(.addrWidth(5), .dataWidth(32)) rom_1 (.addr(COUNTER), .data(rom_1_data));
  ROM #(.addrWidth(5), .dataWidth(32)) rom_2 (.addr(COUNTER), .data(rom_2_data));
  ROM #(.addrWidth(5), .dataWidth(32)) rom_3 (.addr(COUNTER), .data(rom_3_data));
  ROM #(.addrWidth(5), .dataWidth(32)) rom_4 (.addr(COUNTER), .data(rom_4_data));
  Multiplexer #(.select(2), .width(32)) multiplexer_1 (
    .in0(rom_1_data), .in1(rom_2_data), .in2(rom_3_data), .in3(rom_4_data), .out(LINE_OUT), .sel(CONTROL));

  // Notes on the sheet:
  //   Блок памяти. Содержит всевозможные спрайты в ПЗУ. Выходной спрайт регулируется CONTROL
  //   contents of rom_1 (hex, n*v repeats v):
  //   200000 700000 200000 0 200400 200400 300c00 300c00 481200 442200 442200 424200 818100 81ff00 818100
  //   824100 1024080 1042080 1081080 1081080 2100840 2200440 2200440 2400240 4800120 4800120 50000a0
  //   6000060 a000050 c000030 8000010 8000010
  //   contents of rom_2 (hex, n*v repeats v):
  //   0 0 15dddc0 1484480 1c9dc80 1484480 149dc80 0 0 0 18000 3c000 3c000 18000 0 0 0 181800 3c3c00 3c3c00
  //   181800 4*0 1bb8ee0 2a882a0 2aa8ea0 2aa82a0 1bb82e0
  //   contents of rom_3 (hex, n*v repeats v):
  //   0 0 15dddc0 1484480 1c9dc80 1484480 149dc80 0 0 0 18000 3c000 3c000 18000 0 0 0 181800 3c3c00 3c3c00
  //   181800 4*0 1bb8ee0 2a882a0 2aa8ea0 2aa82a0 1bb82e0
  //   contents of rom_4 (hex, n*v repeats v):
  //   ff7fffff f7e5ce5f f35cf5cf f55d76d7 f5654dd7 ffffffff ffffffff fffe7fff fffc3fff fffc3fff fffe7fff
  //   6*ffffffff f8efdbbf 7e18d863 199b3337 b03198e3 1eee3e0c 3870ed9c e38783bf 1e1e1e3c f71f3f0 601f9e07
  //   3f7003fc cc0ffc00 ffc03ff 7f819f00 1ff81ff
endmodule

module comp_v2 (
  input  [31:0] LINE_IN,
  input  RESET,
  input  CLK,
  output PUSH,
  output out_5,
  output [5:0] out_6,
  output [6:0] COMP_STR
);

  wire and_1_out, and_2_out, comparator_1_eq, comparator_2_eq, d_ff_1_q, d_ff_1_qn, multiplexer_1_out,
       or_2_out, xor_1_out;
  wire [4:0] counter_1_q;
  wire [5:0] adder_1_out, multiplexer_2_out;

  Counter #(.max('h1f), .width(5)) counter_1 (
    .clr(RESET), .count(d_ff_1_qn), .clk(CLK), .Q(counter_1_q));  // open: load, up, D, carry
  and and_1 (and_1_out, xor_1_out, comparator_1_eq);
  D_Flip_Flop d_ff_1 (.D(1'b0), .clk(CLK), .Q(d_ff_1_q), .Qn(d_ff_1_qn), .preset(and_1_out), .reset(RESET));
  Multiplexer #(.select(5)) multiplexer_1 (
    .in0(LINE_IN[31]), .in1(LINE_IN[30]), .in2(LINE_IN[29]), .in3(LINE_IN[28]), .in4(LINE_IN[27]),
    .in5(LINE_IN[26]), .in6(LINE_IN[25]), .in7(LINE_IN[24]), .in8(LINE_IN[23]), .in9(LINE_IN[22]),
    .in10(LINE_IN[21]), .in11(LINE_IN[20]), .in12(LINE_IN[19]), .in13(LINE_IN[18]), .in14(LINE_IN[17]),
    .in15(LINE_IN[16]), .in16(LINE_IN[15]), .in17(LINE_IN[14]), .in18(LINE_IN[13]), .in19(LINE_IN[12]),
    .in20(LINE_IN[11]), .in21(LINE_IN[10]), .in22(LINE_IN[9]), .in23(LINE_IN[8]), .in24(LINE_IN[7]),
    .in25(LINE_IN[6]), .in26(LINE_IN[5]), .in27(LINE_IN[4]), .in28(LINE_IN[3]), .in29(LINE_IN[2]),
    .in30(LINE_IN[1]), .in31(LINE_IN[0]), .out(multiplexer_1_out), .sel(counter_1_q));
  Register #(.width(1)) register_1 (.D(multiplexer_1_out), .en(or_2_out), .clk(CLK), .Q(COMP_STR[0]), .clr(RESET));
  xor xor_1 (xor_1_out, multiplexer_1_out, COMP_STR[0]);
  and and_2 (and_2_out, xor_1_out, ~comparator_2_eq);  // AND_Gate
  or or_1 (PUSH, d_ff_1_q, comparator_1_eq, and_2_out);
  Comparator #(.width(5)) comparator_1 (.a(counter_1_q), .b({5{1'b1}}), .eq(comparator_1_eq));  // open: gt, lt
  Comparator #(.width(5)) comparator_2 (.a(counter_1_q), .b({5{1'b0}}), .eq(comparator_2_eq));  // open: gt, lt
  or or_2 (or_2_out, PUSH, comparator_2_eq);
  Multiplexer #(.width(6)) multiplexer_2 (.in0(adder_1_out), .in1(6'b000001), .out(multiplexer_2_out), .sel(or_2_out));
  Register #(.width(6)) register_2 (.D(multiplexer_2_out), .clk(CLK), .Q(COMP_STR[6:1]), .clr(RESET));  // open: en
  Adder #(.width(6)) adder_1 (.a(COMP_STR[6:1]), .b(6'b000001), .out(adder_1_out));  // open: cin, cout

  assign out_5 = COMP_STR[0];
  assign out_6 = COMP_STR[6:1];
endmodule

module real_fifo_test (
  input  RESET,
  input  PUSH_IN,
  input  TX_SIGNAL,
  input  [6:0] DATA_IN,
  input  CLK,
  output VALID_SIG,
  output [2:0] write_s,
  output [6:0] DATA_OUT,
  output [2:0] read_s
);

  wire comparator_1_eq;
  wire [2:0] multiplexer_1_out;

  Counter #(.max('h7), .width(3)) write (
    .clr(RESET), .count(PUSH_IN), .clk(CLK), .Q(write_s));  // open: load, up, D, carry
  Counter #(.max('h7), .width(3)) read (
    .clr(RESET), .count(TX_SIGNAL), .clk(CLK), .Q(read_s));  // open: load, up, D, carry
  RAM #(.addrWidth(3), .dataWidth(7)) ram_1 (
    .addr(multiplexer_1_out), .we(PUSH_IN), .oe(1'b1), .clk(CLK), .din(DATA_IN), .dout(DATA_OUT));
  Multiplexer #(.width(3)) multiplexer_1 (.in0(read_s), .in1(write_s), .out(multiplexer_1_out), .sel(PUSH_IN));
  not not_1 (VALID_SIG, comparator_1_eq);
  Comparator #(.width(3)) comparator_1 (.a(write_s), .b(read_s), .eq(comparator_1_eq));  // open: gt, lt
  DotMatrix #(.matrixcols(1)) dotmatrix_1 (.col0(DATA_OUT));

  // Notes on the sheet:
  //   Выдаёт 1, если ячейка не пуста
  //   Cчётчик WRITE увеличивается на 1 каждый раз, как происходит импульс XOR в блоке сжатия
  //   Счётчик READ увеличивается на 1 каждый раз, когда передатчик успешно отправил слово в канал.
endmodule

module tx_reg_fix1 (
  input  CLK,
  input  RESET,
  input  VALID_SIG,
  input  [6:0] DATA_IN,
  output TX_SIGNAL,
  output TX_OUT
);

  wire and_1_out, and_2_out, and_3_out, and_4_out, and_5_out, counter_3bit_reset_1_s0,
       counter_3bit_reset_1_s1, counter_3bit_reset_1_s2, d_ff_1_q, d_ff_1_qn, or_1_out, shift_register_1_p8;

  and and_1 (and_1_out, d_ff_1_qn, VALID_SIG);
  and and_2 (and_2_out, d_ff_1_q, ~and_3_out);  // AND_Gate
  counter_3bit_reset counter_3bit_reset_1 (
    .EN(d_ff_1_q), .CLK(CLK), .RESET(d_ff_1_qn), .S0(counter_3bit_reset_1_s0), .S1(counter_3bit_reset_1_s1),
    .S2(counter_3bit_reset_1_s2));
  or or_1 (or_1_out, and_1_out, and_2_out);
  and and_3 (and_3_out, counter_3bit_reset_1_s0, counter_3bit_reset_1_s1, counter_3bit_reset_1_s2);
  D_Flip_Flop d_ff_1 (.D(or_1_out), .clk(CLK), .Q(d_ff_1_q), .Qn(d_ff_1_qn), .reset(RESET));  // open: preset
  and and_4 (and_4_out, ~and_5_out, d_ff_1_q);  // AND_Gate
  and and_5 (and_5_out, d_ff_1_qn, VALID_SIG);
  // Shift_Register #(.length(9)) shift_register_1: pin names not known; wires that end beside it: RESET, and_5_out, and_4_out, CLK, 1'b1, 1'b1, 1'b0, shift_register_1_p8
  and and_6 (TX_SIGNAL, VALID_SIG, d_ff_1_qn);
  or or_2 (TX_OUT, shift_register_1_p8, d_ff_1_qn);

  // Notes on the sheet:
  //   По первому фронту CLK сдвиговый регистр обработает команду load и защёлкнет данные
  //   D-триггер и счётчик формируют мозг операции. Как только данные пришли, триггер застревает на 1, пока счётчик не выведет 111. 
  //   Пометка: Счётчик, хоть и не имеет сам по себе "сброс", при EN = 0 делает его автоматически. Не уверен, вызовет ли это проблему.
  //   Пояснение за логику M2: Когда схема в покое, то есть Q = 0, а данные пришли (VALID_SIG = 1) - M2 загорается до импульса CLK.
  //   КА к этому готов
  //   Сдвиговый регистр хранит в себе серию битов. Сигнал DATA_IN запускает промежуточные 7 битов. По краям выстроены граничные биты.
  //   Пояснение за логику M1: Как только триггер покажет состояние работы (Q = 1), то надо сделать сдвиг, так как в следующем такте M2 = 0.
  //   Пояснение за логику TX_SIGNAL: По сути это разрешение на выдачу следующей порции данных. По сути он делает переход к новому пакету в счётчике READ FIFO-буфера. 
  //   Пояснение за логику TX_OUT: В идеальном варианте UART нам надо, чтоб приёмник не крякнулся от количества начальных флагов (я поставил как 0), чтоб в состоянии покоя в линии была гарантированная 1.
endmodule

module fifo_tx_rx (
  input  in_1,
  input  [6:0] in_2,
  output [6:0] out_3
);

  wire button_1_out, button_2_out, fifo_buffer_v1_1_p3, fifo_buffer_v1_1_p6, fifo_buffer_v1_1_p7,
       fifo_buffer_v1_1_p9, use_transmitter_reg_v1_1_tx_out;
  wire [6:0] fifo_buffer_v1_1_p8;

  Button button_1 (.out(button_1_out));
  Button button_2 (.out(button_2_out));
  // FIFO_buffer_v1 fifo_buffer_v1_1: pin names not known; wires that end beside it: button_2_out, in_1, fifo_buffer_v1_1_p3, in_2, button_1_out, fifo_buffer_v1_1_p6, fifo_buffer_v1_1_p7, fifo_buffer_v1_1_p8, fifo_buffer_v1_1_p9
  // Probe on fifo_buffer_v1_1_p7
  // Probe on fifo_buffer_v1_1_p9
  // Probe on fifo_buffer_v1_1_p8
  use_transmitter_reg_v1 use_transmitter_reg_v1_1 (
    .CLK(button_1_out), .RESET(button_2_out), .VALID_SIG(fifo_buffer_v1_1_p6), .DATA_IN(fifo_buffer_v1_1_p8),
    .TX_SIGNAL(fifo_buffer_v1_1_p3), .TX_OUT(use_transmitter_reg_v1_1_tx_out));
  uart_receiver uart_receiver_1 (
    .RESET(button_2_out), .CLK(button_1_out), .RX_IN(use_transmitter_reg_v1_1_tx_out), .DATA_OUT(out_3));  // open: SIGN_OUT
endmodule

module comp_fifo_tx_rx (
  input  choice,
  output [6:0] out_2
);

  wire button_4_out, CLK, clock_1_out, decomp_naaaahb_1_p5, decomp_naaaahb_1_p6, decomp_naaaahb_1_p7,
       decomp_naaaahb_1_p8, decomp_naaaahb_1_p9, decomp_naaaahb_1_p10, not_1_out, R, rgb_video_1_p1,
       rx_worksaaaaaaaaa_1_p5, sotiiireeed_1_v, stability_unput_v4_v2_1_key_output_1,
       stability_unput_v4_v2_1_key_output_2, undriven, undriven_2, undriven_3,
       use_transmitter_reg_v1_1_tx_out, use_transmitter_reg_v1_1_tx_signal;
  wire [1:0] control_1_control_out;
  wire [6:0] comp_xor_1_comp_str, sotiiireeed_1_data_out;
  wire [9:0] counter_1_q;
  wire [31:0] mem_test_1_line_out, memory_1_line_out, multiplexer_1_out;

  Counter #(.max('h3ff), .width(10)) counter_1 (
    .clr(R), .clk(CLK), .Q(counter_1_q));  // open: load, up, count, D, carry
  Button button_1 ();  // open: out
  Button button_2 ();  // open: out
  Button button_3 (.out(R));
  stability_unput_v4_v2 stability_unput_v4_v2_1 (
    .KEY_OUTPUT_1(stability_unput_v4_v2_1_key_output_1), .KEY_OUTPUT_2(stability_unput_v4_v2_1_key_output_2));  // open: KEY_INPUT_1, CLK, KEY_INPUT_2
  DotMatrix #(.dotshape("circle"), .matrixcols(1), .matrixrows(32)) dotmatrix_1 (.col0(memory_1_line_out));
  control control_1 (.CONTROL_OUT(control_1_control_out));  // open: RC, RESET, CLK, RCC
  memory memory_1 (.CONTROL(control_1_control_out), .COUNTER(counter_1_q[9:5]), .LINE_OUT(memory_1_line_out));
  mem_test mem_test_1 (.LINE_OUT(mem_test_1_line_out));  // open: CONTROL, COUNTER
  Multiplexer #(.width(32)) multiplexer_1 (
    .in0(32'hffffff0), .in1(memory_1_line_out), .out(multiplexer_1_out), .sel(not_1_out));
  not not_1 (not_1_out, choice);
  // Probe on sotiiireeed_1_data_out
  // Probe on use_transmitter_reg_v1_1_tx_out
  // Probe on out_2
  // Probe on decomp_naaaahb_1_p9
  // Probe on comp_xor_1_comp_str[6:1]
  comp_xor comp_xor_1 (
    .DATA_IN(multiplexer_1_out), .RESET(R), .CLK(CLK), .COMP_STR(comp_xor_1_comp_str));  // open: PUSH
  // Probe on undriven
  FIFO_buffer_v1 fifo_buffer_v1_1 ();  // open: WRITE_SIG, READ_SIG, DATA_IN, CLK, RESET, VALID_SIG, write_s, DATA_OUT, read_s
  // Probe on use_transmitter_reg_v1_1_tx_signal
  Clock clock_1 (.out(clock_1_out));
  Button button_4 (.out(button_4_out));
  or or_1 (CLK, clock_1_out, button_4_out);
  SOTIIIREEED sotiiireeed_1 (
    .wr(undriven), .rd(use_transmitter_reg_v1_1_tx_signal), .clk(CLK), .d_in(comp_xor_1_comp_str), .CLR(R),
    .V(sotiiireeed_1_v), .data_out(sotiiireeed_1_data_out));
  use_transmitter_reg_v1 use_transmitter_reg_v1_1 (
    .CLK(CLK), .RESET(R), .VALID_SIG(sotiiireeed_1_v), .DATA_IN(sotiiireeed_1_data_out),
    .TX_SIGNAL(use_transmitter_reg_v1_1_tx_signal), .TX_OUT(use_transmitter_reg_v1_1_tx_out));
  // Probe on use_transmitter_reg_v1_1_tx_out
  dual_port_RAM_my dual_port_ram_my_1 ();  // open: WR_SIG, RD_SIG, CLK, DATA_IN, R, VALID_SIG, DATA_OUT
  // rx_WORKSAAAAAAAAA rx_worksaaaaaaaaa_1: pin names not known; wires that end beside it: R, CLK, use_transmitter_reg_v1_1_tx_out, out_2, rx_worksaaaaaaaaa_1_p5
  // Probe on out_2[6:1]
  // Probe on rx_worksaaaaaaaaa_1_p5
  // decomp_naaaahb decomp_naaaahb_1: pin names not known; wires that end beside it: R, rx_worksaaaaaaaaa_1_p5, out_2, CLK, decomp_naaaahb_1_p5, decomp_naaaahb_1_p6, decomp_naaaahb_1_p7, decomp_naaaahb_1_p8, decomp_naaaahb_1_p9, decomp_naaaahb_1_p10
  // Probe on undriven_3
  // RGB_Video #(.height(32), .scale(8), .width(32)) rgb_video_1: pin names not known; wires that end beside it: rgb_video_1_p1, R, CLK, decomp_naaaahb_1_p6, decomp_naaaahb_1_p7, decomp_naaaahb_1_p8, decomp_naaaahb_1_p5
  // Probe on decomp_naaaahb_1_p10
  // Probe on rgb_video_1_p1
  // Probe on undriven_2
  ROM #(.addrWidth(5), .dataWidth(32)) rom_1 ();  // open: addr, data
  ROM #(.addrWidth(5), .dataWidth(32)) rom_2 ();  // open: addr, data
  ROM #(.addrWidth(5), .dataWidth(32)) rom_3 ();  // open: addr, data
  ROM #(.addrWidth(5), .dataWidth(32)) rom_4 ();  // open: addr, data

  // Notes on the sheet:
  //   При смене данных X не сбрасывается, оно рисуется со сдвигом
  //   Увеличение FIFO буфера лишь откладывает неизбежное
  //   Скорее всего дело в декомпрессоре
  //   _____
  //   _____
  //   Марш опарышей
  //   contents of rom_1 (hex, n*v repeats v):
  //   18000 18000 3c000 3c000 7e000 7e000 ff000 ff000 1ff800 1ff800 3ffc00 3ffc00 7ffe00 7ffe00 ffff00
  //   ffff00 1ffff80 1ffff80 3ffffc0 3ffffc0 7ffffe0 7ffffe0 ffffff0 ffffff0 1ffffff8 1ffffff8 3ffffffc
  //   3ffffffc 7ffffffe 7ffffffe ffffffff ffffffff
  //   5 циклов и на 6 хана.
  //   contents of rom_2 (hex, n*v repeats v):
  //   3 f 3f ff 3ff fff 3fff ffff 3ffff fffff 3fffff ffffff 3ffffff fffffff 3fffffff ffffffff ffffffff
  //   3fffffff fffffff 3ffffff ffffff 3fffff fffff 3ffff ffff 3fff fff 3ff ff 3f f 3
  //   contents of rom_3 (hex, n*v repeats v):
  //   ffffffff ffffffff 7ffffffe 7ffffffe 3ffffffc 3ffffffc 1ffffff8 1ffffff8 ffffff0 ffffff0 7ffffe0
  //   7ffffe0 3ffffc0 3ffffc0 1ffff80 1ffff80 ffff00 ffff00 7ffe00 7ffe00 3ffc00 3ffc00 1ff800 1ff800
  //   ff000 ff000 7e000 7e000 3c000 3c000 18000 18000
  //   contents of rom_4 (hex, n*v repeats v):
  //   c0000000 f0000000 fc000000 ff000000 ffc00000 fff00000 fffc0000 ffff0000 ffffc000 fffff000 fffffc00
  //   ffffff00 ffffffc0 fffffff0 fffffffc ffffffff ffffffff fffffffc fffffff0 ffffffc0 ffffff00 fffffc00
  //   fffff000 ffffc000 ffff0000 fffc0000 fff00000 ffc00000 ff000000 fc000000 f0000000 c0000000
endmodule

module rx_2 (
  input  RESET,
  input  CLK,
  input  RX_IN,
  output [6:0] DATA_OUT,
  output SIGN_OUT
);

  wire and_1_out, and_2_out, and_3_out, d_ff_1_q, nor_1_out, not_1_out, or_1_out;
  wire [3:0] counter_1_q;
  wire [6:0] undriven;

  not not_1 (not_1_out, d_ff_1_q);
  Counter #(.max('hf), .width(4)) counter_1 (
    .clr(not_1_out), .count(d_ff_1_q), .clk(CLK), .Q(counter_1_q));  // open: load, up, D, carry
  Comparator #(.width(4)) comparator_1 (.a(counter_1_q), .b(4'b1000), .eq(SIGN_OUT));  // open: gt, lt
  and and_1 (and_1_out, ~SIGN_OUT, d_ff_1_q);  // AND_Gate
  nor nor_1 (nor_1_out, RX_IN, d_ff_1_q);
  and and_2 (and_2_out, ~SIGN_OUT, d_ff_1_q);  // AND_Gate
  or or_1 (or_1_out, nor_1_out, and_2_out);
  D_Flip_Flop d_ff_1 (.D(or_1_out), .clk(CLK), .Q(d_ff_1_q), .reset(RESET));  // open: Qn, preset
  // Shift_Register #(.length(9)) shift_register_1: pin names not known; wires that end beside it: RESET, 1'b0, and_1_out, CLK, RX_IN
  and and_3 (and_3_out, d_ff_1_q, SIGN_OUT);
  Register #(.width(7)) register_1 (.D(undriven), .en(and_3_out), .clk(CLK), .Q(DATA_OUT), .clr(RESET));

  // Notes on the sheet:
  //   Чота надо делать с этим
  //   Так же можно не инвертировать CLK у конечного регистра. 
  //   3И идёт на вход D ещё одного триггера. Его Q будет загораться на 1 такт позже, чем счётчик дошёл до 7. Поставить его к WE регистра.
  //   Сдвиг разрешён только в RECEIVE и только пока не досчитали до 9. На 10-м такте (когда CNT_EQ_9=1) сдвиг запрещается, чтобы не сдвинуть лишний раз. 
  //   Это концепт
  //   Когда происходит захват: ровно на один такт, когда счётчик достиг 9 и автомат ещё в RECEIVE. В этот момент в Q7…Q1 лежат чистые 7 бит данных.
endmodule

module rx_WORKSAAAAAAAAA (
  input  RESET,
  input  CLK,
  input  RX_IN,
  output SIGN_OUT,
  output [6:0] DATA_OUT
);

  wire and_1_out, and_2_out, comparator_1_eq, d_ff_1_q, or_1_out, or_2_out;
  wire [3:0] counter_sync_4bit_1_s0;
  wire [6:0] undriven;

  or or_1 (or_1_out, comparator_1_eq, RESET);
  counter_sync_4bit counter_sync_4bit_1 (
    .EN(d_ff_1_q), .CLK(CLK), .RESET(or_1_out), .S0(counter_sync_4bit_1_s0[0]),
    .S1(counter_sync_4bit_1_s0[1]), .S2(counter_sync_4bit_1_s0[2]), .S3(counter_sync_4bit_1_s0[3]));
  Comparator #(.width(4)) comparator_1 (.a(counter_sync_4bit_1_s0), .b(4'b1000), .eq(comparator_1_eq));  // open: gt, lt
  and and_1 (and_1_out, ~comparator_1_eq, d_ff_1_q);  // AND_Gate
  and and_2 (and_2_out, ~comparator_1_eq, d_ff_1_q);  // AND_Gate
  D_Flip_Flop d_ff_1 (.D(or_2_out), .clk(CLK), .Q(d_ff_1_q), .reset(RESET));  // open: Qn, preset
  or or_2 (or_2_out, ~RX_IN, and_1_out);  // OR_Gate
  // Shift_Register #(.length(9)) shift_register_1: pin names not known; wires that end beside it: RESET, 1'b0, and_2_out, CLK, RX_IN
  Register #(.width(7)) register_1 (.D(undriven), .en(comparator_1_eq), .clk(CLK), .Q(DATA_OUT), .clr(RESET));
  D_Flip_Flop d_ff_2 (.D(comparator_1_eq), .clk(CLK), .Q(SIGN_OUT), .reset(RESET));  // open: Qn, preset

  // Other names for the same wires on the sheet: R = RESET

  // Notes on the sheet:
  //   Чота надо делать с этим
endmodule

module rx_please (
  input  RESET,
  input  CLK,
  input  RX_IN,
  output [6:0] DATA_OUT,
  output SIGN_OUT
);

  wire and_1_out, and_3_out, comparator_1_eq, IDL_out, nor_1_out, nor_2_out, or_1_out, REC_out;
  wire [1:0] or_2_out, register_1_q;
  wire [3:0] counter_sync_4bit_1_s0;
  wire [6:0] undriven;

  or or_1 (or_1_out, RESET, IDL_out);
  and and_1 (and_1_out, REC_out, ~comparator_1_eq);  // AND_Gate
  counter_sync_4bit counter_sync_4bit_1 (
    .EN(and_1_out), .CLK(CLK), .RESET(or_1_out), .S0(counter_sync_4bit_1_s0[0]),
    .S1(counter_sync_4bit_1_s0[1]), .S2(counter_sync_4bit_1_s0[2]), .S3(counter_sync_4bit_1_s0[3]));
  Comparator #(.width(4)) comparator_1 (.a(counter_sync_4bit_1_s0), .b(4'b1001), .eq(comparator_1_eq));  // open: gt, lt
  nor nor_1 (nor_1_out, register_1_q[0], register_1_q[1], RX_IN);
  or or_2 (or_2_out[0], nor_1_out, nor_2_out);
  nor nor_2 (nor_2_out, register_1_q[0], ~register_1_q[1], comparator_1_eq);  // NOR_Gate
  and and_2 (or_2_out[1], ~register_1_q[0], register_1_q[1], comparator_1_eq);  // AND_Gate
  Register #(.width(2)) register_1 (.D(or_2_out), .clk(CLK), .Q(register_1_q), .clr(or_1_out));  // open: en
  and REC (REC_out, ~register_1_q[0], register_1_q[1]);  // AND_Gate
  nor IDL (IDL_out, register_1_q[0], register_1_q[1]);
  and STP (SIGN_OUT, register_1_q[0], ~register_1_q[1]);  // AND_Gate
  and and_3 (and_3_out, REC_out, ~comparator_1_eq);  // AND_Gate
  // Shift_Register #(.length(9)) shift_register_1: pin names not known; wires that end beside it: RESET, 1'b0, and_3_out, CLK, RX_IN
  Register #(.width(7)) register_2 (.D(undriven), .en(SIGN_OUT), .clk(CLK), .Q(DATA_OUT), .clr(RESET));
endmodule

module counter_sync_4bit (
  input  EN,
  input  CLK,
  input  RESET,
  output S0,
  output S1,
  output S2,
  output S3
);

  wire and_1_out, and_2_out, and_3_out, multiplexer_1_out, multiplexer_2_out, multiplexer_3_out,
       multiplexer_4_out;

  Multiplexer multiplexer_1 (.in0(EN), .in1(S0), .out(multiplexer_1_out), .sel(RESET));
  T_Flip_Flop t_ff_1 (.T(multiplexer_1_out), .clk(CLK), .Q(S0));  // open: Qn, reset, preset
  and and_1 (and_1_out, EN, S0);
  Multiplexer multiplexer_2 (.in0(and_1_out), .in1(S1), .out(multiplexer_2_out), .sel(RESET));
  T_Flip_Flop t_ff_2 (.T(multiplexer_2_out), .clk(CLK), .Q(S1));  // open: Qn, reset, preset
  and and_2 (and_2_out, and_1_out, S1);
  Multiplexer multiplexer_3 (.in0(and_2_out), .in1(S2), .out(multiplexer_3_out), .sel(RESET));
  T_Flip_Flop t_ff_3 (.T(multiplexer_3_out), .clk(CLK), .Q(S2));  // open: Qn, reset, preset
  and and_3 (and_3_out, and_2_out, S2);
  Multiplexer multiplexer_4 (.in0(and_3_out), .in1(S3), .out(multiplexer_4_out), .sel(RESET));
  T_Flip_Flop t_ff_4 (.T(multiplexer_4_out), .clk(CLK), .Q(S3));  // open: Qn, reset, preset

  // Notes on the sheet:
  //   Рельсотрон V2
endmodule

module counter_sync_6bit (
  input  EN,
  input  CLK,
  input  RESET,
  output [5:0] S_OUT
);

  wire and_1_out, and_2_out, and_3_out, and_4_out, and_5_out, multiplexer_1_out, multiplexer_2_out,
       multiplexer_3_out, multiplexer_4_out, multiplexer_5_out, multiplexer_6_out, not_1_out;

  Multiplexer multiplexer_1 (.in0(EN), .in1(not_1_out), .out(multiplexer_1_out), .sel(RESET));
  not not_1 (not_1_out, S_OUT[0]);
  T_Flip_Flop t_ff_1 (.T(multiplexer_1_out), .clk(CLK), .Q(S_OUT[0]));  // open: Qn, reset, preset
  and and_1 (and_1_out, EN, S_OUT[0]);
  Multiplexer multiplexer_2 (.in0(and_1_out), .in1(S_OUT[1]), .out(multiplexer_2_out), .sel(RESET));
  T_Flip_Flop t_ff_2 (.T(multiplexer_2_out), .clk(CLK), .Q(S_OUT[1]));  // open: Qn, reset, preset
  and and_2 (and_2_out, and_1_out, S_OUT[1]);
  Multiplexer multiplexer_3 (.in0(and_2_out), .in1(S_OUT[2]), .out(multiplexer_3_out), .sel(RESET));
  T_Flip_Flop t_ff_3 (.T(multiplexer_3_out), .clk(CLK), .Q(S_OUT[2]));  // open: Qn, reset, preset
  and and_3 (and_3_out, and_2_out, S_OUT[2]);
  Multiplexer multiplexer_4 (.in0(and_3_out), .in1(S_OUT[3]), .out(multiplexer_4_out), .sel(RESET));
  T_Flip_Flop t_ff_4 (.T(multiplexer_4_out), .clk(CLK), .Q(S_OUT[3]));  // open: Qn, reset, preset
  and and_4 (and_4_out, and_3_out, S_OUT[3]);
  Multiplexer multiplexer_5 (.in0(and_4_out), .in1(S_OUT[4]), .out(multiplexer_5_out), .sel(RESET));
  T_Flip_Flop t_ff_5 (.T(multiplexer_5_out), .clk(CLK), .Q(S_OUT[4]));  // open: Qn, reset, preset
  and and_5 (and_5_out, and_4_out, S_OUT[4]);
  Multiplexer multiplexer_6 (.in0(and_5_out), .in1(S_OUT[5]), .out(multiplexer_6_out), .sel(RESET));
  T_Flip_Flop t_ff_6 (.T(multiplexer_6_out), .clk(CLK), .Q(S_OUT[5]));  // open: Qn, reset, preset

  // Notes on the sheet:
  //   Рельсотрон V2
endmodule

module comp_xor_var2 (
  input  [31:0] DATA_IN,
  input  RESET,
  input  CLK,
  output [6:0] COMP_STR,
  output CI_CLR,
  output [5:0] CI_NUM,
  output PUSH
);

  wire button_1_out, comparator_1_eq, comparator_2_eq, multiplexer_1_out, or_1_out, register_1_q, xor_1_out;
  wire [4:0] counter_1_q;

  Button button_1 (.out(button_1_out));
  Counter #(.max('h1f), .width(5)) counter_1 (
    .clr(RESET), .clk(button_1_out), .Q(counter_1_q));  // open: load, up, count, D, carry
  Multiplexer #(.select(5)) multiplexer_1 (
    .in0(DATA_IN[31]), .in1(DATA_IN[30]), .in2(DATA_IN[29]), .in3(DATA_IN[28]), .in4(DATA_IN[27]),
    .in5(DATA_IN[26]), .in6(DATA_IN[25]), .in7(DATA_IN[24]), .in8(DATA_IN[23]), .in9(DATA_IN[22]),
    .in10(DATA_IN[21]), .in11(DATA_IN[20]), .in12(DATA_IN[19]), .in13(DATA_IN[18]), .in14(DATA_IN[17]),
    .in15(DATA_IN[16]), .in16(DATA_IN[15]), .in17(DATA_IN[14]), .in18(DATA_IN[13]), .in19(DATA_IN[12]),
    .in20(DATA_IN[11]), .in21(DATA_IN[10]), .in22(DATA_IN[9]), .in23(DATA_IN[8]), .in24(DATA_IN[7]),
    .in25(DATA_IN[6]), .in26(DATA_IN[5]), .in27(DATA_IN[4]), .in28(DATA_IN[3]), .in29(DATA_IN[2]),
    .in30(DATA_IN[1]), .in31(DATA_IN[0]), .out(multiplexer_1_out), .sel(counter_1_q));
  Comparator #(.width(5)) comparator_1 (.a(counter_1_q), .b({5{1'b0}}), .eq(comparator_1_eq));  // open: gt, lt
  Comparator #(.width(5)) comparator_2 (.a(counter_1_q), .b({5{1'b1}}), .eq(comparator_2_eq));  // open: gt, lt
  or or_1 (or_1_out, comparator_1_eq, PUSH);
  Register #(.width(1)) register_1 (
    .D(multiplexer_1_out), .en(or_1_out), .clk(button_1_out), .Q(register_1_q), .clr(RESET));
  xor xor_1 (xor_1_out, multiplexer_1_out, register_1_q);
  or or_2 (PUSH, xor_1_out, comparator_2_eq);
  // counter_pix counter_pix_1: pin names not known; wires that end beside it: COMP_STR, CI_CLR, CI_NUM
  // Probe on PUSH

  // Notes on the sheet:
  //   Сложная система сжатия. На вход подаются данные строки. 
  //   Полученные сжатые данные будут храниться в ОЗУ.
  //   Тест на 32 пройден
  //   Тест на нечёт пройден
  //   Тут хранится строка
  //   Счётчик строки
  //   Теперь оно... эээ.. ну вроде работает
  //   Выборка бита
  //   Но как немецкий автомобиль - со своими приколами
  //   Сравнение цвета и бита
  //   триггер решает проблему срабатываения PUSH на 0000110
  //   IT'S ALIIIIIIIVE (нет)
  //   Из огня да в полымя.
  //   Возможно, сброс счёта PC эту проблему решит. А может и нет. 
  //   Я ПОНЯЛ ПОЧЕМУ! PUSH действует сначала в 0001000, а потом в 0010000 раз в 2 цикла. 
  //   XOR_OUT - важный выход. Он - индикатор окончания серии.
  //   То есть на что делится проблема: Если мы привязываем PUSH только к XOR, то ломается логика "32 одного цвета подряд". Если привязываем через OR с концом строки - ломается подача. Нужен принудительный сброс счётчика и отправка PUSH.
  //   Слово 7 бит
  //   В том случае, когда пиксели в строке все одинаковые:
  //   Нужен принудительный PUSH когда будет досчёт до 32
  //   Выход COMP_IN принимает значение 0001000 только один раз - в начале. А FIFO почему-то его по кд прокручивает.
  //   Теперь надо решить проблему с тем, что счётчик считает всё далее
  //   От принудительного Push появляются глюки с информацией в FIFO... Либо увеличивать слово COMP_STR до 8 бит, либо думы думать
  //   То есть нам в данном случае МЕШАЕТ подсчёт до конца строки. Однако сброс счётчика PC + принудительный PUSH гипотетически могут решить эту проблему.
endmodule

module PC_save (
  input  COLOR_IN,
  input  PUSH,
  input  CLK,
  input  RESET,
  output [6:0] MEMORY_OUT,
  output CI_COLOR,
  output [5:0] CI_BIT_COUNT
);

  wire [5:0] adder_1_out, multiplexer_1_out, register_2_q;

  Multiplexer #(.width(6)) multiplexer_1 (.in0(adder_1_out), .in1(6'b000001), .out(multiplexer_1_out), .sel(PUSH));
  Register #(.width(6)) register_1 (.D(multiplexer_1_out), .en(1'b1), .clk(CLK), .Q(CI_BIT_COUNT), .clr(RESET));
  Register #(.width(6)) register_2 (.Q(register_2_q));  // open: D, en, clk, clr
  // Probe on {CI_BIT_COUNT, COLOR_IN}
  Register #(.width(6)) register_3 (.D(register_2_q));  // open: en, clk, Q, clr
  Adder #(.width(6)) adder_1 (.a(CI_BIT_COUNT), .b(6'b000001), .out(adder_1_out));  // open: cin, cout

  assign CI_COLOR = COLOR_IN;
  assign MEMORY_OUT = {CI_BIT_COUNT, COLOR_IN};

  // Notes on the sheet:
  //   Регистр держит в себе текущее 5-битное число
  //   Мультиплексор - по сути развилка. Поясняю.
  //   Система подсчёта последовательности пикселей с одинаковым цветом.
  //   XOR - по сути простейший инвертированный компаратор.
  //   То есть на регистр подаётся константа 00001, как у сумматора.
  //   . 
  //   Сумматор берёт число из регистра и всегда прибавляет константу 1 - то есть в 5 бит это 00001
  //   Пока бит данных и бит цвета равны, то есть COMP_IN = 0, у нас продолжается зацикленная работа с сумматором.
  //   строку полностью заполенную оно считает... странно, но правильно - в 2 цикла сброса CI_BIT_COUNT до 64 фактически
  //   Как только бит данных и бит цвета перестанут быть равны, то есть COMP_IN = 1, у нас начинается новая серия серия с единицы.
endmodule

module decomp_DONOTTOUCH (
  input  RESET,
  input  SIGN,
  input  CLK,
  input  [6:0] DATA_IN,
  output [23:0] DATA_OUT,
  output [4:0] X0,
  output [4:0] Y0,
  output WE
);

  wire and_1_out, and_3_out, and_4_out, and_5_out, and_6_out, and_7_out, C_REG_q, comparator_1_eq,
       comparator_2_eq, comparator_3_eq, d_ff_1_q, EN_out, fifo_buffer_v1_1_p3, fifo_buffer_v1_1_p6, L_out,
       multiplexer_3_out, multiplexer_4_out, multiplexer_5_out, nand_1_out, nand_2_out, OE_out, or_1_out,
       or_4_out, R_out, ram_1_dout, ram_2_dout, xor_1_out, Y_out;
  wire [0:0] fifo_buffer_v1_1_p7, or_3_out;
  wire [1:0] and_2_out, register_1_q, register_2_q;
  wire [4:0] counter_1_q, multiplexer_1_out, multiplexer_2_out;
  wire [5:0] counter_2_q, fifo_buffer_v1_1_p7_2, L_REG_q;

  // Probe on nothing
  Register #(.width(1)) C_REG (.D(fifo_buffer_v1_1_p7[0]), .en(L_out), .clk(CLK), .Q(C_REG_q), .clr(RESET));
  Register #(.width(6)) L_REG (.D(fifo_buffer_v1_1_p7_2), .en(L_out), .clk(CLK), .Q(L_REG_q), .clr(RESET));
  // FIFO_buffer_v1 fifo_buffer_v1_1: pin names not known; wires that end beside it: RESET, SIGN, fifo_buffer_v1_1_p3, DATA_IN, CLK, fifo_buffer_v1_1_p6, {fifo_buffer_v1_1_p7_2, fifo_buffer_v1_1_p7[0]}
  nand nand_1 (nand_1_out, nand_2_out, R_out);
  nand nand_2 (nand_2_out, nand_1_out, WE);
  or or_1 (or_1_out, RESET, R_out);
  and and_1 (and_1_out, ~comparator_2_eq, register_1_q[1]);  // AND_Gate
  Counter #(.max('h1f), .width(5)) counter_1 (
    .clr(or_1_out), .count(EN_out), .clk(CLK), .Q(counter_1_q));  // open: load, up, D, carry
  Counter #(.max('h3f), .ongoal("stay"), .width(6)) counter_2 (
    .clr(RESET), .load(L_out), .up(1'b0), .count(EN_out), .clk(CLK), .D(L_REG_q), .Q(counter_2_q));  // open: carry
  or or_2 (and_2_out[1], register_1_q[0], and_1_out);
  and and_2 (and_2_out[0], ~register_1_q[1], ~register_1_q[0], fifo_buffer_v1_1_p6);  // AND_Gate
  and and_3 (and_3_out, nand_1_out, ~register_2_q[0]);  // AND_Gate
  Register #(.width(2)) register_1 (.D(and_2_out), .clk(CLK), .Q(register_1_q), .clr(RESET));  // open: en
  and and_4 (and_4_out, ~register_2_q[0], and_3_out);  // AND_Gate
  and and_5 (and_5_out, register_2_q[0], comparator_3_eq);
  or or_3 (or_3_out[0], and_4_out, and_5_out);
  Comparator #(.width(5)) comparator_1 (.a(counter_1_q), .b({5{1'b1}}), .eq(comparator_1_eq));  // open: gt, lt
  Comparator #(.width(6)) comparator_2 (.a(counter_2_q), .b({6{1'b0}}), .eq(comparator_2_eq));  // open: gt, lt
  Register #(.width(2)) register_2 (.D({1'b0, or_3_out[0]}), .clk(CLK), .Q(register_2_q), .clr(RESET));  // open: en
  and P (fifo_buffer_v1_1_p3, ~register_1_q[1], ~register_1_q[0], fifo_buffer_v1_1_p6);  // AND_Gate
  and L (L_out, ~register_1_q[1], register_1_q[0]);  // AND_Gate
  and EN (EN_out, register_1_q[1], ~register_1_q[0], ~comparator_2_eq);  // AND_Gate
  and R (R_out, register_1_q[1], ~register_1_q[0], comparator_2_eq, comparator_1_eq);  // AND_Gate
  and RS (WE, ~register_2_q[0], and_3_out);  // AND_Gate
  and Y (Y_out, register_2_q[0], comparator_3_eq);
  and OE (OE_out, register_2_q[0], ~comparator_3_eq);  // AND_Gate
  Multiplexer #(.width(5)) multiplexer_1 (.in0(X0), .in1(counter_1_q), .out(multiplexer_1_out), .sel(and_6_out));
  and and_6 (and_6_out, EN_out, ~d_ff_1_q);  // AND_Gate
  Multiplexer #(.width(5)) multiplexer_2 (.in0(X0), .in1(counter_1_q), .out(multiplexer_2_out), .sel(and_7_out));
  and and_7 (and_7_out, EN_out, d_ff_1_q);
  Multiplexer multiplexer_3 (.in0(C_REG_q), .in1(1'b1), .out(multiplexer_3_out), .sel(and_6_out));
  Multiplexer multiplexer_4 (.in0(C_REG_q), .in1(1'b1), .out(multiplexer_4_out), .sel(and_7_out));
  D_Flip_Flop d_ff_1 (.D(xor_1_out), .clk(CLK), .Q(d_ff_1_q), .reset(RESET));  // open: Qn, preset
  xor xor_1 (xor_1_out, R_out, d_ff_1_q);
  RAM #(.addrWidth(5), .dataWidth(1)) ram_1 (
    .addr(multiplexer_1_out), .we(1'b1), .clk(CLK), .din(multiplexer_3_out), .dout(ram_1_dout));  // open: oe
  RAM #(.addrWidth(5), .dataWidth(1)) ram_2 (
    .addr(multiplexer_2_out), .we(1'b1), .clk(CLK), .din(multiplexer_4_out), .dout(ram_2_dout));  // open: oe
  Counter #(.max('h1f), .width(5)) counter_3 (
    .clr(or_4_out), .count(OE_out), .clk(CLK), .Q(X0));  // open: load, up, D, carry
  or or_4 (or_4_out, RESET, WE);
  Comparator #(.width(5)) comparator_3 (.a(X0), .b({5{1'b1}}), .eq(comparator_3_eq));  // open: gt, lt
  Multiplexer multiplexer_5 (.in0(ram_1_dout), .in1(ram_2_dout), .out(multiplexer_5_out), .sel(d_ff_1_q));
  Multiplexer #(.width(24)) multiplexer_6 (.in0({24{1'b0}}), .in1({24{1'b1}}), .out(DATA_OUT), .sel(multiplexer_5_out));
  Counter #(.max('h1f), .width(5)) counter_4 (
    .clr(RESET), .count(Y_out), .clk(CLK), .Q(Y0));  // open: load, up, D, carry
endmodule

module decomp_huh (
  input  RESET,
  input  CLK,
  input  SIGN,
  input  [6:0] DATA_IN,
  output [23:0] DATA_OUT,
  output [4:0] X0,
  output WE,
  output [4:0] Y0
);

  wire and_1_out, and_2_out, and_3_out, and_4_out, and_5_out, and_6_out, and_7_out, C_out, C_REG_q,
       comparator_1_eq, comparator_2_eq, fifo_morebit_1_valid_sig, I_out, L_out, or_3_out, P_out, R_out,
       ram_1_dout, W_out;
  wire [1:0] or_1_out, register_1_q;
  wire [5:0] counter_1_q, L_REG_q;
  wire [6:0] fifo_morebit_1_data_out;

  FIFO_morebit fifo_morebit_1 (
    .WRITE_SIG(SIGN), .READ_SIG(P_out), .DATA_IN(DATA_IN), .CLK(CLK), .VALID_SIG(fifo_morebit_1_valid_sig),
    .DATA_OUT(fifo_morebit_1_data_out));  // open: RESET, write_s, read_s
  Register #(.width(1)) C_REG (.D(fifo_morebit_1_data_out[0]), .en(L_out), .clk(CLK), .Q(C_REG_q), .clr(RESET));
  Register #(.width(6)) L_REG (.D(fifo_morebit_1_data_out[6:1]), .en(L_out), .clk(CLK), .Q(L_REG_q), .clr(RESET));
  and and_1 (and_1_out, ~register_1_q[1], ~register_1_q[0], fifo_morebit_1_valid_sig);  // AND_Gate
  and and_2 (and_2_out, register_1_q[1], ~register_1_q[0], comparator_1_eq, comparator_2_eq);  // AND_Gate
  or or_1 (or_1_out[0], and_1_out, and_2_out, and_3_out);
  and and_3 (and_3_out, register_1_q[1], register_1_q[0], ~comparator_2_eq);  // AND_Gate
  and and_4 (and_4_out, ~register_1_q[1], register_1_q[0]);  // AND_Gate
  and and_5 (and_5_out, register_1_q[1], ~register_1_q[0], ~comparator_1_eq);  // AND_Gate
  and and_6 (and_6_out, register_1_q[1], ~register_1_q[0], comparator_1_eq, comparator_2_eq);  // AND_Gate
  and and_7 (and_7_out, register_1_q[1], register_1_q[0], ~comparator_2_eq);  // AND_Gate
  Register #(.width(2)) register_1 (.D(or_1_out), .clk(CLK), .Q(register_1_q), .clr(RESET));  // open: en
  or or_2 (or_1_out[1], and_4_out, and_5_out, and_6_out, and_7_out);
  and P (P_out, ~register_1_q[1], ~register_1_q[0], fifo_morebit_1_valid_sig);  // AND_Gate
  and L (L_out, ~register_1_q[1], register_1_q[0]);  // AND_Gate
  and W (W_out, register_1_q[1], ~register_1_q[0], ~comparator_1_eq);  // AND_Gate
  or C (C_out, W_out, WE);
  and and_8 (WE, register_1_q[1], register_1_q[0]);
  and R (R_out, register_1_q[1], ~register_1_q[0], comparator_1_eq, comparator_2_eq);  // AND_Gate
  and I (I_out, register_1_q[1], register_1_q[0], comparator_2_eq);
  Counter #(.max('h3f), .width(6)) counter_1 (
    .clr(RESET), .load(L_out), .up(1'b0), .count(C_out), .clk(CLK), .D(L_REG_q), .Q(counter_1_q));  // open: carry
  Counter #(.max('h1f), .width(5)) counter_2 (
    .clr(or_3_out), .count(C_out), .clk(CLK), .Q(X0));  // open: load, up, D, carry
  or or_3 (or_3_out, R_out, RESET);
  Counter #(.max('h1f), .width(5)) counter_3 (
    .clr(RESET), .count(I_out), .clk(CLK), .Q(Y0));  // open: load, up, D, carry
  Comparator #(.width(6)) comparator_1 (.a(counter_1_q), .b({6{1'b0}}), .eq(comparator_1_eq));  // open: gt, lt
  Comparator #(.width(5)) comparator_2 (.a(X0), .b({5{1'b1}}), .eq(comparator_2_eq));  // open: gt, lt
  RAM #(.addrWidth(5), .dataWidth(1)) ram_1 (
    .addr(X0), .we(W_out), .clk(CLK), .din(C_REG_q), .dout(ram_1_dout));  // open: oe
  Multiplexer #(.width(24)) multiplexer_1 (.in0({24{1'b0}}), .in1({24{1'b1}}), .out(DATA_OUT), .sel(ram_1_dout));
endmodule

module FIFO_morebit (
  input  RESET,
  input  WRITE_SIG,
  input  READ_SIG,
  input  [6:0] DATA_IN,
  input  CLK,
  output VALID_SIG,
  output [6:0] write_s,
  output [6:0] DATA_OUT,
  output [6:0] read_s
);

  wire comparator_1_eq;
  wire [6:0] multiplexer_1_out;

  Counter #(.max('h7f), .width(7)) write (
    .clr(RESET), .count(WRITE_SIG), .clk(CLK), .Q(write_s));  // open: load, up, D, carry
  Counter #(.max('h7f), .width(7)) read (
    .clr(RESET), .count(READ_SIG), .clk(CLK), .Q(read_s));  // open: load, up, D, carry
  Multiplexer #(.width(7)) multiplexer_1 (.in0(read_s), .in1(write_s), .out(multiplexer_1_out), .sel(WRITE_SIG));
  RAM #(.addrWidth(7), .clearpin("true"), .dataWidth(7)) ram_1 (
    .addr(multiplexer_1_out), .we(WRITE_SIG), .oe(1'b1), .clk(CLK), .din(DATA_IN), .dout(DATA_OUT),
    .clr(RESET));
  not not_1 (VALID_SIG, comparator_1_eq);
  Comparator #(.width(7)) comparator_1 (.a(write_s), .b(read_s), .eq(comparator_1_eq));  // open: gt, lt

  // Notes on the sheet:
  //   Выдаёт 1, если ячейка не пуста
  //   Cчётчик WRITE увеличивается на 1 каждый раз, как происходит импульс XOR в блоке сжатия
  //   Счётчик READ увеличивается на 1 каждый раз, когда передатчик успешно отправил слово в канал.
endmodule

module decomp_naaaahb (
  input  RESET,
  input  SIGN,
  input  [6:0] DATA_IN,
  input  CLK,
  input  stahp,
  output [2:0] DATA_RGB_OUT,
  output WE_RGB,
  output [4:0] X0,
  output [4:0] Y0
);

  wire and_1_out, C_REG_q, LOAD, or_2_out, or_3_out, POP, VALID, W_out, ZERO;
  wire [1:0] and_2_out, register_1_q;
  wire [5:0] LENGTH_COUNTER_q;
  wire [6:0] sotiiireeed_1_data_out;

  or or_1 (and_2_out[1], register_1_q[0], and_1_out);
  and and_1 (and_1_out, register_1_q[1], ~ZERO);  // AND_Gate
  and and_2 (and_2_out[0], ~register_1_q[1], or_2_out);  // AND_Gate
  or or_2 (or_2_out, register_1_q[0], VALID);
  Register #(.width(2)) register_1 (.D(and_2_out), .clk(CLK), .Q(register_1_q), .clr(stahp));  // open: en
  SOTIIIREEED sotiiireeed_1 (
    .wr(SIGN), .rd(POP), .clk(CLK), .d_in(DATA_IN), .CLR(stahp), .V(VALID), .data_out(sotiiireeed_1_data_out));
  Register #(.width(1)) C_REG (.D(sotiiireeed_1_data_out[0]), .en(LOAD), .clk(CLK), .Q(C_REG_q), .clr(RESET));
  and P (POP, ~register_1_q[1], register_1_q[0]);  // AND_Gate
  and L (LOAD, register_1_q[0], register_1_q[1]);
  and W (W_out, register_1_q[1], ~register_1_q[0]);  // AND_Gate
  and C (WE_RGB, W_out, ~ZERO);  // AND_Gate
  Counter #(.max('h3f), .width(6)) LENGTH_COUNTER (
    .clr(RESET), .load(LOAD), .up(1'b0), .count(WE_RGB), .clk(CLK), .D(sotiiireeed_1_data_out[6:1]),
    .Q(LENGTH_COUNTER_q));  // open: carry
  Counter #(.max('h3ff), .width(10)) XY_CNT (
    .clr(or_3_out), .count(WE_RGB), .clk(CLK), .Q({Y0, X0}));  // open: load, up, D, carry
  or or_3 (or_3_out, RESET, stahp);
  Multiplexer #(.width(3)) multiplexer_1 (.in0(3'b000), .in1(3'b111), .out(DATA_RGB_OUT), .sel(C_REG_q));
  Comparator #(.width(6)) comparator_1 (.a(LENGTH_COUNTER_q), .b({6{1'b0}}), .eq(ZERO));  // open: gt, lt
  yet_another_fifo yet_another_fifo_1 ();  // open: WR_SIG, RD_SIG, CLK, DATA_IN, R, FL, VALID, DATA_OUT
  tired tired_1 ();  // open: WR_SIG, RD_SIG, CLK, DATA_IN, R, flush, VALID, DATA_OUT
  dual_port_RAM_my dual_port_ram_my_1 ();  // open: WR_SIG, RD_SIG, CLK, DATA_IN, R, VALID_SIG, DATA_OUT
  TIIIREEEEED tiiireeeeed_1 ();  // open: WR_SIG, RD_SIG, CLK, DATA_IN, R, flush, VALID, DATA_OUT

  // Other names for the same wires on the sheet: DRAW = WE_RGB; R = RESET
endmodule

module main_with_memtest (
  input  Drawing_EN,
  input  [23:0] COLOR_BACK,
  input  [23:0] COLOR_BASE,
  input  RESET,
  output [6:0] CI1,
  output [6:0] CI2
);

  wire CLK_out, comp_xor_1_p4, comp_xor_1_p5, comp_xor_1_p6, decomp_naaaahb_1_p5, decomp_naaaahb_1_p6,
       decomp_naaaahb_1_p7, decomp_naaaahb_1_p8, fifo_buffer_v1_1_p3, fifo_buffer_v1_1_p6, RC_out, RCC_out,
       rx_worksaaaaaaaaa_1_p4, rx_worksaaaaaaaaa_1_p5, stability_unput_v4_v2_1_p3,
       stability_unput_v4_v2_1_p4, use_transmitter_reg_v1_1_tx_out;
  wire [1:0] control_1_control_out;
  wire [2:0] rgb_video_1_p10;
  wire [6:0] fifo_buffer_v1_1_p7;
  wire [9:0] counter_1_q;
  wire [31:0] mem_test_1_line_out;

  Clock CLK (.out(CLK_out));
  Button button_1 ();  // open: out
  Button RC (.out(RC_out));
  Button RCC (.out(RCC_out));
  Counter #(.max('h3ff), .width(10)) counter_1 (
    .clr(RESET), .clk(CLK_out), .Q(counter_1_q));  // open: load, up, count, D, carry
  // stability_unput_v4_v2 stability_unput_v4_v2_1: pin names not known; wires that end beside it: CI1, CI2, stability_unput_v4_v2_1_p3, stability_unput_v4_v2_1_p4
  comp_v2 comp_v2_1 ();  // open: LINE_IN, RESET, CLK, PUSH, out_5, out_6, COMP_STR
  control control_1 (.CONTROL_OUT(control_1_control_out));  // open: RC, RESET, CLK, RCC
  mem_test mem_test_1 (.CONTROL(control_1_control_out), .COUNTER(counter_1_q[9:5]), .LINE_OUT(mem_test_1_line_out));
  // RGB_Video #(.height(32), .scale(8), .width(32)) rgb_video_1: pin names not known; wires that end beside it: COLOR_BACK, COLOR_BASE, mem_test_1_line_out, counter_1_q[4:0], RESET, CLK_out, 1'b1, counter_1_q[4:0], counter_1_q[9:5], rgb_video_1_p10
  pixel_selector pixel_selector_1 (.DATA_output(rgb_video_1_p10));  // open: ROM_input, COUNTER_input, COLOR_0, COLOR_1
  // comp_xor comp_xor_1: pin names not known; wires that end beside it: mem_test_1_line_out, RESET, CLK_out, comp_xor_1_p4, comp_xor_1_p5, comp_xor_1_p6, comp_xor_1_p5
  compression_v1 compression_v1_1 ();  // open: DATA_IN, RESET, CLK, COMP_STR, CI_CLR, CI_NUM, PUSH
  // FIFO_buffer_v1 fifo_buffer_v1_1: pin names not known; wires that end beside it: RESET, comp_xor_1_p6, fifo_buffer_v1_1_p3, comp_xor_1_p4, CLK_out, fifo_buffer_v1_1_p6, fifo_buffer_v1_1_p7
  // Probe on fifo_buffer_v1_1_p7
  // Probe on rx_worksaaaaaaaaa_1_p4
  // Probe on comp_xor_1_p4
  // Probe on use_transmitter_reg_v1_1_tx_out
  use_transmitter_reg_v1 use_transmitter_reg_v1_1 (
    .CLK(CLK_out), .RESET(RESET), .VALID_SIG(fifo_buffer_v1_1_p6), .DATA_IN(fifo_buffer_v1_1_p7),
    .TX_SIGNAL(fifo_buffer_v1_1_p3), .TX_OUT(use_transmitter_reg_v1_1_tx_out));
  use_transmitter_reg_v1 use_transmitter_reg_v1_2 ();  // open: CLK, RESET, VALID_SIG, DATA_IN, TX_SIGNAL, TX_OUT
  // rx_WORKSAAAAAAAAA rx_worksaaaaaaaaa_1: pin names not known; wires that end beside it: RESET, CLK_out, use_transmitter_reg_v1_1_tx_out, rx_worksaaaaaaaaa_1_p4, rx_worksaaaaaaaaa_1_p5
  // decomp_naaaahb decomp_naaaahb_1: pin names not known; wires that end beside it: RESET, rx_worksaaaaaaaaa_1_p5, rx_worksaaaaaaaaa_1_p4, CLK_out, decomp_naaaahb_1_p5, decomp_naaaahb_1_p6, decomp_naaaahb_1_p7, decomp_naaaahb_1_p8
  // RGB_Video #(.height(32), .scale(8), .width(32)) rgb_video_2: pin names not known; wires that end beside it: RESET, CLK_out, decomp_naaaahb_1_p6, decomp_naaaahb_1_p7, decomp_naaaahb_1_p8, decomp_naaaahb_1_p5

  // Notes on the sheet:
  //   База цепи. 
  //   1. Сделать блок сжатия
  //   2. Сделать блок разжатия
  //   3. Проверить систему прямо
  //   4. Сделать систему  UART
  //   4.1 Сделать TX 
  //   4.2 Сделать RX
  //   4.3 Проверить в отдельности передачу картинки
endmodule
module there_is_another_decomp (
  input  RESET,
  input  SIGN,
  input  [6:0] DATA_IN,
  input  CLK,
  output [23:0] DATA_RGB_OUT,
  output [4:0] X0,
  output [4:0] Y0,
  output WE
);

  wire and_1_out, and_2_out, and_3_out, and_4_out, and_5_out, and_6_out, and_7_out, C_REG_q, comparator_1_eq,
       comparator_2_eq, EN_C_out, fifo_morebit_1_valid_sig, multiplexer_2_out, PL_out, ram_1_dout, SD_out,
       Y_out;
  wire [1:0] or_2_out, register_1_q;
  wire [5:0] LENGTH_COUNTER_q;
  wire [6:0] fifo_morebit_1_data_out;

  and and_1 (and_1_out, ~register_1_q[1], register_1_q[0]);  // AND_Gate
  and and_2 (and_2_out, register_1_q[1], ~register_1_q[0], ~comparator_1_eq);  // AND_Gate
  or or_1 (or_2_out[1], and_1_out, and_2_out, and_3_out, and_4_out);
  and and_3 (and_3_out, register_1_q[1], ~register_1_q[0], comparator_1_eq, comparator_2_eq);  // AND_Gate
  and and_4 (and_4_out, register_1_q[1], register_1_q[0], ~comparator_2_eq);  // AND_Gate
  and and_5 (and_5_out, ~register_1_q[1], ~register_1_q[0], fifo_morebit_1_valid_sig);  // AND_Gate
  and and_6 (and_6_out, register_1_q[1], ~register_1_q[0], comparator_1_eq, comparator_2_eq);  // AND_Gate
  or or_2 (or_2_out[0], and_5_out, and_6_out, and_7_out);
  and and_7 (and_7_out, register_1_q[1], register_1_q[0], ~comparator_2_eq);  // AND_Gate
  Register #(.width(2)) register_1 (.D(or_2_out), .clk(CLK), .Q(register_1_q), .clr(RESET));  // open: en
  FIFO_morebit fifo_morebit_1 (
    .RESET(RESET), .WRITE_SIG(SIGN), .READ_SIG(PL_out), .DATA_IN(DATA_IN), .CLK(CLK),
    .VALID_SIG(fifo_morebit_1_valid_sig), .DATA_OUT(fifo_morebit_1_data_out));  // open: write_s, read_s
  Register #(.width(1)) C_REG (.D(fifo_morebit_1_data_out[0]), .en(PL_out), .clk(CLK), .Q(C_REG_q), .clr(RESET));
  and PL (PL_out, ~register_1_q[1], register_1_q[0]);  // AND_Gate
  and SD (SD_out, register_1_q[1], ~register_1_q[0], ~comparator_1_eq);  // AND_Gate
  and W (WE, register_1_q[1], register_1_q[0]);
  or EN_C (EN_C_out, SD_out, WE);
  and Y (Y_out, WE, comparator_2_eq);
  Counter #(.max('h3f), .width(6)) LENGTH_COUNTER (
    .clr(RESET), .load(PL_out), .up(1'b0), .count(SD_out), .clk(CLK), .D(fifo_morebit_1_data_out[6:1]),
    .Q(LENGTH_COUNTER_q));  // open: carry
  Counter #(.max('h1f), .width(5)) X_COUNTER (
    .clr(RESET), .count(EN_C_out), .clk(CLK), .Q(X0));  // open: load, up, D, carry
  Multiplexer #(.width(24)) multiplexer_1 (.in0({24{1'b0}}), .in1({24{1'b1}}), .out(DATA_RGB_OUT), .sel(ram_1_dout));
  Comparator #(.mode("unsigned"), .width(6)) comparator_1 (
    .a(LENGTH_COUNTER_q), .b({6{1'b0}}), .eq(comparator_1_eq));  // open: gt, lt
  Multiplexer multiplexer_2 (.in0(1'b0), .in1(C_REG_q), .out(multiplexer_2_out), .sel(SD_out));
  Comparator #(.mode("unsigned"), .width(5)) comparator_2 (
    .a(X0), .b({5{1'b1}}), .eq(comparator_2_eq));  // open: gt, lt
  RAM #(.addrWidth(5), .dataWidth(1)) ram_1 (
    .addr(X0), .we(SD_out), .clk(CLK), .din(multiplexer_2_out), .dout(ram_1_dout));  // open: oe
  Counter #(.max('h1f), .width(5)) Y_COUNTER (
    .clr(RESET), .count(Y_out), .clk(CLK), .Q(Y0));  // open: load, up, D, carry

  // Notes on the sheet:
  //   1
  //   0
endmodule

module counter_4bit_1000 (
  input  EN,
  input  CLK,
  input  RESET,
  output OUT_1000
);

  wire and_1_out, and_2_out, and_3_out, multiplexer_1_out, multiplexer_2_out, multiplexer_3_out,
       multiplexer_4_out, or_1_out, t_ff_1_q, t_ff_2_q, t_ff_3_q, t_ff_4_q;

  nor nor_1 (OUT_1000, t_ff_1_q, t_ff_2_q, t_ff_3_q, ~t_ff_4_q);  // NOR_Gate
  Multiplexer multiplexer_1 (.in0(EN), .in1(t_ff_1_q), .out(multiplexer_1_out), .sel(or_1_out));
  or or_1 (or_1_out, OUT_1000, RESET);
  T_Flip_Flop t_ff_1 (.T(multiplexer_1_out), .clk(CLK), .Q(t_ff_1_q));  // open: Qn, reset, preset
  and and_1 (and_1_out, EN, t_ff_1_q);
  Multiplexer multiplexer_2 (.in0(and_1_out), .in1(t_ff_2_q), .out(multiplexer_2_out), .sel(or_1_out));
  T_Flip_Flop t_ff_2 (.T(multiplexer_2_out), .clk(CLK), .Q(t_ff_2_q));  // open: Qn, reset, preset
  and and_2 (and_2_out, and_1_out, t_ff_2_q);
  Multiplexer multiplexer_3 (.in0(and_2_out), .in1(t_ff_3_q), .out(multiplexer_3_out), .sel(or_1_out));
  T_Flip_Flop t_ff_3 (.T(multiplexer_3_out), .clk(CLK), .Q(t_ff_3_q));  // open: Qn, reset, preset
  and and_3 (and_3_out, and_2_out, t_ff_3_q);
  Multiplexer multiplexer_4 (.in0(and_3_out), .in1(t_ff_4_q), .out(multiplexer_4_out), .sel(or_1_out));
  T_Flip_Flop t_ff_4 (.T(multiplexer_4_out), .clk(CLK), .Q(t_ff_4_q));  // open: Qn, reset, preset

  // Notes on the sheet:
  //   Рельсотрон V2
endmodule

module bruh (
  input  [31:0] in_1
);

  wire button_1_out, clock_1_out, decomp_naaaahb_1_we_rgb, undriven;
  wire [2:0] decomp_naaaahb_1_data_rgb_out;
  wire [4:0] decomp_naaaahb_1_x0, decomp_naaaahb_1_y0;
  wire [6:0] comp_xor_1_comp_str;

  Button button_1 (.out(button_1_out));
  Clock clock_1 (.out(clock_1_out));
  DotMatrix #(.matrixcols(1), .matrixrows(32)) dotmatrix_1 (.col0(in_1));
  comp_xor comp_xor_1 (
    .DATA_IN(in_1), .RESET(button_1_out), .CLK(clock_1_out), .COMP_STR(comp_xor_1_comp_str));  // open: PUSH
  decomp_naaaahb decomp_naaaahb_1 (
    .RESET(button_1_out), .SIGN(undriven), .DATA_IN(comp_xor_1_comp_str), .CLK(clock_1_out),
    .DATA_RGB_OUT(decomp_naaaahb_1_data_rgb_out), .WE_RGB(decomp_naaaahb_1_we_rgb), .X0(decomp_naaaahb_1_x0),
    .Y0(decomp_naaaahb_1_y0));  // open: stahp
  // RGB_Video #(.height(32), .scale(8), .width(32)) rgb_video_1: pin names not known; wires that end beside it: button_1_out, clock_1_out, decomp_naaaahb_1_we_rgb, decomp_naaaahb_1_x0, decomp_naaaahb_1_y0, decomp_naaaahb_1_data_rgb_out
endmodule

module eugh (
  input  START_TEST
);

  wire clock_1_out, comparator_1_eq, decomp_naaaahb_1_we_rgb, s_r_ff_1_q, SIGN_out;
  wire [2:0] decomp_naaaahb_1_data_rgb_out;
  wire [4:0] decomp_naaaahb_1_x0, decomp_naaaahb_1_y0;
  wire [6:0] counter_1_q, rom_1_data;

  Clock clock_1 (.out(clock_1_out));
  Counter #(.max('h5f), .width(7)) counter_1 (
    .clk(clock_1_out), .Q(counter_1_q));  // open: clr, load, up, count, D, carry
  Comparator #(.mode("unsigned"), .width(7)) comparator_1 (
    .a(counter_1_q), .b(7'b1011111), .eq(comparator_1_eq));  // open: gt, lt
  ROM #(.addrWidth(7), .dataWidth(7)) rom_1 (.addr(counter_1_q), .data(rom_1_data));
  S_R_Flip_Flop s_r_ff_1 (
    .S(START_TEST), .R(comparator_1_eq), .clk(clock_1_out), .Q(s_r_ff_1_q));  // open: reset, Qn, preset
  and SIGN (SIGN_out, s_r_ff_1_q, ~clock_1_out);  // AND_Gate
  decomp_naaaahb decomp_naaaahb_1 (
    .SIGN(SIGN_out), .DATA_IN(rom_1_data), .CLK(clock_1_out), .DATA_RGB_OUT(decomp_naaaahb_1_data_rgb_out),
    .WE_RGB(decomp_naaaahb_1_we_rgb), .X0(decomp_naaaahb_1_x0), .Y0(decomp_naaaahb_1_y0));  // open: RESET, stahp
  // RGB_Video #(.height(32), .scale(8), .width(32)) rgb_video_1: pin names not known; wires that end beside it: clock_1_out, decomp_naaaahb_1_we_rgb, decomp_naaaahb_1_x0, decomp_naaaahb_1_y0, decomp_naaaahb_1_data_rgb_out

  // Notes on the sheet:
  //   contents of rom_1 (hex, n*v repeats v):
  //   1e 5 1e 1e 5 1e 1c 9 1c 1c 9 1c 1a d 1a 1a d 1a 18 11 18 18 11 18 16 15 16 16 15 16 14 19 14 14 19
  //   14 12 1d 12 12 1d 12 10 21 10 10 21 10 e 25 e e 25 e c 29 c c 29 c a 2d a a 2d a 8 31 8 8 31 8 6 35
  //   6 6 35 6 4 39 4 4 39 4 2 3d 2 2 3d 2 0 41 0 0 41
endmodule

module comp_xor_5bit (
  input  [31:0] DATA_IN,
  input  RESET,
  input  CLK,
  output [6:0] COMP_STR,
  output CI_CLR,
  output [5:0] CI_NUM,
  output PUSH
);

  wire button_1_out, comparator_1_eq, d_ff_1_q, multiplexer_1_out, or_1_out, xor_1_out;
  wire [4:0] counter_1_q;

  Button button_1 (.out(button_1_out));
  Counter #(.max('h1f), .width(5)) counter_1 (
    .clr(RESET), .load(comparator_1_eq), .clk(button_1_out), .D(5'b00001), .Q(counter_1_q));  // open: up, count, carry
  Multiplexer #(.select(5)) multiplexer_1 (
    .in0(DATA_IN[31]), .in1(DATA_IN[30]), .in2(DATA_IN[29]), .in3(DATA_IN[28]), .in4(DATA_IN[27]),
    .in5(DATA_IN[26]), .in6(DATA_IN[25]), .in7(DATA_IN[24]), .in8(DATA_IN[23]), .in9(DATA_IN[22]),
    .in10(DATA_IN[21]), .in11(DATA_IN[20]), .in12(DATA_IN[19]), .in13(DATA_IN[18]), .in14(DATA_IN[17]),
    .in15(DATA_IN[16]), .in16(DATA_IN[15]), .in17(DATA_IN[14]), .in18(DATA_IN[13]), .in19(DATA_IN[12]),
    .in20(DATA_IN[11]), .in21(DATA_IN[10]), .in22(DATA_IN[9]), .in23(DATA_IN[8]), .in24(DATA_IN[7]),
    .in25(DATA_IN[6]), .in26(DATA_IN[5]), .in27(DATA_IN[4]), .in28(DATA_IN[3]), .in29(DATA_IN[2]),
    .in30(DATA_IN[1]), .in31(DATA_IN[0]), .out(multiplexer_1_out), .sel(counter_1_q));
  Comparator #(.width(5)) comparator_1 (.a(counter_1_q), .b({5{1'b1}}), .eq(comparator_1_eq));  // open: gt, lt
  D_Flip_Flop d_ff_1 (.D(multiplexer_1_out), .clk(button_1_out), .Q(d_ff_1_q), .reset(RESET));  // open: Qn, preset
  xor xor_1 (xor_1_out, multiplexer_1_out, d_ff_1_q);
  or or_1 (or_1_out, xor_1_out, comparator_1_eq);
  or or_2 (PUSH, xor_1_out, comparator_1_eq);
  // counter_pix counter_pix_1: pin names not known; wires that end beside it: COMP_STR, CI_CLR, CI_NUM
  // Probe on PUSH

  // Notes on the sheet:
  //   Сложная система сжатия. На вход подаются данные строки. 
  //   Полученные сжатые данные будут храниться в ОЗУ.
  //   Тест на 32 пройден
  //   Тест на нечёт пройден
  //   Счётчик строки
  //   Тут хранится строка
  //   Выборка бита
  //   Сравнение цвета и бита
  //   триггер решает проблему срабатываения PUSH на 0000110
  //   ((да он ваще монстр)
  //   IT'S ALIIIIIIIVE (нет) (да) (под подозрением)
  //   Из огня да в полымя.
  //   Возможно, сброс счёта PC эту проблему решит. А может и нет. 
  //   Я ПОНЯЛ ПОЧЕМУ! PUSH действует сначала в 0001000, а потом в 0010000 раз в 2 цикла. 
  //   XOR_OUT - важный выход. Он - индикатор окончания серии.
  //   То есть на что делится проблема: Если мы привязываем PUSH только к XOR, то ломается логика "32 одного цвета подряд". Если привязываем через OR с концом строки - ломается подача. Нужен принудительный сброс счётчика и отправка PUSH.
  //   Слово 7 бит
  //   В том случае, когда пиксели в строке все одинаковые:
  //   Нужен принудительный PUSH когда будет досчёт до 32
  //   Выход COMP_IN принимает значение 0001000 только один раз - в начале. А FIFO почему-то его по кд прокручивает.
  //   Теперь надо решить проблему с тем, что счётчик считает всё далее
  //   От принудительного Push появляются глюки с информацией в FIFO... Либо увеличивать слово COMP_STR до 8 бит, либо думы думать
  //   То есть нам в данном случае МЕШАЕТ подсчёт до конца строки. Однако сброс счётчика PC + принудительный PUSH гипотетически могут решить эту проблему.
endmodule

module dual_port_RAM_forum (
  input  WR_SIG,
  input  RD_SIG,
  input  CLK,
  input  [6:0] DATA_IN,
  input  R,
  output VALID_SIG,
  output [6:0] DATA_OUT
);

  wire comparator_1_eq;
  wire [6:0] read_q, write_q;

  Counter #(.max('h7f), .width(7)) write (.clr(R), .count(WR_SIG), .clk(CLK), .Q(write_q));  // open: load, up, D, carry
  Counter #(.max('h7f), .width(7)) read (.clr(R), .count(RD_SIG), .clk(CLK), .Q(read_q));  // open: load, up, D, carry
  Comparator #(.width(7)) comparator_1 (.a(write_q), .b(read_q), .eq(comparator_1_eq));  // open: gt, lt
  // DualRAM #(.addrWidth(7), .dataWidth(7)) dualram_1: pin names not known; wires that end beside it: write_q, WR_SIG, 1'b0, CLK, read_q, 1'b0, 1'b1, CLK, DATA_IN, DATA_OUT
  not not_1 (VALID_SIG, comparator_1_eq);
endmodule

module dual_port_RAM_my (
  input  WR_SIG,
  input  RD_SIG,
  input  CLK,
  input  [6:0] DATA_IN,
  input  R,
  output VALID_SIG,
  output [6:0] DATA_OUT
);

  wire comparator_1_eq, comparator_2_eq, xor_1_out;
  wire [6:0] read_q, write_q;
  wire [7:0] counter_1_q;

  Counter #(.max('h7f), .width(7)) write (.clr(R), .count(WR_SIG), .clk(CLK), .Q(write_q));  // open: load, up, D, carry
  Counter #(.max('h7f), .width(7)) read (.clr(R), .count(RD_SIG), .clk(CLK), .Q(read_q));  // open: load, up, D, carry
  xor xor_1 (xor_1_out, WR_SIG, RD_SIG);
  Counter #(.max('h78)) counter_1 (
    .up(xor_1_out), .count(WR_SIG), .clk(CLK), .Q(counter_1_q));  // open: clr, load, D, carry
  Comparator #(.mode("unsigned")) comparator_1 (.a(counter_1_q), .b(8'h78), .eq(comparator_1_eq));  // open: gt, lt
  Comparator #(.width(7)) comparator_2 (.a(write_q), .b(read_q), .eq(comparator_2_eq));  // open: gt, lt
  // DualRAM #(.addrWidth(7), .dataWidth(7)) dualram_1: pin names not known; wires that end beside it: write_q, WR_SIG, 1'b0, CLK, read_q, 1'b0, 1'b1, CLK, DATA_IN, DATA_OUT
  not not_1 (VALID_SIG, comparator_2_eq);
endmodule

module yet_another_fifo (
  input  WR_SIG,
  input  RD_SIG,
  input  CLK,
  input  [6:0] DATA_IN,
  input  R,
  input  FL,
  output VALID,
  output [6:0] DATA_OUT
);

  wire and_1_out, and_2_out, and_3_out, and_4_out, comparator_1_eq, E, F, init, s_r_ff_1_q, s_r_ff_1_qn;
  wire [6:0] read_q, write_q;

  and and_1 (and_1_out, WR_SIG, ~F);  // AND_Gate
  and and_2 (and_2_out, RD_SIG, ~E);  // AND_Gate
  Counter #(.max('h7f), .width(7)) write (
    .clr(FL), .count(and_1_out), .clk(CLK), .Q(write_q));  // open: load, up, D, carry
  Counter #(.max('h7f), .width(7)) read (
    .clr(FL), .count(and_2_out), .clk(CLK), .Q(read_q));  // open: load, up, D, carry
  and and_3 (and_3_out, ~init, WR_SIG);  // AND_Gate
  Register #(.width(1)) register_1 (.D(1'b1), .en(and_3_out), .clk(CLK), .Q(init), .clr(R));
  S_R_Flip_Flop s_r_ff_1 (
    .S(WR_SIG), .R(and_2_out), .clk(CLK), .Q(s_r_ff_1_q), .reset(R), .Qn(s_r_ff_1_qn));  // open: preset
  Comparator #(.width(7)) comparator_1 (.a(write_q), .b(read_q), .eq(comparator_1_eq));  // open: gt, lt
  // DualRAM #(.addrWidth(7), .clearpin("true"), .dataWidth(7)) dualram_1: pin names not known; wires that end beside it: write_q, WR_SIG, 1'b0, CLK, read_q, 1'b0, 1'b1, CLK, DATA_IN, FL, DATA_OUT
  or or_1 (E, ~init, and_4_out);  // OR_Gate
  and and_4 (and_4_out, comparator_1_eq, s_r_ff_1_q);
  and and_5 (F, s_r_ff_1_qn, comparator_1_eq, init);
  not not_1 (VALID, F);

  // Other names for the same wires on the sheet: DATA[6:0] = DATA_IN
endmodule

module tired (
  input  WR_SIG,
  input  RD_SIG,
  input  CLK,
  input  [6:0] DATA_IN,
  input  R,
  input  flush,
  output VALID,
  output [6:0] DATA_OUT
);

  wire and_1_out, and_2_out, and_3_out, and_5_out, comparator_1_eq, comparator_2_eq, dualram_1_p11,
       dualram_1_p13, E, F, init, s_r_ff_1_q, s_r_ff_1_qn, undriven, undriven_2, xor_1_out;
  wire [7:0] read_q, write_q;

  and and_1 (and_1_out, WR_SIG, ~F);  // AND_Gate
  and and_2 (and_2_out, RD_SIG, ~E);  // AND_Gate
  Counter write (.clr(undriven), .count(and_1_out), .clk(CLK), .Q(write_q));  // open: load, up, D, carry
  Counter read (.clr(undriven_2), .count(and_2_out), .clk(CLK), .Q(read_q));  // open: load, up, D, carry
  and and_3 (and_3_out, ~init, WR_SIG);  // AND_Gate
  Register #(.width(1)) register_1 (.D(1'b1), .en(and_3_out), .clk(CLK), .Q(init), .clr(R));
  S_R_Flip_Flop s_r_ff_1 (
    .S(WR_SIG), .R(and_2_out), .clk(CLK), .Q(s_r_ff_1_q), .reset(R), .Qn(s_r_ff_1_qn));  // open: preset
  Comparator #(.mode("unsigned")) comparator_1 (.a(write_q), .b(read_q), .eq(comparator_1_eq));  // open: gt, lt
  Comparator #(.mode("unsigned"), .width(7)) comparator_2 (
    .a(write_q[6:0]), .b(read_q[6:0]), .eq(comparator_2_eq));  // open: gt, lt
  xor xor_1 (xor_1_out, write_q[7], read_q[7]);
  and and_4 (F, comparator_2_eq, xor_1_out);
  not not_1 (VALID, comparator_1_eq);
  // DualRAM #(.addrWidth(7), .clearpin("true"), .dataWidth(7)) dualram_1: pin names not known; wires that end beside it: write_q[6:0], WR_SIG, 1'b0, CLK, read_q[6:0], 1'b0, 1'b1, CLK, DATA_IN, flush, dualram_1_p11, dualram_1_p11, dualram_1_p13, dualram_1_p13, DATA_OUT
  or or_1 (E, ~init, and_5_out);  // OR_Gate
  and and_5 (and_5_out, comparator_1_eq, s_r_ff_1_q);
  and and_6 (dualram_1_p11, s_r_ff_1_qn, comparator_1_eq, init);

  // Other names for the same wires on the sheet: DATA[6:0] = DATA_IN; fl = flush
endmodule

module TIIIREEEEED (
  input  WR_SIG,
  input  RD_SIG,
  input  CLK,
  input  [6:0] DATA_IN,
  input  R,
  input  flush,
  output VALID,
  output [6:0] DATA_OUT
);

  wire and_1_out, and_2_out, comparator_2_eq, dualram_1_p2, E, F, undriven, undriven_2, xor_1_out;
  wire [7:0] read_q, write_q;

  and and_1 (and_1_out, WR_SIG, ~F);  // AND_Gate
  and and_2 (and_2_out, RD_SIG, ~E);  // AND_Gate
  Counter write (.clr(undriven), .count(and_1_out), .clk(CLK), .Q(write_q));  // open: load, up, D, carry
  Counter read (.clr(undriven_2), .count(and_2_out), .clk(CLK), .Q(read_q));  // open: load, up, D, carry
  Comparator #(.mode("unsigned")) comparator_1 (.a(write_q), .b(read_q), .eq(E));  // open: gt, lt
  Comparator #(.mode("unsigned"), .width(7)) comparator_2 (
    .a(write_q[6:0]), .b(read_q[6:0]), .eq(comparator_2_eq));  // open: gt, lt
  xor xor_1 (xor_1_out, write_q[7], read_q[7]);
  and and_3 (F, comparator_2_eq, xor_1_out);
  not not_1 (VALID, E);
  // DualRAM #(.addrWidth(7), .clearpin("true"), .dataWidth(7)) dualram_1: pin names not known; wires that end beside it: write_q[6:0], dualram_1_p2, 1'b0, CLK, read_q[6:0], 1'b0, 1'b1, CLK, DATA_IN, R, DATA_OUT
  and and_4 (dualram_1_p2, and_1_out, ~F);  // AND_Gate

  // Other names for the same wires on the sheet: DATA[6:0] = DATA_IN; fl = flush
endmodule

module SOTIIIREEED (
  input  wr,
  input  rd,
  input  clk,
  input  [6:0] d_in,
  input  CLR,
  output V,
  output [6:0] data_out
);

  wire and_1_out, and_2_out, comparator_2_eq, E, F, xor_1_out;
  wire [7:0] r_q, w_q;

  and and_1 (and_1_out, wr, ~F);  // AND_Gate
  and and_2 (and_2_out, rd, ~E);  // AND_Gate
  Counter w (.clr(CLR), .count(and_1_out), .clk(clk), .Q(w_q));  // open: load, up, D, carry
  Counter r (.clr(CLR), .count(and_2_out), .clk(clk), .Q(r_q));  // open: load, up, D, carry
  not not_1 (V, E);
  Comparator comparator_1 (.a(w_q), .b(r_q), .eq(E));  // open: gt, lt
  Comparator #(.width(7)) comparator_2 (.a(w_q[6:0]), .b(r_q[6:0]), .eq(comparator_2_eq));  // open: gt, lt
  xor xor_1 (xor_1_out, w_q[7], r_q[7]);
  and and_3 (F, comparator_2_eq, xor_1_out);
  // DualRAM #(.addrWidth(7), .clearpin("true"), .dataWidth(7)) dualram_1: pin names not known; wires that end beside it: w_q[6:0], and_1_out, 1'b0, clk, r_q[6:0], 1'b0, 1'b1, clk, d_in, CLR, data_out
endmodule

module counter_11bit_sync (
  input  EN,
  input  CLK,
  input  RESET,
  output [10:0] S_OUT
);

  wire and_1_out, and_2_out, and_3_out, and_4_out, and_5_out, and_6_out, and_7_out, and_8_out, and_9_out,
       and_10_out, multiplexer_1_out, multiplexer_2_out, multiplexer_3_out, multiplexer_4_out,
       multiplexer_5_out, multiplexer_6_out, multiplexer_7_out, multiplexer_8_out, multiplexer_9_out,
       multiplexer_10_out, multiplexer_11_out, not_1_out;

  Multiplexer multiplexer_1 (.in0(EN), .in1(not_1_out), .out(multiplexer_1_out), .sel(RESET));
  not not_1 (not_1_out, S_OUT[0]);
  T_Flip_Flop t_ff_1 (.T(multiplexer_1_out), .clk(CLK), .Q(S_OUT[0]));  // open: Qn, reset, preset
  and and_1 (and_1_out, EN, S_OUT[0]);
  Multiplexer multiplexer_2 (.in0(and_1_out), .in1(S_OUT[1]), .out(multiplexer_2_out), .sel(RESET));
  T_Flip_Flop t_ff_2 (.T(multiplexer_2_out), .clk(CLK), .Q(S_OUT[1]));  // open: Qn, reset, preset
  and and_2 (and_2_out, and_1_out, S_OUT[1]);
  Multiplexer multiplexer_3 (.in0(and_2_out), .in1(S_OUT[2]), .out(multiplexer_3_out), .sel(RESET));
  T_Flip_Flop t_ff_3 (.T(multiplexer_3_out), .clk(CLK), .Q(S_OUT[2]));  // open: Qn, reset, preset
  and and_3 (and_3_out, and_2_out, S_OUT[2]);
  Multiplexer multiplexer_4 (.in0(and_3_out), .in1(S_OUT[3]), .out(multiplexer_4_out), .sel(RESET));
  T_Flip_Flop t_ff_4 (.T(multiplexer_4_out), .clk(CLK), .Q(S_OUT[3]));  // open: Qn, reset, preset
  and and_4 (and_4_out, and_3_out, S_OUT[3]);
  Multiplexer multiplexer_5 (.in0(and_4_out), .in1(S_OUT[4]), .out(multiplexer_5_out), .sel(RESET));
  T_Flip_Flop t_ff_5 (.T(multiplexer_5_out), .clk(CLK), .Q(S_OUT[4]));  // open: Qn, reset, preset
  and and_5 (and_5_out, and_4_out, S_OUT[4]);
  Multiplexer multiplexer_6 (.in0(and_5_out), .in1(S_OUT[5]), .out(multiplexer_6_out), .sel(RESET));
  T_Flip_Flop t_ff_6 (.T(multiplexer_6_out), .clk(CLK), .Q(S_OUT[5]));  // open: Qn, reset, preset
  and and_6 (and_6_out, and_5_out, S_OUT[5]);
  Multiplexer multiplexer_7 (.in0(and_6_out), .in1(S_OUT[6]), .out(multiplexer_7_out), .sel(RESET));
  T_Flip_Flop t_ff_7 (.T(multiplexer_7_out), .clk(CLK), .Q(S_OUT[6]));  // open: Qn, reset, preset
  and and_7 (and_7_out, and_6_out, S_OUT[6]);
  Multiplexer multiplexer_8 (.in0(and_7_out), .in1(S_OUT[7]), .out(multiplexer_8_out), .sel(RESET));
  T_Flip_Flop t_ff_8 (.T(multiplexer_8_out), .clk(CLK), .Q(S_OUT[7]));  // open: Qn, reset, preset
  and and_8 (and_8_out, and_7_out, S_OUT[7]);
  Multiplexer multiplexer_9 (.in0(and_8_out), .in1(S_OUT[8]), .out(multiplexer_9_out), .sel(RESET));
  T_Flip_Flop t_ff_9 (.T(multiplexer_9_out), .clk(CLK), .Q(S_OUT[8]));  // open: Qn, reset, preset
  and and_9 (and_9_out, and_8_out, S_OUT[8]);
  Multiplexer multiplexer_10 (.in0(and_9_out), .in1(S_OUT[9]), .out(multiplexer_10_out), .sel(RESET));
  T_Flip_Flop t_ff_10 (.T(multiplexer_10_out), .clk(CLK), .Q(S_OUT[9]));  // open: Qn, reset, preset
  and and_10 (and_10_out, and_9_out, S_OUT[9]);
  Multiplexer multiplexer_11 (.in0(and_10_out), .in1(S_OUT[10]), .out(multiplexer_11_out), .sel(RESET));
  T_Flip_Flop t_ff_11 (.T(multiplexer_11_out), .clk(CLK), .Q(S_OUT[10]));  // open: Qn, reset, preset

  // Notes on the sheet:
  //   Рельсотрон 9000
endmodule

module RES_SYS (
  input  [4:0] X,
  input  [4:0] Y,
  input  CL,
  input  CLK,
  output RES
);

  wire and_1_out, comparator_1_eq, comparator_2_eq, or_1_out;

  Comparator #(.width(5)) comparator_1 (.a(X), .b({5{1'b1}}), .eq(comparator_1_eq));  // open: gt, lt
  Comparator #(.width(5)) comparator_2 (.a(Y), .b({5{1'b1}}), .eq(comparator_2_eq));  // open: gt, lt
  and and_1 (and_1_out, comparator_1_eq, comparator_2_eq);
  D_Flip_Flop d_ff_1 (.D(or_1_out), .clk(CLK), .Q(RES));  // open: Qn, preset, reset
  or or_1 (or_1_out, and_1_out, CL);
endmodule

module STATION_1 (
  input  RC,
  input  RCC,
  input  RES,
  input  RESET,
  input  CLK,
  input  choice,
  output [4:0] X,
  output [4:0] Y,
  output [2:0] DATA_RGB_OUT,
  output LINE_OUT,
  output CL
);

  wire button_1_out, button_2_out, CLEAR, CLK_t, comp_xor_1_push, or_5_out, R, RC_t, RCC_t, sotiiireeed_1_v,
       use_transmitter_reg_v1_1_tx_signal;
  wire [1:0] control_1_control_out;
  wire [6:0] comp_xor_1_comp_str, sotiiireeed_1_data_out;
  wire [31:0] mem_gost_1_line_out, mem_test_1_line_out, multiplexer_1_out;

  Button button_1 (.out(button_1_out));
  Button button_2 (.out(button_2_out));
  or or_1 (R, RESET, button_1_out);
  or or_2 (CLK_t, CLK, button_2_out);
  or or_3 (CLEAR, R, RES);
  or or_4 (CL, RCC_t, RC_t);
  or or_5 (or_5_out, RES, R, CL);
  stability_unput_v4_v2 stability_unput_v4_v2_1 (
    .KEY_INPUT_1(RC), .CLK(CLK_t), .KEY_INPUT_2(RCC), .KEY_OUTPUT_1(RC_t), .KEY_OUTPUT_2(RCC_t));
  counter_10bit counter_10bit_1 (.EN(1'b1), .RESET(or_5_out), .CLK(CLK_t), .Q({Y, X}));
  control control_1 (.RC(RC_t), .RESET(R), .CLK(CLK_t), .RCC(RCC_t), .CONTROL_OUT(control_1_control_out));
  mem_gost mem_gost_1 (.CONTROL(control_1_control_out), .COUNTER(Y), .LINE_OUT(mem_gost_1_line_out));
  Multiplexer #(.width(32)) multiplexer_1 (
    .in0(mem_gost_1_line_out), .in1(mem_test_1_line_out), .out(multiplexer_1_out), .sel(choice));
  mem_test mem_test_1 (.CONTROL(control_1_control_out), .COUNTER(Y), .LINE_OUT(mem_test_1_line_out));
  pixel_selector pixel_selector_1 (
    .ROM_input(multiplexer_1_out), .COUNTER_input(X), .COLOR_0(3'b000), .COLOR_1(3'b111),
    .DATA_output(DATA_RGB_OUT));
  comp_xor comp_xor_1 (
    .DATA_IN(multiplexer_1_out), .RESET(CLEAR), .CLK(CLK_t), .COMP_STR(comp_xor_1_comp_str),
    .PUSH(comp_xor_1_push));
  SOTIIIREEED sotiiireeed_1 (
    .wr(comp_xor_1_push), .rd(use_transmitter_reg_v1_1_tx_signal), .clk(CLK_t), .d_in(comp_xor_1_comp_str),
    .CLR(CLEAR), .V(sotiiireeed_1_v), .data_out(sotiiireeed_1_data_out));
  use_transmitter_reg_v1 use_transmitter_reg_v1_1 (
    .CLK(CLK_t), .RESET(CLEAR), .VALID_SIG(sotiiireeed_1_v), .DATA_IN(sotiiireeed_1_data_out),
    .TX_SIGNAL(use_transmitter_reg_v1_1_tx_signal), .TX_OUT(LINE_OUT));
endmodule

module STATION_2 (
  input  LINE_IN,
  input  RESET,
  input  CLK,
  input  CL,
  output [4:0] X,
  output [4:0] Y,
  output WE,
  output [2:0] DATA_RGB_OUT,
  output RES
);

  wire button_1_out, button_2_out, CLEAR, CLK_t, R, rx_worksaaaaaaaaa_1_sign_out;
  wire [4:0] decomp_naaaahb_1_x0;
  wire [6:0] rx_worksaaaaaaaaa_1_data_out;

  Button button_1 (.out(button_1_out));
  Button button_2 (.out(button_2_out));
  or or_1 (R, RESET, button_1_out);
  or or_2 (CLK_t, CLK, button_2_out);
  or or_3 (CLEAR, R, RES);
  rx_WORKSAAAAAAAAA rx_worksaaaaaaaaa_1 (
    .RESET(CLEAR), .CLK(CLK_t), .RX_IN(LINE_IN), .SIGN_OUT(rx_worksaaaaaaaaa_1_sign_out),
    .DATA_OUT(rx_worksaaaaaaaaa_1_data_out));
  decomp_naaaahb decomp_naaaahb_1 (
    .RESET(R), .SIGN(rx_worksaaaaaaaaa_1_sign_out), .DATA_IN(rx_worksaaaaaaaaa_1_data_out), .CLK(CLK_t),
    .stahp(RES), .DATA_RGB_OUT(DATA_RGB_OUT), .WE_RGB(WE), .X0(decomp_naaaahb_1_x0), .Y0(Y));
  assign X = ~decomp_naaaahb_1_x0;  // NOT_Gate not_1, 5 bits wide
  RES_SYS res_sys_1 (.X(decomp_naaaahb_1_x0), .Y(Y), .CL(CL), .CLK(CLK_t), .RES(RES));
endmodule

module MAIN_SCHEME (
  input  secre,
  input  RESET
);

  wire button_1_out, button_2_out, button_3_out, button_4_out, CLK, CLK_out, R, RES, station_1_1_cl,
       station_1_1_line_out, station_2_1_we;
  wire [2:0] rgb_video_1_p6, station_2_1_data_rgb_out;
  wire [4:0] rgb_video_1_p4, rgb_video_1_p5, station_2_1_x, station_2_1_y;

  Button button_1 (.out(button_1_out));
  Clock u_CLK (.out(CLK_out));
  Button button_2 (.out(button_2_out));
  Button button_3 (.out(button_3_out));
  Button button_4 (.out(button_4_out));
  or or_1 (R, RESET, button_1_out);
  or or_2 (CLK, CLK_out, button_2_out);
  // RGB_Video #(.height(32), .scale(8), .width(32)) rgb_video_1: pin names not known; wires that end beside it: R, CLK, 1'b1, rgb_video_1_p4, rgb_video_1_p5, rgb_video_1_p6
  STATION_1 station_1_1 (
    .RC(button_3_out), .RCC(button_4_out), .RES(RES), .RESET(R), .CLK(CLK), .choice(secre),
    .X(rgb_video_1_p4), .Y(rgb_video_1_p5), .DATA_RGB_OUT(rgb_video_1_p6), .LINE_OUT(station_1_1_line_out),
    .CL(station_1_1_cl));
  STATION_2 station_2_1 (
    .LINE_IN(station_1_1_line_out), .RESET(R), .CLK(CLK), .CL(station_1_1_cl), .X(station_2_1_x),
    .Y(station_2_1_y), .WE(station_2_1_we), .DATA_RGB_OUT(station_2_1_data_rgb_out), .RES(RES));
  // RGB_Video #(.height(32), .scale(8), .width(32)) rgb_video_2: pin names not known; wires that end beside it: R, CLK, station_2_1_we, station_2_1_x, station_2_1_y, station_2_1_data_rgb_out
endmodule

module FULLFILL_STATION (
  input  RESET,
  input  choice,
  output CI_COLOR,
  output [5:0] CI_BIT_COUNT,
  output [6:0] out_5,
  output [6:0] CI_2
);

  wire and_1_out, and_2_out, and_3_out, and_4_out, and_5_out, and_6_out, and_7_out, and_8_out, and_9_out,
       and_10_out, and_11_out, and_12_out, and_13_out, and_14_out, and_17_out, and_18_out, and_19_out,
       and_20_out, and_22_out, and_23_out, and_24_out, and_25_out, and_26_out, and_27_out, and_28_out,
       and_29_out, and_30_out, and_31_out, and_32_out, and_33_out, and_34_out, and_35_out, and_36_out,
       and_39_out, and_40_out, button_1_out, button_2_out, C_REG_q, cl, CLEAR, CLK, clock_1_out,
       comparator_2_eq, comparator_3_eq, comparator_5_eq, comparator_7_eq, comparator_8_eq, d_ff_1_qn,
       d_ff_2_qn, d_ff_4_q, d_ff_4_qn, d_ff_5_q, d_ff_6_q, DRAW, E, E2, F, F2, LOAD, multiplexer_1_out,
       multiplexer_6_out, multiplexer_8_out, multiplexer_9_out, multiplexer_10_out, multiplexer_11_out,
       nand_1_out, nand_2_out, nand_3_out, nand_4_out, nand_5_out, nand_6_out, nand_7_out, nor_1_out,
       not_1_out, not_2_out, not_3_out, not_4_out, not_5_out, not_6_out, or_5_out, or_6_out, or_7_out,
       or_8_out, or_9_out, or_10_out, or_11_out, or_12_out, or_14_out, POP, R, RC, RC_out, RCC, RCC_out, RES,
       shift_register_1_p8, t_ff_15_q, t_ff_16_q, t_ff_17_q, VALID, VALID2, xor_2_out, xor_3_out, xor_4_out,
       ZERO;
  wire [0:0] dualram_2_p11;
  wire [1:0] and_37_out, nand_8_out, register_1_q, register_4_q;
  wire [3:0] t_ff_18_q;
  wire [4:0] X, Y;
  wire [5:0] adder_1_out, counter_2_q, dualram_2_p11_2, LENGTH_COUNTER_q, multiplexer_7_out;
  wire [6:0] dualram_1_p11, register_3_q, undriven;
  wire [7:0] counter_3_q, counter_4_q, r_q, w_q;
  wire [9:0] counter_1_q;
  wire [23:0] DATA, multiplexer_12_out;
  wire [31:0] multiplexer_2_out, multiplexer_4_out, multiplexer_5_out, rom_1_data, rom_2_data, rom_3_data,
       rom_4_data, rom_5_data, rom_6_data, rom_7_data, rom_8_data;

  Button u_RC (.out(RC_out));
  Button u_RCC (.out(RCC_out));
  Button button_1 (.out(button_1_out));
  Clock clock_1 (.out(clock_1_out));
  Button button_2 (.out(button_2_out));
  or or_1 (R, RESET, button_1_out);
  or or_2 (CLK, clock_1_out, button_2_out);
  or or_3 (CLEAR, R, RES);
  or or_4 (cl, RCC, RC);
  nand nand_1 (nand_1_out, out_5[0], out_5[1], out_5[2], out_5[3], out_5[4], out_5[5], out_5[6]);
  not not_1 (not_1_out, RC_out);
  nand nand_2 (nand_2_out, CI_2[0], CI_2[1], CI_2[2], CI_2[3], CI_2[4], CI_2[5], CI_2[6]);
  not not_2 (not_2_out, RCC_out);
  T_Flip_Flop t_ff_1 (.T(and_1_out), .clk(CLK), .Q(out_5[0]), .reset(not_1_out));  // open: Qn, preset
  and and_1 (and_1_out, nand_1_out, RC_out);
  T_Flip_Flop t_ff_2 (.T(and_2_out), .clk(CLK), .Q(CI_2[0]), .reset(not_2_out));  // open: Qn, preset
  and and_2 (and_2_out, nand_2_out, RCC_out);
  and and_3 (and_3_out, and_1_out, out_5[0]);
  T_Flip_Flop t_ff_3 (.T(and_3_out), .clk(CLK), .Q(out_5[1]), .reset(not_1_out));  // open: Qn, preset
  and and_4 (and_4_out, and_2_out, CI_2[0]);
  T_Flip_Flop t_ff_4 (.T(and_4_out), .clk(CLK), .Q(CI_2[1]), .reset(not_2_out));  // open: Qn, preset
  and and_5 (and_5_out, and_3_out, out_5[1]);
  and and_6 (and_6_out, and_4_out, CI_2[1]);
  T_Flip_Flop t_ff_5 (.T(and_5_out), .clk(CLK), .Q(out_5[2]), .reset(not_1_out));  // open: Qn, preset
  T_Flip_Flop t_ff_6 (.T(and_6_out), .clk(CLK), .Q(CI_2[2]), .reset(not_2_out));  // open: Qn, preset
  and and_7 (and_7_out, and_5_out, out_5[2]);
  T_Flip_Flop t_ff_7 (.T(and_7_out), .clk(CLK), .Q(out_5[3]), .reset(not_1_out));  // open: Qn, preset
  and and_8 (and_8_out, and_6_out, CI_2[2]);
  T_Flip_Flop t_ff_8 (.T(and_8_out), .clk(CLK), .Q(CI_2[3]), .reset(not_2_out));  // open: Qn, preset
  and and_9 (and_9_out, and_7_out, out_5[3]);
  T_Flip_Flop t_ff_9 (.T(and_9_out), .clk(CLK), .Q(out_5[4]), .reset(not_1_out));  // open: Qn, preset
  and and_10 (and_10_out, and_8_out, CI_2[3]);
  T_Flip_Flop t_ff_10 (.T(and_10_out), .clk(CLK), .Q(CI_2[4]), .reset(not_2_out));  // open: Qn, preset
  and and_11 (and_11_out, and_9_out, out_5[4]);
  and and_12 (and_12_out, and_10_out, CI_2[4]);
  T_Flip_Flop t_ff_11 (.T(and_11_out), .clk(CLK), .Q(out_5[5]), .reset(not_1_out));  // open: Qn, preset
  T_Flip_Flop t_ff_12 (.T(and_12_out), .clk(CLK), .Q(CI_2[5]), .reset(not_2_out));  // open: Qn, preset
  and and_13 (and_13_out, and_11_out, out_5[5]);
  T_Flip_Flop t_ff_13 (.T(and_13_out), .clk(CLK), .Q(out_5[6]), .reset(not_1_out));  // open: Qn, preset
  and and_14 (and_14_out, and_12_out, CI_2[5]);
  T_Flip_Flop t_ff_14 (.T(and_14_out), .clk(CLK), .Q(CI_2[6]), .reset(not_2_out));  // open: Qn, preset
  Counter #(.max('h3ff), .width(10)) counter_1 (
    .clr(or_5_out), .clk(CLK), .Q(counter_1_q));  // open: load, up, count, D, carry
  or or_5 (or_5_out, RES, R, cl);
  and and_15 (RC, RC_out, out_5[6], out_5[5], out_5[4], out_5[3], out_5[2], out_5[1], out_5[0]);
  and and_16 (RCC, RCC_out, CI_2[6], CI_2[5], CI_2[4], CI_2[3], CI_2[2], CI_2[1], CI_2[0]);
  D_Flip_Flop d_ff_1 (.D(RC), .clk(CLK), .Qn(d_ff_1_qn), .reset(R));  // open: Q, preset
  ROM #(.addrWidth(5), .dataWidth(32)) rom_1 (.addr(counter_1_q[9:5]), .data(rom_1_data));
  ROM #(.addrWidth(5), .dataWidth(32)) rom_2 (.addr(counter_1_q[9:5]), .data(rom_2_data));
  and and_17 (and_17_out, RC, d_ff_1_qn);
  not not_3 (not_3_out, register_1_q[0]);
  not not_4 (not_4_out, register_1_q[1]);
  not not_5 (not_5_out, and_17_out);
  not not_6 (not_6_out, and_18_out);
  ROM #(.addrWidth(5), .dataWidth(32)) rom_3 (.addr(counter_1_q[9:5]), .data(rom_3_data));
  ROM #(.addrWidth(5), .dataWidth(32)) rom_4 (.addr(counter_1_q[9:5]), .data(rom_4_data));
  // RGB_Video #(.height(32), .scale(8), .width(32)) rgb_video_1: pin names not known; wires that end beside it: R, CLK, 1'b1, counter_1_q[4:0], counter_1_q[9:5], DATA, DATA
  D_Flip_Flop d_ff_2 (.D(RCC), .clk(CLK), .Qn(d_ff_2_qn), .reset(R));  // open: Q, preset
  nand nand_3 (nand_3_out, not_3_out, not_4_out, not_5_out, and_18_out);
  nand nand_4 (nand_4_out, not_3_out, register_1_q[1], and_17_out, not_6_out);
  nand nand_5 (nand_5_out, register_1_q[0], not_4_out, and_17_out);
  nand nand_6 (nand_6_out, register_1_q[0], not_5_out, not_6_out);
  nand nand_7 (nand_7_out, register_1_q[0], register_1_q[1], and_18_out);
  xor xor_1 (nand_8_out[1], register_1_q[1], and_17_out, and_18_out);
  and and_18 (and_18_out, RCC, d_ff_2_qn);
  nand nand_8 (nand_8_out[0], nand_3_out, nand_4_out, nand_5_out, nand_6_out, nand_7_out);
  ROM #(.addrWidth(5), .dataWidth(32)) rom_5 (.addr(counter_1_q[9:5]), .data(rom_5_data));
  ROM #(.addrWidth(5), .dataWidth(32)) rom_6 (.addr(counter_1_q[9:5]), .data(rom_6_data));
  Register #(.width(2)) register_1 (.D(nand_8_out), .clk(CLK), .Q(register_1_q), .clr(R));  // open: en
  ROM #(.addrWidth(5), .dataWidth(32)) rom_7 (.addr(counter_1_q[9:5]), .data(rom_7_data));
  ROM #(.addrWidth(5), .dataWidth(32)) rom_8 (.addr(counter_1_q[9:5]), .data(rom_8_data));
  Multiplexer #(.select(5)) multiplexer_1 (
    .in0(multiplexer_5_out[0]), .in1(multiplexer_5_out[1]), .in2(multiplexer_5_out[2]),
    .in3(multiplexer_5_out[3]), .in4(multiplexer_5_out[4]), .in5(multiplexer_5_out[5]),
    .in6(multiplexer_5_out[6]), .in7(multiplexer_5_out[7]), .in8(multiplexer_5_out[8]),
    .in9(multiplexer_5_out[9]), .in10(multiplexer_5_out[10]), .in11(multiplexer_5_out[11]),
    .in12(multiplexer_5_out[12]), .in13(multiplexer_5_out[13]), .in14(multiplexer_5_out[14]),
    .in15(multiplexer_5_out[15]), .in16(multiplexer_5_out[16]), .in17(multiplexer_5_out[17]),
    .in18(multiplexer_5_out[18]), .in19(multiplexer_5_out[19]), .in20(multiplexer_5_out[20]),
    .in21(multiplexer_5_out[21]), .in22(multiplexer_5_out[22]), .in23(multiplexer_5_out[23]),
    .in24(multiplexer_5_out[24]), .in25(multiplexer_5_out[25]), .in26(multiplexer_5_out[26]),
    .in27(multiplexer_5_out[27]), .in28(multiplexer_5_out[28]), .in29(multiplexer_5_out[29]),
    .in30(multiplexer_5_out[30]), .in31(multiplexer_5_out[31]), .out(multiplexer_1_out),
    .sel(counter_1_q[4:0]));
  Multiplexer #(.select(2), .width(32)) multiplexer_2 (
    .in0(rom_1_data), .in1(rom_3_data), .in2(rom_5_data), .in3(rom_7_data), .out(multiplexer_2_out),
    .sel({register_1_q[0], register_1_q[1]}));
  Multiplexer #(.width(24)) multiplexer_3 (.in0({24{1'b0}}), .in1({24{1'b1}}), .out(DATA), .sel(multiplexer_1_out));
  Multiplexer #(.select(2), .width(32)) multiplexer_4 (
    .in0(rom_2_data), .in1(rom_4_data), .in2(rom_6_data), .in3(rom_8_data), .out(multiplexer_4_out),
    .sel({register_1_q[0], register_1_q[1]}));
  Multiplexer #(.width(32)) multiplexer_5 (
    .in0(multiplexer_2_out), .in1(multiplexer_4_out), .out(multiplexer_5_out), .sel(choice));
  Counter #(.max('h20), .width(6)) counter_2 (
    .clr(CLEAR), .load(nor_1_out), .clk(CLK), .D(6'b000001), .Q(counter_2_q));  // open: up, count, carry
  Multiplexer #(.select(5)) multiplexer_6 (
    .in0(multiplexer_5_out[31]), .in1(multiplexer_5_out[30]), .in2(multiplexer_5_out[29]),
    .in3(multiplexer_5_out[28]), .in4(multiplexer_5_out[27]), .in5(multiplexer_5_out[26]),
    .in6(multiplexer_5_out[25]), .in7(multiplexer_5_out[24]), .in8(multiplexer_5_out[23]),
    .in9(multiplexer_5_out[22]), .in10(multiplexer_5_out[21]), .in11(multiplexer_5_out[20]),
    .in12(multiplexer_5_out[19]), .in13(multiplexer_5_out[18]), .in14(multiplexer_5_out[17]),
    .in15(multiplexer_5_out[16]), .in16(multiplexer_5_out[15]), .in17(multiplexer_5_out[14]),
    .in18(multiplexer_5_out[13]), .in19(multiplexer_5_out[12]), .in20(multiplexer_5_out[11]),
    .in21(multiplexer_5_out[10]), .in22(multiplexer_5_out[9]), .in23(multiplexer_5_out[8]),
    .in24(multiplexer_5_out[7]), .in25(multiplexer_5_out[6]), .in26(multiplexer_5_out[5]),
    .in27(multiplexer_5_out[4]), .in28(multiplexer_5_out[3]), .in29(multiplexer_5_out[2]),
    .in30(multiplexer_5_out[1]), .in31(multiplexer_5_out[0]), .out(multiplexer_6_out), .sel(counter_2_q[4:0]));
  // Probe on counter_2_q
  D_Flip_Flop d_ff_3 (.D(multiplexer_6_out), .clk(CLK), .Q(CI_COLOR), .reset(CLEAR));  // open: Qn, preset
  xor xor_2 (xor_2_out, multiplexer_6_out, CI_COLOR);
  nor nor_1 (nor_1_out, counter_2_q[0], counter_2_q[1], counter_2_q[2], counter_2_q[3], counter_2_q[4], ~counter_2_q[5]);  // NOR_Gate
  or or_6 (or_6_out, xor_2_out, nor_1_out);
  or or_7 (or_7_out, xor_2_out, nor_1_out);
  Multiplexer #(.width(6)) multiplexer_7 (.in0(adder_1_out), .in1(6'b000001), .out(multiplexer_7_out), .sel(or_6_out));
  Register #(.width(6)) register_2 (.D(multiplexer_7_out), .en(1'b1), .clk(CLK), .Q(CI_BIT_COUNT), .clr(CLEAR));
  Adder #(.width(6)) adder_1 (.a(CI_BIT_COUNT), .b(6'b000001), .out(adder_1_out));  // open: cin, cout
  and and_19 (and_19_out, or_7_out, ~F);  // AND_Gate
  and and_20 (and_20_out, and_28_out, ~E);  // AND_Gate
  Counter w (.clr(CLEAR), .count(and_19_out), .clk(CLK), .Q(w_q));  // open: load, up, D, carry
  Counter u_r (.clr(CLEAR), .count(and_20_out), .clk(CLK), .Q(r_q));  // open: load, up, D, carry
  Comparator comparator_1 (.a(w_q), .b(r_q), .eq(E));  // open: gt, lt
  Comparator #(.width(7)) comparator_2 (.a(w_q[6:0]), .b(r_q[6:0]), .eq(comparator_2_eq));  // open: gt, lt
  xor xor_3 (xor_3_out, w_q[7], r_q[7]);
  not not_7 (VALID, E);
  and and_21 (F, comparator_2_eq, xor_3_out);
  // DualRAM #(.addrWidth(7), .clearpin("true"), .dataWidth(7)) dualram_1: pin names not known; wires that end beside it: w_q[6:0], and_19_out, 1'b0, CLK, r_q[6:0], 1'b0, 1'b1, CLK, {CI_BIT_COUNT, CI_COLOR}, CLEAR, dualram_1_p11
  T_Flip_Flop t_ff_15 (.T(d_ff_4_q), .clk(CLK), .Q(t_ff_15_q), .reset(d_ff_4_qn));  // open: Qn, preset
  and and_22 (and_22_out, d_ff_4_q, t_ff_15_q);
  T_Flip_Flop t_ff_16 (.T(and_22_out), .clk(CLK), .Q(t_ff_16_q), .reset(d_ff_4_qn));  // open: Qn, preset
  and and_23 (and_23_out, and_22_out, t_ff_16_q);
  T_Flip_Flop t_ff_17 (.T(and_23_out), .clk(CLK), .Q(t_ff_17_q), .reset(d_ff_4_qn));  // open: Qn, preset
  and and_24 (and_24_out, d_ff_4_qn, VALID);
  and and_25 (and_25_out, d_ff_4_q, ~and_26_out);  // AND_Gate
  or or_8 (or_8_out, and_24_out, and_25_out);
  D_Flip_Flop d_ff_4 (.D(or_8_out), .clk(CLK), .Q(d_ff_4_q), .Qn(d_ff_4_qn), .reset(CLEAR));  // open: preset
  and and_26 (and_26_out, t_ff_15_q, t_ff_16_q, t_ff_17_q);
  and and_27 (and_27_out, d_ff_4_qn, VALID);
  // Shift_Register #(.length(9)) shift_register_1: pin names not known; wires that end beside it: CLEAR, and_27_out, d_ff_4_q, CLK, 1'b1, 1'b1, 1'b0, shift_register_1_p8
  and and_28 (and_28_out, VALID, d_ff_4_qn);
  or or_9 (or_9_out, shift_register_1_p8, d_ff_4_qn);
  or or_10 (or_10_out, comparator_3_eq, CLEAR);
  Multiplexer multiplexer_8 (.in0(d_ff_5_q), .in1(t_ff_18_q[0]), .out(multiplexer_8_out), .sel(or_10_out));
  T_Flip_Flop t_ff_18 (.T(multiplexer_8_out), .clk(CLK), .Q(t_ff_18_q[0]));  // open: Qn, reset, preset
  and and_29 (and_29_out, d_ff_5_q, t_ff_18_q[0]);
  Multiplexer multiplexer_9 (.in0(and_29_out), .in1(t_ff_18_q[1]), .out(multiplexer_9_out), .sel(or_10_out));
  T_Flip_Flop t_ff_19 (.T(multiplexer_9_out), .clk(CLK), .Q(t_ff_18_q[1]));  // open: Qn, reset, preset
  and and_30 (and_30_out, and_29_out, t_ff_18_q[1]);
  Multiplexer multiplexer_10 (.in0(and_30_out), .in1(t_ff_18_q[2]), .out(multiplexer_10_out), .sel(or_10_out));
  T_Flip_Flop t_ff_20 (.T(multiplexer_10_out), .clk(CLK), .Q(t_ff_18_q[2]));  // open: Qn, reset, preset
  and and_31 (and_31_out, and_30_out, t_ff_18_q[2]);
  Multiplexer multiplexer_11 (.in0(and_31_out), .in1(t_ff_18_q[3]), .out(multiplexer_11_out), .sel(or_10_out));
  T_Flip_Flop t_ff_21 (.T(multiplexer_11_out), .clk(CLK), .Q(t_ff_18_q[3]));  // open: Qn, reset, preset
  Comparator #(.width(4)) comparator_3 (.a(t_ff_18_q), .b(4'b1000), .eq(comparator_3_eq));  // open: gt, lt
  and and_32 (and_32_out, ~comparator_3_eq, d_ff_5_q);  // AND_Gate
  or or_11 (or_11_out, ~or_9_out, and_32_out);  // OR_Gate
  and and_33 (and_33_out, ~comparator_3_eq, d_ff_5_q);  // AND_Gate
  D_Flip_Flop d_ff_5 (.D(or_11_out), .clk(CLK), .Q(d_ff_5_q), .reset(CLEAR));  // open: Qn, preset
  // Shift_Register #(.length(9)) shift_register_2: pin names not known; wires that end beside it: CLEAR, 1'b0, and_33_out, CLK, or_9_out, CLEAR
  Register #(.width(7)) register_3 (.D(undriven), .en(comparator_3_eq), .clk(CLK), .Q(register_3_q), .clr(CLEAR));
  D_Flip_Flop d_ff_6 (.D(comparator_3_eq), .clk(CLK), .Q(d_ff_6_q), .reset(CLEAR));  // open: Qn, preset
  and and_34 (and_34_out, d_ff_6_q, ~F2);  // AND_Gate
  and and_35 (and_35_out, POP, ~E2);  // AND_Gate
  Counter counter_3 (.clr(CLEAR), .count(and_34_out), .clk(CLK), .Q(counter_3_q));  // open: load, up, D, carry
  Counter counter_4 (.clr(CLEAR), .count(and_35_out), .clk(CLK), .Q(counter_4_q));  // open: load, up, D, carry
  and and_36 (and_36_out, register_4_q[1], ~ZERO);  // AND_Gate
  or or_12 (or_12_out, register_4_q[0], VALID2);
  or or_13 (and_37_out[1], register_4_q[0], and_36_out);
  and and_37 (and_37_out[0], ~register_4_q[1], or_12_out);  // AND_Gate
  Register #(.width(2)) register_4 (.D(and_37_out), .clk(CLK), .Q(register_4_q), .clr(CLEAR));  // open: en
  Comparator comparator_4 (.a(counter_3_q), .b(counter_4_q), .eq(E2));  // open: gt, lt
  Comparator #(.width(7)) comparator_5 (
    .a(counter_3_q[6:0]), .b(counter_4_q[6:0]), .eq(comparator_5_eq));  // open: gt, lt
  xor xor_4 (xor_4_out, counter_3_q[7], counter_4_q[7]);
  not not_8 (VALID2, E2);
  and and_38 (F2, comparator_5_eq, xor_4_out);
  and P (POP, ~register_4_q[1], register_4_q[0]);  // AND_Gate
  and L (LOAD, register_4_q[0], register_4_q[1]);
  and and_39 (and_39_out, register_4_q[1], ~register_4_q[0]);  // AND_Gate
  and C (DRAW, and_39_out, ~ZERO);  // AND_Gate
  // DualRAM #(.addrWidth(7), .clearpin("true"), .dataWidth(7)) dualram_2: pin names not known; wires that end beside it: counter_3_q[6:0], and_34_out, 1'b0, CLK, counter_4_q[6:0], 1'b0, 1'b1, CLK, register_3_q, CLEAR, {dualram_2_p11_2, dualram_2_p11[0]}
  Register #(.width(1)) C_REG (.D(dualram_2_p11[0]), .en(LOAD), .clk(CLK), .Q(C_REG_q), .clr(R));
  Counter #(.max('h3ff), .width(10)) XY_CNT (
    .clr(CLEAR), .count(DRAW), .clk(CLK), .Q({Y, X}));  // open: load, up, D, carry
  Counter #(.max('h3f), .width(6)) LENGTH_COUNTER (
    .clr(R), .load(LOAD), .up(1'b0), .count(DRAW), .clk(CLK), .D(dualram_2_p11_2), .Q(LENGTH_COUNTER_q));  // open: carry
  Multiplexer #(.width(24)) multiplexer_12 (
    .in0({24{1'b0}}), .in1({24{1'b1}}), .out(multiplexer_12_out), .sel(C_REG_q));
  Comparator #(.width(6)) comparator_6 (.a(LENGTH_COUNTER_q), .b({6{1'b0}}), .eq(ZERO));  // open: gt, lt
  // RGB_Video #(.height(32), .scale(8), .width(32)) rgb_video_2: pin names not known; wires that end beside it: R, CLK, DRAW, Y, multiplexer_12_out
  // NOT_Gate not_9 has open pins: in=X, out=open
  Comparator #(.width(5)) comparator_7 (.a(X), .b({5{1'b1}}), .eq(comparator_7_eq));  // open: gt, lt
  Comparator #(.width(5)) comparator_8 (.a(Y), .b({5{1'b1}}), .eq(comparator_8_eq));  // open: gt, lt
  and and_40 (and_40_out, comparator_7_eq, comparator_8_eq);
  or or_14 (or_14_out, and_40_out, cl);
  D_Flip_Flop d_ff_7 (.D(or_14_out), .clk(CLK), .Q(RES));  // open: Qn, preset, reset

  // Notes on the sheet:
  //   contents of rom_1 (hex, n*v repeats v):
  //   18000 18000 3c000 3c000 7e000 7e000 ff000 ff000 1ff800 1ff800 3ffc00 3ffc00 7ffe00 7ffe00 ffff00
  //   ffff00 1ffff80 1ffff80 3ffffc0 3ffffc0 7ffffe0 7ffffe0 ffffff0 ffffff0 1ffffff8 1ffffff8 3ffffffc
  //   3ffffffc 7ffffffe 7ffffffe ffffffff ffffffff
  //   contents of rom_2 (hex, n*v repeats v):
  //   200000 700000 200000 0 200400 200400 300c00 300c00 481200 442200 442200 424200 818100 81ff00 818100
  //   824100 1024080 1042080 1081080 1081080 2100840 2200440 2200440 2400240 4800120 4800120 50000a0
  //   6000060 a000050 c000030 8000010 8000010
  //   contents of rom_3 (hex, n*v repeats v):
  //   3 f 3f ff 3ff fff 3fff ffff 3ffff fffff 3fffff ffffff 3ffffff fffffff 3fffffff ffffffff ffffffff
  //   3fffffff fffffff 3ffffff ffffff 3fffff fffff 3ffff ffff 3fff fff 3ff ff 3f f 3
  //   contents of rom_4 (hex, n*v repeats v):
  //   0 0 15dddc0 1484480 1c9dc80 1484480 149dc80 0 0 0 18000 3c000 3c000 18000 0 0 0 181800 3c3c00 3c3c00
  //   181800 4*0 1bb8ee0 2a882a0 2aa8ea0 2aa82a0 1bb82e0
  //   contents of rom_5 (hex, n*v repeats v):
  //   ffffffff ffffffff 7ffffffe 7ffffffe 3ffffffc 3ffffffc 1ffffff8 1ffffff8 ffffff0 ffffff0 7ffffe0
  //   7ffffe0 3ffffc0 3ffffc0 1ffff80 1ffff80 ffff00 ffff00 7ffe00 7ffe00 3ffc00 3ffc00 1ff800 1ff800
  //   ff000 ff000 7e000 7e000 3c000 3c000 18000 18000
  //   contents of rom_6 (hex, n*v repeats v):
  //   0 0 15dddc0 1484480 1c9dc80 1484480 149dc80 0 0 0 18000 3c000 3c000 18000 0 0 0 181800 3c3c00 3c3c00
  //   181800 4*0 1bb8ee0 2a882a0 2aa8ea0 2aa82a0 1bb82e0
  //   contents of rom_7 (hex, n*v repeats v):
  //   c0000000 f0000000 fc000000 ff000000 ffc00000 fff00000 fffc0000 ffff0000 ffffc000 fffff000 fffffc00
  //   ffffff00 ffffffc0 fffffff0 fffffffc ffffffff ffffffff fffffffc fffffff0 ffffffc0 ffffff00 fffffc00
  //   fffff000 ffffc000 ffff0000 fffc0000 fff00000 ffc00000 ff000000 fc000000 f0000000 c0000000
  //   contents of rom_8 (hex, n*v repeats v):
  //   ff7fffff f7e5ce5f f35cf5cf f55d76d7 f5654dd7 ffffffff ffffffff fffe7fff fffc3fff fffc3fff fffe7fff
  //   6*ffffffff f8efdbbf 7e18d863 199b3337 b03198e3 1eee3e0c 3870ed9c e38783bf 1e1e1e3c f71f3f0 601f9e07
  //   3f7003fc cc0ffc00 ffc03ff 7f819f00 1ff81ff
  //   Счётчик строки
  //   Выборка бита
  //   Сравнение цвета и бита
endmodule

module mem_gost (
  input  [1:0] CONTROL,
  input  [4:0] COUNTER,
  output [31:0] LINE_OUT
);

  wire [31:0] mem1_1_q, mem2_1_q, mem3_1_q, mem4_1_q;

  mem1 mem1_1 (.A(COUNTER), .Q(mem1_1_q));
  mem2 mem2_1 (.A(COUNTER), .Q(mem2_1_q));
  mem3 mem3_1 (.A(COUNTER), .Q(mem3_1_q));
  mem4 mem4_1 (.A(COUNTER), .Q(mem4_1_q));
  // mux8_2 mux8_2_1: pin names not known; wires that end beside it: CONTROL, mem1_1_q, mem2_1_q, mem3_1_q, mem4_1_q, LINE_OUT

  // Notes on the sheet:
  //   Блок памяти. Содержит всевозможные спрайты в ПЗУ. Выходной спрайт регулируется CONTROL
endmodule

module mem2 (
  input  [4:0] A,
  output [31:0] Q
);

  ROM #(.addrWidth(5), .dataWidth(32)) rom_1 (.addr(A), .data(Q));

  // Notes on the sheet:
  //   contents of rom_1 (hex, n*v repeats v):
  //   3 f 3f ff 3ff fff 3fff ffff 3ffff fffff 3fffff ffffff 3ffffff fffffff 3fffffff ffffffff ffffffff
  //   3fffffff fffffff 3ffffff ffffff 3fffff fffff 3ffff ffff 3fff fff 3ff ff 3f f 3
endmodule

module mem3 (
  input  [4:0] A,
  output [31:0] Q
);

  ROM #(.addrWidth(5), .dataWidth(32)) rom_1 (.addr(A), .data(Q));

  // Notes on the sheet:
  //   contents of rom_1 (hex, n*v repeats v):
  //   ffffffff ffffffff 7ffffffe 7ffffffe 3ffffffc 3ffffffc 1ffffff8 1ffffff8 ffffff0 ffffff0 7ffffe0
  //   7ffffe0 3ffffc0 3ffffc0 1ffff80 1ffff80 ffff00 ffff00 7ffe00 7ffe00 3ffc00 3ffc00 1ff800 1ff800
  //   ff000 ff000 7e000 7e000 3c000 3c000 18000 18000
endmodule

module mem4 (
  input  [4:0] A,
  output [31:0] Q
);

  ROM #(.addrWidth(5), .dataWidth(32)) rom_1 (.addr(A), .data(Q));

  // Notes on the sheet:
  //   contents of rom_1 (hex, n*v repeats v):
  //   c0000000 f0000000 fc000000 ff000000 ffc00000 fff00000 fffc0000 ffff0000 ffffc000 fffff000 fffffc00
  //   ffffff00 ffffffc0 fffffff0 fffffffc ffffffff ffffffff fffffffc fffffff0 ffffffc0 ffffff00 fffffc00
  //   fffff000 ffffc000 ffff0000 fffc0000 fff00000 ffc00000 ff000000 fc000000 f0000000 c0000000
endmodule

module mem1 (
  input  [4:0] A,
  output [31:0] Q
);

  ROM #(.addrWidth(5), .dataWidth(32)) rom_1 (.addr(A), .data(Q));

  // Notes on the sheet:
  //   contents of rom_1 (hex, n*v repeats v):
  //   18000 18000 3c000 3c000 7e000 7e000 ff000 ff000 1ff800 1ff800 3ffc00 3ffc00 7ffe00 7ffe00 ffff00
  //   ffff00 1ffff80 1ffff80 3ffffc0 3ffffc0 7ffffe0 7ffffe0 ffffff0 ffffff0 1ffffff8 1ffffff8 3ffffffc
  //   3ffffffc 7ffffffe 7ffffffe ffffffff ffffffff
endmodule

module mux8_2 (
  input  [1:0] SEL,
  input  [7:0] D0,
  input  [7:0] D1,
  input  [7:0] D2,
  input  [7:0] D3,
  output [7:0] Q
);

  Multiplexer #(.select(2), .width(8)) multiplexer_1 (.in0(D0), .in1(D1), .in2(D2), .in3(D3), .out(Q), .sel(SEL));
endmodule

module dtrig (
  input  S,
  input  D,
  input  C,
  input  R,
  output Q,
  output NOT_Q
);

  D_Flip_Flop d_ff_1 (.D(D), .clk(C), .Q(Q), .Qn(NOT_Q), .preset(S), .reset(R));
endmodule

module ttrig (
  input  S,
  input  D,
  input  C,
  input  R,
  output Q,
  output NOT_Q
);

  T_Flip_Flop t_ff_1 (.T(D), .clk(C), .Q(Q), .Qn(NOT_Q), .reset(R), .preset(S));
endmodule

module reg_2 (
  input  [1:0] D,
  input  WE,
  input  C,
  input  R,
  output [1:0] Q
);

  Register #(.width(2)) register_1 (.D(D), .en(WE), .clk(C), .Q(Q), .clr(R));
endmodule

module mux32bit (
  input  D0,
  input  D1,
  input  D2,
  input  D3,
  input  D4,
  input  D5,
  input  D6,
  input  D7,
  input  D8,
  input  D9,
  input  D10,
  input  D11,
  input  D12,
  input  D13,
  input  D14,
  input  D15,
  input  D16,
  input  D17,
  input  D18,
  input  D19,
  input  D20,
  input  D21,
  input  D22,
  input  D23,
  input  D24,
  input  D25,
  input  D26,
  input  D27,
  input  D28,
  input  D29,
  input  D30,
  input  D31,
  input  [4:0] A,
  output Q
);

  Multiplexer #(.select(5)) multiplexer_1 (
    .in0(D0), .in1(D1), .in2(D2), .in3(D3), .in4(D4), .in5(D5), .in6(D6), .in7(D7), .in8(D8), .in9(D9),
    .in10(D10), .in11(D11), .in12(D12), .in13(D13), .in14(D14), .in15(D15), .in16(D16), .in17(D17),
    .in18(D18), .in19(D19), .in20(D20), .in21(D21), .in22(D22), .in23(D23), .in24(D24), .in25(D25),
    .in26(D26), .in27(D27), .in28(D28), .in29(D29), .in30(D30), .in31(D31), .out(Q), .sel(A));
endmodule

module mux2in1_8bit (
  input  [7:0] D0,
  input  [7:0] D1,
  input  A,
  output [7:0] Q
);

  Multiplexer #(.width(8)) multiplexer_1 (.in0(D0), .in1(D1), .out(Q), .sel(A));
endmodule

module cnt_6_comp (
  input  LOAD,
  input  EN,
  input  CLK,
  input  R,
  input  in_5,
  input  in_6,
  input  in_7,
  input  in_8,
  output [5:0] Q,
  output [5:0] out_10
);

  wire and_1_out, and_2_out, and_3_out, and_4_out, and_5_out, and_6_out, and_7_out, and_8_out, and_9_out,
       and_10_out, and_11_out, and_12_out, and_13_out, and_14_out, and_15_out, and_16_out, and_17_out,
       and_18_out, and_19_out, and_20_out, and_21_out, and_22_out, and_23_out, and_24_out, or_1_out,
       or_2_out, or_3_out, or_4_out, or_5_out, or_6_out, or_7_out, or_8_out, or_9_out, or_10_out, or_11_out,
       or_12_out;

  and and_1 (and_1_out, ~Q[0], LOAD);  // AND_Gate
  and and_2 (and_2_out, ~LOAD, EN);  // AND_Gate
  and and_3 (and_3_out, ~out_10[0], in_5);  // AND_Gate
  or or_1 (or_1_out, and_3_out, and_4_out);
  and and_4 (and_4_out, ~in_5, in_6);  // AND_Gate
  or or_2 (or_2_out, and_1_out, and_2_out);
  T_Flip_Flop t_ff_1 (.T(or_2_out), .clk(CLK), .Q(Q[0]), .reset(R));  // open: Qn, preset
  and and_5 (and_5_out, Q[1], LOAD);
  and and_6 (and_6_out, Q[0], and_2_out);
  ttrig ttrig_1 (.D(or_1_out), .C(in_7), .R(in_8), .Q(out_10[0]));  // open: S, NOT_Q
  or or_3 (or_3_out, and_5_out, and_6_out);
  T_Flip_Flop t_ff_2 (.T(or_3_out), .clk(CLK), .Q(Q[1]), .reset(R));  // open: Qn, preset
  and and_7 (and_7_out, out_10[1], in_5);
  or or_4 (or_4_out, and_7_out, and_8_out);
  and and_8 (and_8_out, out_10[0], and_4_out);
  and and_9 (and_9_out, Q[2], LOAD);
  or or_5 (or_5_out, and_9_out, and_10_out);
  and and_10 (and_10_out, Q[1], and_6_out);
  ttrig ttrig_2 (.D(or_4_out), .C(in_7), .R(in_8), .Q(out_10[1]));  // open: S, NOT_Q
  T_Flip_Flop t_ff_3 (.T(or_5_out), .clk(CLK), .Q(Q[2]), .reset(R));  // open: Qn, preset
  and and_11 (and_11_out, out_10[2], in_5);
  or or_6 (or_6_out, and_11_out, and_12_out);
  and and_12 (and_12_out, out_10[1], and_8_out);
  and and_13 (and_13_out, Q[3], LOAD);
  and and_14 (and_14_out, Q[2], and_10_out);
  or or_7 (or_7_out, and_13_out, and_14_out);
  T_Flip_Flop t_ff_4 (.T(or_7_out), .clk(CLK), .Q(Q[3]), .reset(R));  // open: Qn, preset
  ttrig ttrig_3 (.D(or_6_out), .C(in_7), .R(in_8), .Q(out_10[2]));  // open: S, NOT_Q
  and and_15 (and_15_out, out_10[3], in_5);
  and and_16 (and_16_out, out_10[2], and_12_out);
  and and_17 (and_17_out, Q[4], LOAD);
  or or_8 (or_8_out, and_17_out, and_18_out);
  and and_18 (and_18_out, Q[3], and_14_out);
  or or_9 (or_9_out, and_15_out, and_16_out);
  T_Flip_Flop t_ff_5 (.T(or_8_out), .clk(CLK), .Q(Q[4]), .reset(R));  // open: Qn, preset
  ttrig ttrig_4 (.D(or_9_out), .C(in_7), .R(in_8), .Q(out_10[3]));  // open: S, NOT_Q
  and and_19 (and_19_out, Q[5], LOAD);
  and and_20 (and_20_out, Q[4], and_18_out);
  and and_21 (and_21_out, out_10[4], in_5);
  and and_22 (and_22_out, out_10[3], and_16_out);
  or or_10 (or_10_out, and_19_out, and_20_out);
  T_Flip_Flop t_ff_6 (.T(or_10_out), .clk(CLK), .Q(Q[5]), .reset(R));  // open: Qn, preset
  or or_11 (or_11_out, and_21_out, and_22_out);
  ttrig ttrig_5 (.D(or_11_out), .C(in_7), .R(in_8), .Q(out_10[4]));  // open: S, NOT_Q
  and and_23 (and_23_out, out_10[5], in_5);
  or or_12 (or_12_out, and_23_out, and_24_out);
  and and_24 (and_24_out, out_10[4], and_22_out);
  ttrig ttrig_6 (.D(or_12_out), .C(in_7), .R(in_8), .Q(out_10[5]));  // open: S, NOT_Q
endmodule

module cnt6_comp (
  input  L,
  input  EN,
  input  C,
  input  R,
  output [5:0] out_5
);

  wire and_1_out, and_2_out, and_3_out, and_4_out, and_5_out, and_6_out, and_7_out, and_8_out, and_9_out,
       and_10_out, and_11_out, and_12_out, or_1_out, or_2_out, or_3_out, or_4_out, or_5_out, or_6_out;

  and and_1 (and_1_out, ~out_5[0], L);  // AND_Gate
  and and_2 (and_2_out, ~L, EN);  // AND_Gate
  or or_1 (or_1_out, and_1_out, and_2_out);
  ttrig ttrig_1 (.D(or_1_out), .C(C), .R(R), .Q(out_5[0]));  // open: S, NOT_Q
  and and_3 (and_3_out, out_5[1], L);
  and and_4 (and_4_out, out_5[0], and_2_out);
  or or_2 (or_2_out, and_3_out, and_4_out);
  ttrig ttrig_2 (.D(or_2_out), .C(C), .R(R), .Q(out_5[1]));  // open: S, NOT_Q
  and and_5 (and_5_out, out_5[2], L);
  and and_6 (and_6_out, out_5[1], and_4_out);
  or or_3 (or_3_out, and_5_out, and_6_out);
  ttrig ttrig_3 (.D(or_3_out), .C(C), .R(R), .Q(out_5[2]));  // open: S, NOT_Q
  and and_7 (and_7_out, out_5[3], L);
  and and_8 (and_8_out, out_5[2], and_6_out);
  or or_4 (or_4_out, and_7_out, and_8_out);
  ttrig ttrig_4 (.D(or_4_out), .C(C), .R(R), .Q(out_5[3]));  // open: S, NOT_Q
  and and_9 (and_9_out, out_5[4], L);
  or or_5 (or_5_out, and_9_out, and_10_out);
  and and_10 (and_10_out, out_5[3], and_8_out);
  ttrig ttrig_5 (.D(or_5_out), .C(C), .R(R), .Q(out_5[4]));  // open: S, NOT_Q
  and and_11 (and_11_out, out_5[5], L);
  and and_12 (and_12_out, out_5[4], and_10_out);
  or or_6 (or_6_out, and_11_out, and_12_out);
  ttrig ttrig_6 (.D(or_6_out), .C(C), .R(R), .Q(out_5[5]));  // open: S, NOT_Q
endmodule

module reg_8 (
  input  [7:0] D,
  input  WE,
  input  C,
  input  R,
  output [7:0] Q
);

  Register register_1 (.D(D), .en(WE), .clk(C), .Q(Q), .clr(R));
endmodule

module mux2in1_6bit (
  input  [5:0] D0,
  input  [5:0] D1,
  input  A,
  output [5:0] Q
);

  Multiplexer #(.width(6)) multiplexer_1 (.in0(D0), .in1(D1), .out(Q), .sel(A));
endmodule

module sum8 (
  input  P0,
  input  [7:0] D0,
  input  [7:0] D1,
  output [7:0] Q,
  output P
);

  Adder adder_1 (.a(D0), .b(D1), .out(Q), .cin(P0), .cout(P));
endmodule

module reg16 (
  input  [15:0] D,
  input  WE,
  input  C,
  input  R,
  output [15:0] Q
);

  Register #(.width(16)) register_1 (.D(D), .en(WE), .clk(C), .Q(Q), .clr(R));
endmodule

module sum16 (
  input  P0,
  input  [15:0] D0,
  input  [15:0] D1,
  output [15:0] Q,
  output P
);

  Adder #(.width(16)) adder_1 (.a(D0), .b(D1), .out(Q), .cin(P0), .cout(P));
endmodule

module MPL24 (
  input  [23:0] D0,
  input  [23:0] D1,
  output [23:0] Q
);

  Multiplier #(.width(24)) multiplier_1 (.a(D0), .b(D1), .out(Q));  // open: cin, cout
endmodule

module sub8 (
  input  P0,
  input  [7:0] D0,
  input  [7:0] D1,
  output [7:0] Q,
  output P
);

  Subtractor subtractor_1 (.a(D0), .b(D1), .out(Q), .bin(P0), .bout(P));
endmodule

module sub16 (
  input  P0,
  input  [15:0] D0,
  input  [15:0] D1,
  output [15:0] Q,
  output P
);

  Subtractor #(.width(16)) subtractor_1 (.a(D0), .b(D1), .out(Q), .bin(P0), .bout(P));
endmodule

module COUNTER8 (
  input  in_1,
  input  in_2,
  output out_3,
  output [7:0] out_4
);

  Counter counter_1 (.clr(in_1), .clk(in_2), .carry(out_3), .Q(out_4));  // open: load, up, count, D
endmodule

module count60 (
  input  in_1,
  input  in_2,
  output out_3,
  output [7:0] out_4
);

  Counter #(.max('h3c)) counter_1 (.clr(in_1), .clk(in_2), .carry(out_3), .Q(out_4));  // open: load, up, count, D
endmodule

module MUX2in1_16bit (
  input  [15:0] D0,
  input  [15:0] D1,
  input  A,
  output [15:0] Q
);

  Multiplexer #(.width(16)) multiplexer_1 (.in0(D0), .in1(D1), .out(Q), .sel(A));
endmodule

module comp (
  input  [7:0] in_1,
  input  [7:0] in_2,
  output out_3,
  output out_4,
  output out_5
);

  Comparator comparator_1 (.a(in_1), .b(in_2), .gt(out_3), .eq(out_4), .lt(out_5));
endmodule
